// Logisim project Priority_Encoder.circ as structural Verilog
module Priority_Encoder4_2 (
  input  I0,
  input  I1,
  input  I2,
  input  I3,
  output Y1,
  output Y0
);

  wire and_1_out, not_1_out;

  not not_1 (not_1_out, I2);
  and and_1 (and_1_out, not_1_out, I1);
  or or_1 (Y1, I2, I3);
  or or_2 (Y0, I3, and_1_out);
endmodule

module Priority_Encoder16_4 (
);

  wire and_1_out, and_2_out, and_3_out, and_4_out, and_5_out, and_6_out, and_7_out, and_8_out,
       dipswitch_1_sw1, dipswitch_1_sw2, dipswitch_1_sw3, dipswitch_1_sw4, dipswitch_1_sw5, dipswitch_1_sw6,
       dipswitch_1_sw7, dipswitch_1_sw8, dipswitch_2_sw1, dipswitch_2_sw2, dipswitch_2_sw3, dipswitch_2_sw4,
       dipswitch_2_sw5, dipswitch_2_sw6, dipswitch_2_sw7, dipswitch_2_sw8, not_1_out, not_2_out, not_3_out,
       or_1_out, or_2_out, or_3_out, or_4_out, priority_encoder4_2_1_y0, priority_encoder4_2_1_y1,
       priority_encoder4_2_2_y0, priority_encoder4_2_2_y1, priority_encoder4_2_3_y0,
       priority_encoder4_2_3_y1, priority_encoder4_2_4_y0, priority_encoder4_2_4_y1;
  wire [3:0] or_6_out;

  DipSwitch dipswitch_1 (
    .sw1(dipswitch_1_sw1), .sw2(dipswitch_1_sw2), .sw3(dipswitch_1_sw3), .sw4(dipswitch_1_sw4),
    .sw5(dipswitch_1_sw5), .sw6(dipswitch_1_sw6), .sw7(dipswitch_1_sw7), .sw8(dipswitch_1_sw8));
  DipSwitch dipswitch_2 (
    .sw1(dipswitch_2_sw1), .sw2(dipswitch_2_sw2), .sw3(dipswitch_2_sw3), .sw4(dipswitch_2_sw4),
    .sw5(dipswitch_2_sw5), .sw6(dipswitch_2_sw6), .sw7(dipswitch_2_sw7), .sw8(dipswitch_2_sw8));
  or or_1 (or_1_out, dipswitch_1_sw1, dipswitch_1_sw2, dipswitch_1_sw3, dipswitch_1_sw4);
  or or_2 (or_2_out, dipswitch_1_sw5, dipswitch_1_sw6, dipswitch_1_sw7, dipswitch_1_sw8);
  or or_3 (or_3_out, dipswitch_2_sw1, dipswitch_2_sw2, dipswitch_2_sw3, dipswitch_2_sw4);
  or or_4 (or_4_out, dipswitch_2_sw5, dipswitch_2_sw6, dipswitch_2_sw7, dipswitch_2_sw8);
  not not_1 (not_1_out, or_1_out);
  not not_2 (not_2_out, or_2_out);
  not not_3 (not_3_out, or_3_out);
  Priority_Encoder4_2 priority_encoder4_2_1 (
    .I0(dipswitch_1_sw4), .I1(dipswitch_1_sw3), .I2(dipswitch_1_sw2), .I3(dipswitch_1_sw1),
    .Y1(priority_encoder4_2_1_y1), .Y0(priority_encoder4_2_1_y0));
  Priority_Encoder4_2 priority_encoder4_2_2 (
    .I0(dipswitch_1_sw8), .I1(dipswitch_1_sw7), .I2(dipswitch_1_sw6), .I3(dipswitch_1_sw5),
    .Y1(priority_encoder4_2_2_y1), .Y0(priority_encoder4_2_2_y0));
  Priority_Encoder4_2 priority_encoder4_2_3 (
    .I0(dipswitch_2_sw4), .I1(dipswitch_2_sw3), .I2(dipswitch_2_sw2), .I3(dipswitch_2_sw1),
    .Y1(priority_encoder4_2_3_y1), .Y0(priority_encoder4_2_3_y0));
  Priority_Encoder4_2 priority_encoder4_2_4 (
    .I0(dipswitch_2_sw8), .I1(dipswitch_2_sw7), .I2(dipswitch_2_sw6), .I3(dipswitch_2_sw5),
    .Y1(priority_encoder4_2_4_y1), .Y0(priority_encoder4_2_4_y0));
  and and_1 (and_1_out, or_1_out, priority_encoder4_2_1_y1);
  and and_2 (and_2_out, not_1_out, or_2_out, priority_encoder4_2_2_y1);
  and and_3 (and_3_out, not_1_out, not_2_out, or_3_out, priority_encoder4_2_3_y1);
  and and_4 (and_4_out, not_1_out, not_2_out, not_3_out, or_4_out, priority_encoder4_2_4_y1);
  and and_5 (and_5_out, or_1_out, priority_encoder4_2_1_y0);
  and and_6 (and_6_out, not_1_out, or_2_out, priority_encoder4_2_2_y0);
  and and_7 (and_7_out, not_1_out, not_2_out, or_3_out, priority_encoder4_2_3_y0);
  and and_8 (and_8_out, not_1_out, not_2_out, not_3_out, or_4_out, priority_encoder4_2_4_y0);
  Priority_Encoder4_2 priority_encoder4_2_5 (
    .I0(or_4_out), .I1(or_3_out), .I2(or_2_out), .I3(or_1_out), .Y1(or_6_out[3]), .Y0(or_6_out[2]));
  or or_5 (or_6_out[1], and_1_out, and_2_out, and_3_out, and_4_out);
  or or_6 (or_6_out[0], and_5_out, and_6_out, and_7_out, and_8_out);
  Hex_Digit_Display hex_digit_display_1 (.value(or_6_out));  // open: dp
endmodule
