// Logisim project adde2.circ as structural Verilog: 10 circuits, main circuit full_adder_to_1real
module full_adder_to_1real (
  input  A,
  input  B,
  input  CL,
  output S,
  output CO
);

  wire and_1_out, and_2_out, and_3_out, and_4_out, and_5_out, and_6_out, and_7_out, not_1_out, not_2_out,
       not_3_out;

  not not_1 (not_1_out, A);
  not not_2 (not_2_out, B);
  not not_3 (not_3_out, CL);
  and and_1 (and_1_out, not_1_out, not_2_out, not_3_out);
  and and_2 (and_2_out, A, not_2_out, CL);
  and and_3 (and_3_out, not_1_out, B, CL);
  and and_4 (and_4_out, A, B, not_3_out);
  and and_5 (and_5_out, not_1_out, not_2_out);
  and and_6 (and_6_out, not_2_out, not_3_out);
  and and_7 (and_7_out, not_1_out, not_3_out);
  nor nor_1 (S, and_1_out, and_2_out, and_3_out, and_4_out);
  nor nor_2 (CO, and_5_out, and_6_out, and_7_out);
endmodule

module half_adder_to_1 (
  input  A,
  input  B,
  output S,
  output CO
);

  xor xor_1 (S, A, B);
  and and_1 (CO, A, B);
endmodule

module full_adder_to_1false (
  input  A,
  input  B,
  input  CIN,
  output S,
  output CO
);

  wire half_adder_to_1_1_co, half_adder_to_1_1_s, half_adder_to_1_2_co;

  half_adder_to_1 half_adder_to_1_1 (.A(A), .B(B), .S(half_adder_to_1_1_s), .CO(half_adder_to_1_1_co));
  half_adder_to_1 half_adder_to_1_2 (.A(half_adder_to_1_1_s), .B(CIN), .S(S), .CO(half_adder_to_1_2_co));
  or or_1 (CO, half_adder_to_1_2_co, half_adder_to_1_1_co);
endmodule

module adder_to_4 (
  input  A3,
  input  A2,
  input  A1,
  input  A0,
  input  B3,
  input  B2,
  input  B1,
  input  B0,
  output Y3,
  output Y2,
  output Y1,
  output Y0
);

  wire decoder_1_out0, decoder_1_out1, decoder_1_out2, decoder_1_out3, decoder_1_out4, decoder_1_out5,
       decoder_1_out6, decoder_1_out7, decoder_1_out8, decoder_1_out9, decoder_1_out10, decoder_1_out11,
       decoder_1_out12, decoder_1_out13, decoder_1_out14, decoder_1_out15, decoder_2_out0, decoder_2_out1,
       decoder_2_out2, decoder_2_out3, decoder_2_out4, decoder_2_out5, decoder_2_out6, decoder_2_out7,
       decoder_2_out8, decoder_2_out9, decoder_2_out10, decoder_2_out11, decoder_2_out12, decoder_2_out13,
       decoder_2_out14, decoder_2_out15, decoder_3_out0, decoder_3_out1, decoder_3_out2, decoder_3_out3,
       decoder_3_out4, decoder_3_out5, decoder_3_out6, decoder_3_out7, decoder_3_out8, decoder_3_out9,
       decoder_3_out10, decoder_3_out11, decoder_3_out12, decoder_3_out13, decoder_3_out14, decoder_3_out15,
       full_adder_to_1real_1_co, full_adder_to_1real_2_co, full_adder_to_1real_3_co, full_adder_to_1real_4_co;
  wire [7:0] or_1_out, or_2_out, or_3_out, wire0_1_out_2, wire0_2_out_2, wire0_3_out_2, wire1_1_out_2,
       wire1_2_out_2, wire1_3_out_2, wire2_1_out_2, wire2_2_out_2, wire2_3_out_2, wire3_1_out_2,
       wire3_2_out_2, wire3_3_out_2, wire4_1_out_2, wire4_2_out_2, wire4_3_out_2, wire5_1_out_2,
       wire5_2_out_2, wire5_3_out_2, wire6_1_out_2, wire6_2_out_2, wire6_3_out_2, wire7_1_out_2,
       wire7_2_out_2, wire7_3_out_2, wire8_1_out_2, wire8_2_out_2, wire8_3_out_2, wire9_1_out_2,
       wire9_2_out_2, wire9_3_out_2, wire10_1_out_2, wire10_2_out_2, wire10_3_out_2, wire11_1_out_2,
       wire11_2_out_2, wire11_3_out_2, wire12_1_out_2, wire12_2_out_2, wire12_3_out_2, wire13_1_out_2,
       wire13_2_out_2, wire13_3_out_2, wire14_1_out_2, wire14_2_out_2, wire14_3_out_2, wire15_1_out_2,
       wire15_2_out_2, wire15_3_out_2;

  Decoder #(.select(4)) decoder_1 (
    .out0(decoder_1_out0), .out1(decoder_1_out1), .out2(decoder_1_out2), .out3(decoder_1_out3),
    .out4(decoder_1_out4), .out5(decoder_1_out5), .out6(decoder_1_out6), .out7(decoder_1_out7),
    .out8(decoder_1_out8), .out9(decoder_1_out9), .out10(decoder_1_out10), .out11(decoder_1_out11),
    .out12(decoder_1_out12), .out13(decoder_1_out13), .out14(decoder_1_out14), .out15(decoder_1_out15),
    .sel({A3, A2, A1, A0}), .en(1'b1));
  Decoder #(.select(4)) decoder_2 (
    .out0(decoder_2_out0), .out1(decoder_2_out1), .out2(decoder_2_out2), .out3(decoder_2_out3),
    .out4(decoder_2_out4), .out5(decoder_2_out5), .out6(decoder_2_out6), .out7(decoder_2_out7),
    .out8(decoder_2_out8), .out9(decoder_2_out9), .out10(decoder_2_out10), .out11(decoder_2_out11),
    .out12(decoder_2_out12), .out13(decoder_2_out13), .out14(decoder_2_out14), .out15(decoder_2_out15),
    .sel({B3, B2, B1, B0}), .en(1'b1));
  Decoder #(.select(4)) decoder_3 (
    .out0(decoder_3_out0), .out1(decoder_3_out1), .out2(decoder_3_out2), .out3(decoder_3_out3),
    .out4(decoder_3_out4), .out5(decoder_3_out5), .out6(decoder_3_out6), .out7(decoder_3_out7),
    .out8(decoder_3_out8), .out9(decoder_3_out9), .out10(decoder_3_out10), .out11(decoder_3_out11),
    .out12(decoder_3_out12), .out13(decoder_3_out13), .out14(decoder_3_out14), .out15(decoder_3_out15),
    .sel({Y3, Y2, Y1, Y0}), .en(1'b1));
  full_adder_to_1real full_adder_to_1real_1 (.A(A0), .B(B0), .CL(1'b0), .S(Y0), .CO(full_adder_to_1real_1_co));
  wire0 wire0_1 (.in_1(decoder_1_out0), .out_2(wire0_1_out_2));
  wire1 wire1_1 (.in_1(decoder_1_out1), .out_2(wire1_1_out_2));
  wire2 wire2_1 (.in_1(decoder_1_out2), .out_2(wire2_1_out_2));
  wire3 wire3_1 (.in_1(decoder_1_out3), .out_2(wire3_1_out_2));
  wire4 wire4_1 (.in_1(decoder_1_out4), .out_2(wire4_1_out_2));
  wire5 wire5_1 (.in_1(decoder_1_out5), .out_2(wire5_1_out_2));
  wire6 wire6_1 (.in_1(decoder_1_out6), .out_2(wire6_1_out_2));
  wire7 wire7_1 (.in_1(decoder_1_out7), .out_2(wire7_1_out_2));
  wire8 wire8_1 (.in_1(decoder_1_out8), .out_2(wire8_1_out_2));
  wire9 wire9_1 (.in_1(decoder_1_out9), .out_2(wire9_1_out_2));
  wire10 wire10_1 (.in_1(decoder_1_out10), .out_2(wire10_1_out_2));
  wire11 wire11_1 (.in_1(decoder_1_out11), .out_2(wire11_1_out_2));
  wire12 wire12_1 (.in_1(decoder_1_out12), .out_2(wire12_1_out_2));
  wire13 wire13_1 (.in_1(decoder_1_out13), .out_2(wire13_1_out_2));
  wire14 wire14_1 (.in_1(decoder_1_out14), .out_2(wire14_1_out_2));
  wire15 wire15_1 (.in_1(decoder_1_out15), .out_2(wire15_1_out_2));
  wire0 wire0_2 (.in_1(decoder_2_out0), .out_2(wire0_2_out_2));
  wire1 wire1_2 (.in_1(decoder_2_out1), .out_2(wire1_2_out_2));
  wire2 wire2_2 (.in_1(decoder_2_out2), .out_2(wire2_2_out_2));
  wire3 wire3_2 (.in_1(decoder_2_out3), .out_2(wire3_2_out_2));
  wire4 wire4_2 (.in_1(decoder_2_out4), .out_2(wire4_2_out_2));
  wire5 wire5_2 (.in_1(decoder_2_out5), .out_2(wire5_2_out_2));
  wire6 wire6_2 (.in_1(decoder_2_out6), .out_2(wire6_2_out_2));
  wire7 wire7_2 (.in_1(decoder_2_out7), .out_2(wire7_2_out_2));
  wire8 wire8_2 (.in_1(decoder_2_out8), .out_2(wire8_2_out_2));
  wire9 wire9_2 (.in_1(decoder_2_out9), .out_2(wire9_2_out_2));
  wire10 wire10_2 (.in_1(decoder_2_out10), .out_2(wire10_2_out_2));
  wire11 wire11_2 (.in_1(decoder_2_out11), .out_2(wire11_2_out_2));
  wire12 wire12_2 (.in_1(decoder_2_out12), .out_2(wire12_2_out_2));
  wire13 wire13_2 (.in_1(decoder_2_out13), .out_2(wire13_2_out_2));
  wire14 wire14_2 (.in_1(decoder_2_out14), .out_2(wire14_2_out_2));
  wire15 wire15_2 (.in_1(decoder_2_out15), .out_2(wire15_2_out_2));
  assign or_1_out = wire0_1_out_2 | wire1_1_out_2 | wire2_1_out_2 | wire3_1_out_2 | wire4_1_out_2 | wire5_1_out_2 | wire6_1_out_2 | wire7_1_out_2 | wire8_1_out_2 | wire9_1_out_2 | wire10_1_out_2 | wire11_1_out_2 | wire12_1_out_2 | wire13_1_out_2 | wire14_1_out_2 | wire15_1_out_2;  // OR_Gate or_1, 8 bits wide
  full_adder_to_1real full_adder_to_1real_2 (
    .A(A1), .B(B1), .CL(full_adder_to_1real_1_co), .S(Y1), .CO(full_adder_to_1real_2_co));
  assign or_2_out = wire0_2_out_2 | wire1_2_out_2 | wire2_2_out_2 | wire3_2_out_2 | wire4_2_out_2 | wire5_2_out_2 | wire6_2_out_2 | wire7_2_out_2 | wire8_2_out_2 | wire9_2_out_2 | wire10_2_out_2 | wire11_2_out_2 | wire12_2_out_2 | wire13_2_out_2 | wire14_2_out_2 | wire15_2_out_2;  // OR_Gate or_2, 8 bits wide
  wire0 wire0_3 (.in_1(decoder_3_out0), .out_2(wire0_3_out_2));
  wire1 wire1_3 (.in_1(decoder_3_out1), .out_2(wire1_3_out_2));
  wire2 wire2_3 (.in_1(decoder_3_out2), .out_2(wire2_3_out_2));
  wire3 wire3_3 (.in_1(decoder_3_out3), .out_2(wire3_3_out_2));
  wire4 wire4_3 (.in_1(decoder_3_out4), .out_2(wire4_3_out_2));
  wire5 wire5_3 (.in_1(decoder_3_out5), .out_2(wire5_3_out_2));
  wire6 wire6_3 (.in_1(decoder_3_out6), .out_2(wire6_3_out_2));
  wire7 wire7_3 (.in_1(decoder_3_out7), .out_2(wire7_3_out_2));
  wire8 wire8_3 (.in_1(decoder_3_out8), .out_2(wire8_3_out_2));
  wire9 wire9_3 (.in_1(decoder_3_out9), .out_2(wire9_3_out_2));
  wire10 wire10_3 (.in_1(decoder_3_out10), .out_2(wire10_3_out_2));
  wire11 wire11_3 (.in_1(decoder_3_out11), .out_2(wire11_3_out_2));
  wire12 wire12_3 (.in_1(decoder_3_out12), .out_2(wire12_3_out_2));
  wire13 wire13_3 (.in_1(decoder_3_out13), .out_2(wire13_3_out_2));
  wire14 wire14_3 (.in_1(decoder_3_out14), .out_2(wire14_3_out_2));
  wire15 wire15_3 (.in_1(decoder_3_out15), .out_2(wire15_3_out_2));
  _7_Segment_Display u_7_segment_display_1 (
    .g(or_1_out[6]), .f(or_1_out[5]), .a(or_1_out[0]), .b(or_1_out[1]), .e(or_1_out[4]), .d(or_1_out[3]),
    .c(or_1_out[2]), .dp(or_1_out[7]));
  _7_Segment_Display u_7_segment_display_2 (
    .g(or_2_out[6]), .f(or_2_out[5]), .a(or_2_out[0]), .b(or_2_out[1]), .e(or_2_out[4]), .d(or_2_out[3]),
    .c(or_2_out[2]), .dp(or_2_out[7]));
  full_adder_to_1real full_adder_to_1real_3 (
    .A(A2), .B(B2), .CL(full_adder_to_1real_2_co), .S(Y2), .CO(full_adder_to_1real_3_co));
  assign or_3_out = wire0_3_out_2 | wire1_3_out_2 | wire2_3_out_2 | wire3_3_out_2 | wire4_3_out_2 | wire5_3_out_2 | wire6_3_out_2 | wire7_3_out_2 | wire8_3_out_2 | wire9_3_out_2 | wire10_3_out_2 | wire11_3_out_2 | wire12_3_out_2 | wire13_3_out_2 | wire14_3_out_2 | wire15_3_out_2;  // OR_Gate or_3, 8 bits wide
  full_adder_to_1real full_adder_to_1real_4 (
    .A(A3), .B(B3), .CL(full_adder_to_1real_3_co), .S(Y3), .CO(full_adder_to_1real_4_co));
  LED led_1 (.in(full_adder_to_1real_4_co));
  _7_Segment_Display u_7_segment_display_3 (
    .g(or_3_out[6]), .f(or_3_out[5]), .a(or_3_out[0]), .b(or_3_out[1]), .e(or_3_out[4]), .d(or_3_out[3]),
    .c(or_3_out[2]), .dp(or_3_out[7]));
endmodule

module subtractor_4 (
  input  A3,
  input  A2,
  input  A1,
  input  A0,
  input  B3,
  input  B2,
  input  B1,
  input  B0,
  output S,
  output Y3,
  output Y2,
  output Y1,
  output Y0
);

  wire decoder_1_out0, decoder_1_out1, decoder_1_out2, decoder_1_out3, decoder_1_out4, decoder_1_out5,
       decoder_1_out6, decoder_1_out7, decoder_1_out8, decoder_1_out9, decoder_1_out10, decoder_1_out11,
       decoder_1_out12, decoder_1_out13, decoder_1_out14, decoder_1_out15, decoder_2_out0, decoder_2_out1,
       decoder_2_out2, decoder_2_out3, decoder_2_out4, decoder_2_out5, decoder_2_out6, decoder_2_out7,
       decoder_2_out8, decoder_2_out9, decoder_2_out10, decoder_2_out11, decoder_2_out12, decoder_2_out13,
       decoder_2_out14, decoder_2_out15, decoder_3_out0, decoder_3_out1, decoder_3_out2, decoder_3_out3,
       decoder_3_out4, decoder_3_out5, decoder_3_out6, decoder_3_out7, decoder_3_out8, decoder_3_out9,
       decoder_3_out10, decoder_3_out11, decoder_3_out12, decoder_3_out13, decoder_3_out14, decoder_3_out15,
       full_adder_to_1real_1_co, full_adder_to_1real_2_co, full_adder_to_1real_3_co,
       full_adder_to_1real_4_co, full_adder_to_1real_5_co, full_adder_to_1real_6_co,
       full_adder_to_1real_7_co, not_1_out, not_2_out, not_3_out, not_4_out, not_5_out, not_6_out, not_7_out,
       not_9_out;
  wire [3:0] full_adder_to_1real_1_s, full_adder_to_1real_2_s;
  wire [7:0] or_1_out, or_2_out, or_3_out, wire0_1_out_2, wire0_2_out_2, wire0_3_out_2, wire1_1_out_2,
       wire1_2_out_2, wire1_3_out_2, wire2_1_out_2, wire2_2_out_2, wire2_3_out_2, wire3_1_out_2,
       wire3_2_out_2, wire3_3_out_2, wire4_1_out_2, wire4_2_out_2, wire4_3_out_2, wire5_1_out_2,
       wire5_2_out_2, wire5_3_out_2, wire6_1_out_2, wire6_2_out_2, wire6_3_out_2, wire7_1_out_2,
       wire7_2_out_2, wire7_3_out_2, wire8_1_out_2, wire8_2_out_2, wire8_3_out_2, wire9_1_out_2,
       wire9_2_out_2, wire9_3_out_2, wire10_1_out_2, wire10_2_out_2, wire10_3_out_2, wire11_1_out_2,
       wire11_2_out_2, wire11_3_out_2, wire12_1_out_2, wire12_2_out_2, wire12_3_out_2, wire13_1_out_2,
       wire13_2_out_2, wire13_3_out_2, wire14_1_out_2, wire14_2_out_2, wire14_3_out_2, wire15_1_out_2,
       wire15_2_out_2, wire15_3_out_2;

  Decoder #(.select(4)) decoder_1 (
    .out0(decoder_1_out0), .out1(decoder_1_out1), .out2(decoder_1_out2), .out3(decoder_1_out3),
    .out4(decoder_1_out4), .out5(decoder_1_out5), .out6(decoder_1_out6), .out7(decoder_1_out7),
    .out8(decoder_1_out8), .out9(decoder_1_out9), .out10(decoder_1_out10), .out11(decoder_1_out11),
    .out12(decoder_1_out12), .out13(decoder_1_out13), .out14(decoder_1_out14), .out15(decoder_1_out15),
    .sel({A3, A2, A1, A0}), .en(1'b1));
  Decoder #(.select(4)) decoder_2 (
    .out0(decoder_2_out0), .out1(decoder_2_out1), .out2(decoder_2_out2), .out3(decoder_2_out3),
    .out4(decoder_2_out4), .out5(decoder_2_out5), .out6(decoder_2_out6), .out7(decoder_2_out7),
    .out8(decoder_2_out8), .out9(decoder_2_out9), .out10(decoder_2_out10), .out11(decoder_2_out11),
    .out12(decoder_2_out12), .out13(decoder_2_out13), .out14(decoder_2_out14), .out15(decoder_2_out15),
    .sel({B3, B2, B1, B0}), .en(1'b1));
  not not_1 (not_1_out, B0);
  Decoder #(.select(4)) decoder_3 (
    .out0(decoder_3_out0), .out1(decoder_3_out1), .out2(decoder_3_out2), .out3(decoder_3_out3),
    .out4(decoder_3_out4), .out5(decoder_3_out5), .out6(decoder_3_out6), .out7(decoder_3_out7),
    .out8(decoder_3_out8), .out9(decoder_3_out9), .out10(decoder_3_out10), .out11(decoder_3_out11),
    .out12(decoder_3_out12), .out13(decoder_3_out13), .out14(decoder_3_out14), .out15(decoder_3_out15),
    .sel({Y3, Y2, Y1, Y0}), .en(1'b1));
  not not_2 (not_2_out, B1);
  full_adder_to_1real full_adder_to_1real_1 (
    .A(A0), .B(not_1_out), .CL(1'b1), .S(full_adder_to_1real_1_s[0]), .CO(full_adder_to_1real_1_co));
  full_adder_to_1real full_adder_to_1real_2 (
    .A(not_3_out), .B(1'b1), .CL(1'b0), .S(full_adder_to_1real_2_s[0]), .CO(full_adder_to_1real_2_co));
  wire0 wire0_1 (.in_1(decoder_1_out0), .out_2(wire0_1_out_2));
  wire1 wire1_1 (.in_1(decoder_1_out1), .out_2(wire1_1_out_2));
  wire2 wire2_1 (.in_1(decoder_1_out2), .out_2(wire2_1_out_2));
  wire3 wire3_1 (.in_1(decoder_1_out3), .out_2(wire3_1_out_2));
  wire4 wire4_1 (.in_1(decoder_1_out4), .out_2(wire4_1_out_2));
  wire5 wire5_1 (.in_1(decoder_1_out5), .out_2(wire5_1_out_2));
  wire6 wire6_1 (.in_1(decoder_1_out6), .out_2(wire6_1_out_2));
  wire7 wire7_1 (.in_1(decoder_1_out7), .out_2(wire7_1_out_2));
  wire8 wire8_1 (.in_1(decoder_1_out8), .out_2(wire8_1_out_2));
  wire9 wire9_1 (.in_1(decoder_1_out9), .out_2(wire9_1_out_2));
  wire10 wire10_1 (.in_1(decoder_1_out10), .out_2(wire10_1_out_2));
  wire11 wire11_1 (.in_1(decoder_1_out11), .out_2(wire11_1_out_2));
  wire12 wire12_1 (.in_1(decoder_1_out12), .out_2(wire12_1_out_2));
  wire13 wire13_1 (.in_1(decoder_1_out13), .out_2(wire13_1_out_2));
  wire14 wire14_1 (.in_1(decoder_1_out14), .out_2(wire14_1_out_2));
  wire15 wire15_1 (.in_1(decoder_1_out15), .out_2(wire15_1_out_2));
  wire0 wire0_2 (.in_1(decoder_2_out0), .out_2(wire0_2_out_2));
  wire1 wire1_2 (.in_1(decoder_2_out1), .out_2(wire1_2_out_2));
  wire2 wire2_2 (.in_1(decoder_2_out2), .out_2(wire2_2_out_2));
  wire3 wire3_2 (.in_1(decoder_2_out3), .out_2(wire3_2_out_2));
  wire4 wire4_2 (.in_1(decoder_2_out4), .out_2(wire4_2_out_2));
  wire5 wire5_2 (.in_1(decoder_2_out5), .out_2(wire5_2_out_2));
  wire6 wire6_2 (.in_1(decoder_2_out6), .out_2(wire6_2_out_2));
  wire7 wire7_2 (.in_1(decoder_2_out7), .out_2(wire7_2_out_2));
  wire8 wire8_2 (.in_1(decoder_2_out8), .out_2(wire8_2_out_2));
  wire9 wire9_2 (.in_1(decoder_2_out9), .out_2(wire9_2_out_2));
  wire10 wire10_2 (.in_1(decoder_2_out10), .out_2(wire10_2_out_2));
  wire11 wire11_2 (.in_1(decoder_2_out11), .out_2(wire11_2_out_2));
  wire12 wire12_2 (.in_1(decoder_2_out12), .out_2(wire12_2_out_2));
  wire13 wire13_2 (.in_1(decoder_2_out13), .out_2(wire13_2_out_2));
  wire14 wire14_2 (.in_1(decoder_2_out14), .out_2(wire14_2_out_2));
  wire15 wire15_2 (.in_1(decoder_2_out15), .out_2(wire15_2_out_2));
  not not_3 (not_3_out, full_adder_to_1real_1_s[0]);
  assign or_1_out = wire0_1_out_2 | wire1_1_out_2 | wire2_1_out_2 | wire3_1_out_2 | wire4_1_out_2 | wire5_1_out_2 | wire6_1_out_2 | wire7_1_out_2 | wire8_1_out_2 | wire9_1_out_2 | wire10_1_out_2 | wire11_1_out_2 | wire12_1_out_2 | wire13_1_out_2 | wire14_1_out_2 | wire15_1_out_2;  // OR_Gate or_1, 8 bits wide
  not not_4 (not_4_out, B2);
  full_adder_to_1real full_adder_to_1real_3 (
    .A(A1), .B(not_2_out), .CL(full_adder_to_1real_1_co), .S(full_adder_to_1real_1_s[1]),
    .CO(full_adder_to_1real_3_co));
  assign or_2_out = wire0_2_out_2 | wire1_2_out_2 | wire2_2_out_2 | wire3_2_out_2 | wire4_2_out_2 | wire5_2_out_2 | wire6_2_out_2 | wire7_2_out_2 | wire8_2_out_2 | wire9_2_out_2 | wire10_2_out_2 | wire11_2_out_2 | wire12_2_out_2 | wire13_2_out_2 | wire14_2_out_2 | wire15_2_out_2;  // OR_Gate or_2, 8 bits wide
  not not_5 (not_5_out, full_adder_to_1real_1_s[1]);
  full_adder_to_1real full_adder_to_1real_4 (
    .A(not_5_out), .B(1'b0), .CL(full_adder_to_1real_2_co), .S(full_adder_to_1real_2_s[1]),
    .CO(full_adder_to_1real_4_co));
  wire0 wire0_3 (.in_1(decoder_3_out0), .out_2(wire0_3_out_2));
  wire1 wire1_3 (.in_1(decoder_3_out1), .out_2(wire1_3_out_2));
  wire2 wire2_3 (.in_1(decoder_3_out2), .out_2(wire2_3_out_2));
  wire3 wire3_3 (.in_1(decoder_3_out3), .out_2(wire3_3_out_2));
  wire4 wire4_3 (.in_1(decoder_3_out4), .out_2(wire4_3_out_2));
  wire5 wire5_3 (.in_1(decoder_3_out5), .out_2(wire5_3_out_2));
  wire6 wire6_3 (.in_1(decoder_3_out6), .out_2(wire6_3_out_2));
  wire7 wire7_3 (.in_1(decoder_3_out7), .out_2(wire7_3_out_2));
  wire8 wire8_3 (.in_1(decoder_3_out8), .out_2(wire8_3_out_2));
  wire9 wire9_3 (.in_1(decoder_3_out9), .out_2(wire9_3_out_2));
  wire10 wire10_3 (.in_1(decoder_3_out10), .out_2(wire10_3_out_2));
  wire11 wire11_3 (.in_1(decoder_3_out11), .out_2(wire11_3_out_2));
  wire12 wire12_3 (.in_1(decoder_3_out12), .out_2(wire12_3_out_2));
  wire13 wire13_3 (.in_1(decoder_3_out13), .out_2(wire13_3_out_2));
  wire14 wire14_3 (.in_1(decoder_3_out14), .out_2(wire14_3_out_2));
  wire15 wire15_3 (.in_1(decoder_3_out15), .out_2(wire15_3_out_2));
  _7_Segment_Display u_7_segment_display_1 (
    .g(or_1_out[6]), .f(or_1_out[5]), .a(or_1_out[0]), .b(or_1_out[1]), .e(or_1_out[4]), .d(or_1_out[3]),
    .c(or_1_out[2]), .dp(or_1_out[7]));
  _7_Segment_Display u_7_segment_display_2 (
    .g(or_2_out[6]), .f(or_2_out[5]), .a(or_2_out[0]), .b(or_2_out[1]), .e(or_2_out[4]), .d(or_2_out[3]),
    .c(or_2_out[2]), .dp(or_2_out[7]));
  Multiplexer #(.width(4)) multiplexer_1 (
    .in0(full_adder_to_1real_1_s), .in1(full_adder_to_1real_2_s), .out({Y3, Y2, Y1, Y0}), .sel(S));
  not not_6 (not_6_out, B3);
  full_adder_to_1real full_adder_to_1real_5 (
    .A(A2), .B(not_4_out), .CL(full_adder_to_1real_3_co), .S(full_adder_to_1real_1_s[2]),
    .CO(full_adder_to_1real_5_co));
  not not_7 (not_7_out, full_adder_to_1real_1_s[2]);
  full_adder_to_1real full_adder_to_1real_6 (
    .A(not_7_out), .B(1'b0), .CL(full_adder_to_1real_4_co), .S(full_adder_to_1real_2_s[2]),
    .CO(full_adder_to_1real_6_co));
  assign or_3_out = wire0_3_out_2 | wire1_3_out_2 | wire2_3_out_2 | wire3_3_out_2 | wire4_3_out_2 | wire5_3_out_2 | wire6_3_out_2 | wire7_3_out_2 | wire8_3_out_2 | wire9_3_out_2 | wire10_3_out_2 | wire11_3_out_2 | wire12_3_out_2 | wire13_3_out_2 | wire14_3_out_2 | wire15_3_out_2;  // OR_Gate or_3, 8 bits wide
  full_adder_to_1real full_adder_to_1real_7 (
    .A(A3), .B(not_6_out), .CL(full_adder_to_1real_5_co), .S(full_adder_to_1real_1_s[3]),
    .CO(full_adder_to_1real_7_co));
  not not_8 (S, full_adder_to_1real_7_co);
  not not_9 (not_9_out, full_adder_to_1real_1_s[3]);
  full_adder_to_1real full_adder_to_1real_8 (
    .A(not_9_out), .B(1'b0), .CL(full_adder_to_1real_6_co), .S(full_adder_to_1real_2_s[3]));  // open: CO
  LED led_1 (.in(S));
  _7_Segment_Display u_7_segment_display_3 (
    .g(or_3_out[6]), .f(or_3_out[5]), .a(or_3_out[0]), .b(or_3_out[1]), .e(or_3_out[4]), .d(or_3_out[3]),
    .c(or_3_out[2]), .dp(or_3_out[7]));
endmodule

module sign_magnitude_adder_4 (
  input  A3,
  input  A2,
  input  A1,
  input  A0,
  input  B3,
  input  B2,
  input  B1,
  input  B0,
  output Y3,
  output Y2,
  output Y1,
  output Y0
);

  wire decoder_1_out0, decoder_1_out1, decoder_1_out2, decoder_1_out3, decoder_1_out4, decoder_1_out5,
       decoder_1_out6, decoder_1_out7, decoder_1_out8, decoder_1_out9, decoder_1_out10, decoder_1_out11,
       decoder_1_out12, decoder_1_out13, decoder_1_out14, decoder_1_out15, subtractor_4_1_s, xor_1_out;
  wire [3:0] adder_to_4_1_y0, subtractor_4_1_y0;
  wire [3:3] multiplexer_1_out;
  wire [7:0] or_2_out, wire0_1_out_2, wire1_1_out_2, wire2_1_out_2, wire3_1_out_2, wire4_1_out_2,
       wire5_1_out_2, wire6_1_out_2, wire7_1_out_2, wire8_1_out_2, wire9_1_out_2, wire10_1_out_2,
       wire11_1_out_2, wire12_1_out_2, wire13_1_out_2, wire14_1_out_2, wire15_1_out_2;

  xor xor_1 (xor_1_out, B3, A3);
  adder_to_4 adder_to_4_1 (
    .A2(A2), .A1(A1), .A0(A0), .B2(B2), .B1(B1), .B0(B0), .Y3(adder_to_4_1_y0[3]), .Y2(adder_to_4_1_y0[2]),
    .Y1(adder_to_4_1_y0[1]), .Y0(adder_to_4_1_y0[0]));  // open: A3, B3
  subtractor_4 subtractor_4_1 (
    .A2(A2), .A1(A1), .A0(A0), .B2(B2), .B1(B1), .B0(B0), .S(subtractor_4_1_s), .Y3(subtractor_4_1_y0[3]),
    .Y2(subtractor_4_1_y0[2]), .Y1(subtractor_4_1_y0[1]), .Y0(subtractor_4_1_y0[0]));  // open: A3, B3
  Multiplexer #(.width(4)) multiplexer_1 (
    .in0(adder_to_4_1_y0), .in1(subtractor_4_1_y0), .out({multiplexer_1_out[3], Y2, Y1, Y0}), .sel(xor_1_out));
  _7_Segment_Display u_7_segment_display_1 (.g(subtractor_4_1_s));  // open: f, a, b, e, d, c, dp
  or or_1 (Y3, subtractor_4_1_s, multiplexer_1_out[3]);
  Decoder #(.select(4)) decoder_1 (
    .out0(decoder_1_out0), .out1(decoder_1_out1), .out2(decoder_1_out2), .out3(decoder_1_out3),
    .out4(decoder_1_out4), .out5(decoder_1_out5), .out6(decoder_1_out6), .out7(decoder_1_out7),
    .out8(decoder_1_out8), .out9(decoder_1_out9), .out10(decoder_1_out10), .out11(decoder_1_out11),
    .out12(decoder_1_out12), .out13(decoder_1_out13), .out14(decoder_1_out14), .out15(decoder_1_out15),
    .sel({multiplexer_1_out[3], Y2, Y1, Y0}), .en(1'b1));
  wire0 wire0_1 (.in_1(decoder_1_out0), .out_2(wire0_1_out_2));
  wire1 wire1_1 (.in_1(decoder_1_out1), .out_2(wire1_1_out_2));
  wire2 wire2_1 (.in_1(decoder_1_out2), .out_2(wire2_1_out_2));
  wire3 wire3_1 (.in_1(decoder_1_out3), .out_2(wire3_1_out_2));
  wire4 wire4_1 (.in_1(decoder_1_out4), .out_2(wire4_1_out_2));
  wire5 wire5_1 (.in_1(decoder_1_out5), .out_2(wire5_1_out_2));
  wire6 wire6_1 (.in_1(decoder_1_out6), .out_2(wire6_1_out_2));
  wire7 wire7_1 (.in_1(decoder_1_out7), .out_2(wire7_1_out_2));
  wire8 wire8_1 (.in_1(decoder_1_out8), .out_2(wire8_1_out_2));
  wire9 wire9_1 (.in_1(decoder_1_out9), .out_2(wire9_1_out_2));
  wire10 wire10_1 (.in_1(decoder_1_out10), .out_2(wire10_1_out_2));
  wire11 wire11_1 (.in_1(decoder_1_out11), .out_2(wire11_1_out_2));
  wire12 wire12_1 (.in_1(decoder_1_out12), .out_2(wire12_1_out_2));
  wire13 wire13_1 (.in_1(decoder_1_out13), .out_2(wire13_1_out_2));
  wire14 wire14_1 (.in_1(decoder_1_out14), .out_2(wire14_1_out_2));
  wire15 wire15_1 (.in_1(decoder_1_out15), .out_2(wire15_1_out_2));
  assign or_2_out = wire0_1_out_2 | wire1_1_out_2 | wire2_1_out_2 | wire3_1_out_2 | wire4_1_out_2 | wire5_1_out_2 | wire6_1_out_2 | wire7_1_out_2 | wire8_1_out_2 | wire9_1_out_2 | wire10_1_out_2 | wire11_1_out_2 | wire12_1_out_2 | wire13_1_out_2 | wire14_1_out_2 | wire15_1_out_2;  // OR_Gate or_2, 8 bits wide
  _7_Segment_Display u_7_segment_display_2 (
    .g(or_2_out[6]), .f(or_2_out[5]), .a(or_2_out[0]), .b(or_2_out[1]), .e(or_2_out[4]), .d(or_2_out[3]),
    .c(or_2_out[2]), .dp(or_2_out[7]));
endmodule

module ones_complement_adder1 (
  input  in_1,
  input  in_2,
  input  in_3,
  input  in_4,
  input  in_5,
  input  in_6,
  input  in_7,
  input  in_8,
  output out_9,
  output out_10,
  output out_11,
  output out_12
);

  wire sign_magnitude_adder_4_1_y0, sign_magnitude_adder_4_1_y1, sign_magnitude_adder_4_1_y2, xor_1_out,
       xor_2_out, xor_3_out, xor_4_out, xor_5_out, xor_6_out;

  xor xor_1 (xor_1_out, in_1, in_2);
  xor xor_2 (xor_2_out, in_3, in_1);
  xor xor_3 (xor_3_out, in_4, in_1);
  xor xor_4 (xor_4_out, in_5, in_6);
  xor xor_5 (xor_5_out, in_7, in_5);
  xor xor_6 (xor_6_out, in_8, in_5);
  sign_magnitude_adder_4 sign_magnitude_adder_4_1 (
    .A3(in_1), .A2(xor_1_out), .A1(xor_2_out), .A0(xor_3_out), .B3(in_5), .B2(xor_4_out), .B1(xor_5_out),
    .B0(xor_6_out), .Y3(out_9), .Y2(sign_magnitude_adder_4_1_y2), .Y1(sign_magnitude_adder_4_1_y1),
    .Y0(sign_magnitude_adder_4_1_y0));
  xor xor_7 (out_10, out_9, sign_magnitude_adder_4_1_y2);
  xor xor_8 (out_11, out_9, sign_magnitude_adder_4_1_y1);
  xor xor_9 (out_12, out_9, sign_magnitude_adder_4_1_y0);
endmodule

module ones_complement_adder2 (
  input  A3,
  input  A2,
  input  A1,
  input  A0,
  input  B3,
  input  B2,
  input  B1,
  input  B0,
  output Y1,
  output Y0,
  output Y3,
  output Y2
);

  wire full_adder_to_1real_1_co, full_adder_to_1real_2_co, full_adder_to_1real_3_co, full_adder_to_1real_4_co;

  full_adder_to_1real full_adder_to_1real_1 (
    .A(A0), .B(B0), .CL(full_adder_to_1real_4_co), .S(Y0), .CO(full_adder_to_1real_1_co));
  full_adder_to_1real full_adder_to_1real_2 (
    .A(A1), .B(B1), .CL(full_adder_to_1real_1_co), .S(Y1), .CO(full_adder_to_1real_2_co));
  full_adder_to_1real full_adder_to_1real_3 (
    .A(A2), .B(B2), .CL(full_adder_to_1real_2_co), .S(Y2), .CO(full_adder_to_1real_3_co));
  full_adder_to_1real full_adder_to_1real_4 (
    .A(A3), .B(B3), .CL(full_adder_to_1real_3_co), .S(Y3), .CO(full_adder_to_1real_4_co));
endmodule

module overflow_adder_4 (
  input  in_1,
  input  in_2,
  input  in_3,
  input  in_4,
  input  in_5,
  input  in_6,
  input  in_7,
  input  in_8,
  output out_9,
  output out_10,
  output out_11,
  output out_12
);

  wire and_1_out, and_2_out, not_1_out, not_2_out, not_3_out, or_1_out;

  not not_1 (not_1_out, out_9);
  not not_2 (not_2_out, in_5);
  not not_3 (not_3_out, in_1);
  and and_1 (and_1_out, in_5, not_1_out, in_1);
  and and_2 (and_2_out, not_2_out, out_9, not_3_out);
  adder_to_4 adder_to_4_1 (
    .A3(in_1), .A2(in_2), .A1(in_3), .A0(in_4), .B3(in_5), .B2(in_6), .B1(in_7), .B0(in_8), .Y3(out_9),
    .Y2(out_10), .Y1(out_11), .Y0(out_12));
  or or_1 (or_1_out, and_1_out, and_2_out);
  LED led_1 (.in(or_1_out));
endmodule

module adder_to_8 (
  input  B0,
  input  A0,
  input  A1,
  input  A2,
  input  A5,
  input  B1,
  input  A6,
  input  B2,
  input  A4,
  input  B5,
  input  B6,
  input  B7,
  input  A7,
  input  B3,
  input  A3,
  input  B4,
  output S5,
  output S4,
  output S2,
  output S7,
  output S1,
  output S3,
  output S0,
  output S6
);

  wire full_adder_to_1real_1_co, full_adder_to_1real_2_co, full_adder_to_1real_3_co,
       full_adder_to_1real_4_co, full_adder_to_1real_5_co, full_adder_to_1real_6_co, full_adder_to_1real_7_co;

  full_adder_to_1real full_adder_to_1real_1 (.A(A0), .B(B0), .CL(1'b0), .S(S0), .CO(full_adder_to_1real_1_co));
  full_adder_to_1real full_adder_to_1real_2 (
    .A(A1), .B(B1), .CL(full_adder_to_1real_1_co), .S(S1), .CO(full_adder_to_1real_2_co));
  full_adder_to_1real full_adder_to_1real_3 (
    .A(A2), .B(B2), .CL(full_adder_to_1real_2_co), .S(S2), .CO(full_adder_to_1real_3_co));
  full_adder_to_1real full_adder_to_1real_4 (
    .A(A3), .B(B3), .CL(full_adder_to_1real_3_co), .S(S3), .CO(full_adder_to_1real_4_co));
  full_adder_to_1real full_adder_to_1real_5 (
    .A(A4), .B(B4), .CL(full_adder_to_1real_4_co), .S(S4), .CO(full_adder_to_1real_5_co));
  full_adder_to_1real full_adder_to_1real_6 (
    .A(A5), .B(B5), .CL(full_adder_to_1real_5_co), .S(S5), .CO(full_adder_to_1real_6_co));
  full_adder_to_1real full_adder_to_1real_7 (
    .A(A6), .B(B6), .CL(full_adder_to_1real_6_co), .S(S6), .CO(full_adder_to_1real_7_co));
  full_adder_to_1real full_adder_to_1real_8 (.A(A7), .B(B7), .CL(full_adder_to_1real_7_co), .S(S7));  // open: CO
endmodule
