// Logisim project adder1.circ as structural Verilog
module full_adder_to_1real (
  input  A,
  input  B,
  input  CL,
  output S,
  output CO
);

  wire and_1_out, and_2_out, and_3_out, and_4_out, and_5_out, and_6_out, and_7_out, not_1_out, not_2_out,
       not_3_out;

  not not_1 (not_1_out, A);
  not not_2 (not_2_out, B);
  not not_3 (not_3_out, CL);
  and and_1 (and_1_out, not_1_out, not_2_out, not_3_out);
  and and_2 (and_2_out, A, not_2_out, CL);
  and and_3 (and_3_out, not_1_out, B, CL);
  and and_4 (and_4_out, A, B, not_3_out);
  and and_5 (and_5_out, not_1_out, not_2_out);
  and and_6 (and_6_out, not_2_out, not_3_out);
  and and_7 (and_7_out, not_1_out, not_3_out);
  nor nor_1 (S, and_1_out, and_2_out, and_3_out, and_4_out);
  nor nor_2 (CO, and_5_out, and_6_out, and_7_out);
endmodule

module half_adder_to_1 (
  input  A,
  input  B,
  output S,
  output CO
);

  xor xor_1 (S, A, B);
  and and_1 (CO, A, B);
endmodule

module full_adder_to_1false (
  input  A,
  input  B,
  input  CIN,
  output S,
  output CO
);

  wire half_adder_to_1_1_co, half_adder_to_1_1_s, half_adder_to_1_2_co;

  half_adder_to_1 half_adder_to_1_1 (.A(A), .B(B), .S(half_adder_to_1_1_s), .CO(half_adder_to_1_1_co));
  half_adder_to_1 half_adder_to_1_2 (.A(half_adder_to_1_1_s), .B(CIN), .S(S), .CO(half_adder_to_1_2_co));
  or or_1 (CO, half_adder_to_1_2_co, half_adder_to_1_1_co);
endmodule

module adder_to_4 (
);

  wire [3:0] dipswitch_1_sw4;

  DipSwitch dipswitch_1 (
    .sw1(dipswitch_1_sw4[3]), .sw2(dipswitch_1_sw4[2]), .sw3(dipswitch_1_sw4[1]), .sw4(dipswitch_1_sw4[0]));  // open: sw5, sw6, sw7, sw8
  Decoder #(.select(4)) decoder_1 (
    .sel(dipswitch_1_sw4), .en(1'b1));  // open: out0, out1, out2, out3, out4, out5, out6, out7, out8, out9, out10, out11, out12, out13, out14, out15
  _7_Segment_Display u_7_segment_display_1 ();  // open: g, f, a, b, e, d, c, dp
  full_adder_to_1real full_adder_to_1real_1 ();  // open: A, B, CL, S, CO
endmodule
