// Logisim project comparator1.circ as structural Verilog
module digital_comparator4 (
);

  wire and_1_out, dipswitch_1_sw1, dipswitch_1_sw2, dipswitch_1_sw3, dipswitch_1_sw4, dipswitch_2_sw1,
       dipswitch_2_sw2, dipswitch_2_sw3, dipswitch_2_sw4, not_1_out, not_2_out, not_3_out, not_4_out,
       xor_1_out, xor_2_out, xor_3_out, xor_4_out;

  DipSwitch dipswitch_1 (
    .sw1(dipswitch_1_sw1), .sw2(dipswitch_1_sw2), .sw3(dipswitch_1_sw3), .sw4(dipswitch_1_sw4));  // open: sw5, sw6, sw7, sw8
  DipSwitch dipswitch_2 (
    .sw1(dipswitch_2_sw1), .sw2(dipswitch_2_sw2), .sw3(dipswitch_2_sw3), .sw4(dipswitch_2_sw4));  // open: sw5, sw6, sw7, sw8
  xor xor_1 (xor_1_out, dipswitch_1_sw1, dipswitch_2_sw1);
  xor xor_2 (xor_2_out, dipswitch_1_sw2, dipswitch_2_sw2);
  xor xor_3 (xor_3_out, dipswitch_1_sw3, dipswitch_2_sw3);
  xor xor_4 (xor_4_out, dipswitch_1_sw4, dipswitch_2_sw4);
  not not_1 (not_1_out, xor_1_out);
  not not_2 (not_2_out, xor_2_out);
  not not_3 (not_3_out, xor_3_out);
  not not_4 (not_4_out, xor_4_out);
  and and_1 (and_1_out, not_1_out, not_2_out, not_3_out, not_4_out);
  LED led_1 (.in(and_1_out));
endmodule
