// Logisim project counting.circ as structural Verilog: 1 circuit, main circuit main
module main (
);

  wire [3:0] dipswitch_1_sw1;
  wire [15:4] dipswitch_1_sw5;

  DipSwitch dipswitch_1 (
    .sw1(dipswitch_1_sw1[0]), .sw2(dipswitch_1_sw1[1]), .sw3(dipswitch_1_sw1[2]), .sw4(dipswitch_1_sw1[3]),
    .sw5(dipswitch_1_sw5[4]), .sw6(dipswitch_1_sw5[5]), .sw7(dipswitch_1_sw5[6]), .sw8(dipswitch_1_sw5[7]));
  DipSwitch dipswitch_2 (
    .sw1(dipswitch_1_sw5[8]), .sw2(dipswitch_1_sw5[9]), .sw3(dipswitch_1_sw5[10]), .sw4(dipswitch_1_sw5[11]),
    .sw5(dipswitch_1_sw5[12]), .sw6(dipswitch_1_sw5[13]), .sw7(dipswitch_1_sw5[14]), .sw8(dipswitch_1_sw5[15]));
  Hex_Digit_Display hex_digit_display_1 (.value(dipswitch_1_sw1));  // open: dp
  Hex_Digit_Display hex_digit_display_2 (.value(dipswitch_1_sw5[7:4]));  // open: dp
  Hex_Digit_Display hex_digit_display_3 (.value(dipswitch_1_sw5[11:8]));  // open: dp
  Hex_Digit_Display hex_digit_display_4 (.value(dipswitch_1_sw5[15:12]));  // open: dp
endmodule
