// Logisim project hexadecimal_seven_segment_display.circ as structural Verilog: 17 circuits, main circuit wire0
module wire0 (
  input  in_1,
  output [7:0] out_2
);

  assign out_2 = {8{in_1}} & 8'h3f;  // AND_Gate and_1, 8 bits wide
endmodule

module wire1 (
  input  in_1,
  output [7:0] out_2
);

  assign out_2 = {8{in_1}} & 8'h6;  // AND_Gate and_1, 8 bits wide
endmodule

module wire2 (
  input  in_1,
  output [7:0] out_2
);

  assign out_2 = {8{in_1}} & 8'h5b;  // AND_Gate and_1, 8 bits wide
endmodule

module wire3 (
  input  in_1,
  output [7:0] out_2
);

  assign out_2 = {8{in_1}} & 8'h4f;  // AND_Gate and_1, 8 bits wide
endmodule

module wire4 (
  input  in_1,
  output [7:0] out_2
);

  assign out_2 = {8{in_1}} & 8'h66;  // AND_Gate and_1, 8 bits wide
endmodule

module wire5 (
  input  in_1,
  output [7:0] out_2
);

  assign out_2 = {8{in_1}} & 8'h6d;  // AND_Gate and_1, 8 bits wide
endmodule

module wire6 (
  input  in_1,
  output [7:0] out_2
);

  assign out_2 = {8{in_1}} & 8'h7d;  // AND_Gate and_1, 8 bits wide
endmodule

module wire7 (
  input  in_1,
  output [7:0] out_2
);

  assign out_2 = {8{in_1}} & 8'h7;  // AND_Gate and_1, 8 bits wide
endmodule

module wire8 (
  input  in_1,
  output [7:0] out_2
);

  assign out_2 = {8{in_1}} & 8'h7f;  // AND_Gate and_1, 8 bits wide
endmodule

module wire9 (
  input  in_1,
  output [7:0] out_2
);

  assign out_2 = {8{in_1}} & 8'h6f;  // AND_Gate and_1, 8 bits wide
endmodule

module wire10 (
  input  in_1,
  output [7:0] out_2
);

  assign out_2 = {8{in_1}} & 8'h77;  // AND_Gate and_1, 8 bits wide
endmodule

module wire11 (
  input  in_1,
  output [7:0] out_2
);

  assign out_2 = {8{in_1}} & 8'h7c;  // AND_Gate and_1, 8 bits wide
endmodule

module wire12 (
  input  in_1,
  output [7:0] out_2
);

  assign out_2 = {8{in_1}} & 8'h39;  // AND_Gate and_1, 8 bits wide
endmodule

module wire13 (
  input  in_1,
  output [7:0] out_2
);

  assign out_2 = {8{in_1}} & 8'h5e;  // AND_Gate and_1, 8 bits wide
endmodule

module wire14 (
  input  in_1,
  output [7:0] out_2
);

  assign out_2 = {8{in_1}} & 8'h79;  // AND_Gate and_1, 8 bits wide
endmodule

module wire15 (
  input  in_1,
  output [7:0] out_2
);

  assign out_2 = {8{in_1}} & 8'h71;  // AND_Gate and_1, 8 bits wide
endmodule

module hex_seven_display (
);

  wire decoder_1_out0, decoder_1_out1, decoder_1_out2, decoder_1_out3, decoder_1_out4, decoder_1_out5,
       decoder_1_out6, decoder_1_out7, decoder_1_out8, decoder_1_out9, decoder_1_out10, decoder_1_out11,
       decoder_1_out12, decoder_1_out13, decoder_1_out14, decoder_1_out15;
  wire [3:0] dipswitch_1_sw4;
  wire [7:0] or_1_out, wire0_1_out_2, wire1_1_out_2, wire2_1_out_2, wire3_1_out_2, wire4_1_out_2,
       wire5_1_out_2, wire6_1_out_2, wire7_1_out_2, wire8_1_out_2, wire9_1_out_2, wire10_1_out_2,
       wire11_1_out_2, wire12_1_out_2, wire13_1_out_2, wire14_1_out_2, wire15_1_out_2;

  DipSwitch dipswitch_1 (
    .sw1(dipswitch_1_sw4[3]), .sw2(dipswitch_1_sw4[2]), .sw3(dipswitch_1_sw4[1]), .sw4(dipswitch_1_sw4[0]));  // open: sw5, sw6, sw7, sw8
  Decoder #(.select(4)) decoder_1 (
    .out0(decoder_1_out0), .out1(decoder_1_out1), .out2(decoder_1_out2), .out3(decoder_1_out3),
    .out4(decoder_1_out4), .out5(decoder_1_out5), .out6(decoder_1_out6), .out7(decoder_1_out7),
    .out8(decoder_1_out8), .out9(decoder_1_out9), .out10(decoder_1_out10), .out11(decoder_1_out11),
    .out12(decoder_1_out12), .out13(decoder_1_out13), .out14(decoder_1_out14), .out15(decoder_1_out15),
    .sel(dipswitch_1_sw4), .en(1'b1));
  wire0 wire0_1 (.in_1(decoder_1_out0), .out_2(wire0_1_out_2));
  wire1 wire1_1 (.in_1(decoder_1_out1), .out_2(wire1_1_out_2));
  wire2 wire2_1 (.in_1(decoder_1_out2), .out_2(wire2_1_out_2));
  wire3 wire3_1 (.in_1(decoder_1_out3), .out_2(wire3_1_out_2));
  wire4 wire4_1 (.in_1(decoder_1_out4), .out_2(wire4_1_out_2));
  wire5 wire5_1 (.in_1(decoder_1_out5), .out_2(wire5_1_out_2));
  wire6 wire6_1 (.in_1(decoder_1_out6), .out_2(wire6_1_out_2));
  wire7 wire7_1 (.in_1(decoder_1_out7), .out_2(wire7_1_out_2));
  wire8 wire8_1 (.in_1(decoder_1_out8), .out_2(wire8_1_out_2));
  wire9 wire9_1 (.in_1(decoder_1_out9), .out_2(wire9_1_out_2));
  wire10 wire10_1 (.in_1(decoder_1_out10), .out_2(wire10_1_out_2));
  wire11 wire11_1 (.in_1(decoder_1_out11), .out_2(wire11_1_out_2));
  wire12 wire12_1 (.in_1(decoder_1_out12), .out_2(wire12_1_out_2));
  wire13 wire13_1 (.in_1(decoder_1_out13), .out_2(wire13_1_out_2));
  wire14 wire14_1 (.in_1(decoder_1_out14), .out_2(wire14_1_out_2));
  wire15 wire15_1 (.in_1(decoder_1_out15), .out_2(wire15_1_out_2));
  assign or_1_out = wire0_1_out_2 | wire1_1_out_2 | wire2_1_out_2 | wire3_1_out_2 | wire4_1_out_2 | wire5_1_out_2 | wire6_1_out_2 | wire7_1_out_2 | wire8_1_out_2 | wire9_1_out_2 | wire10_1_out_2 | wire11_1_out_2 | wire12_1_out_2 | wire13_1_out_2 | wire14_1_out_2 | wire15_1_out_2;  // OR_Gate or_1, 8 bits wide
  _7_Segment_Display u_7_segment_display_1 (
    .g(or_1_out[6]), .f(or_1_out[5]), .a(or_1_out[0]), .b(or_1_out[1]), .e(or_1_out[4]), .d(or_1_out[3]),
    .c(or_1_out[2]), .dp(or_1_out[7]));
endmodule
