// Logisim project mux.circ as structural Verilog: 4 circuits, main circuit mux1_bit2_to_1
module mux1_bit2_to_1 (
  input  D0,
  input  S,
  input  D1,
  output Y
);

  wire and_1_out, and_2_out, not_1_out;

  not not_1 (not_1_out, S);
  and and_1 (and_1_out, D0, not_1_out);
  and and_2 (and_2_out, S, D1);
  or or_1 (Y, and_1_out, and_2_out);
endmodule

module mux1_bit4_to_1 (
  input  D0,
  input  D1,
  input  D2,
  input  D3,
  input  S1,
  input  S2,
  output Y
);

  wire and_1_out, and_2_out, and_3_out, and_4_out, and_5_out, and_6_out, and_7_out, and_8_out, not_1_out,
       not_2_out;

  not not_1 (not_1_out, S1);
  not not_2 (not_2_out, S2);
  and and_1 (and_1_out, not_1_out, not_2_out);
  and and_2 (and_2_out, not_2_out, S1);
  and and_3 (and_3_out, not_1_out, S2);
  and and_4 (and_4_out, S1, S2);
  and and_5 (and_5_out, D0, and_1_out);
  and and_6 (and_6_out, D1, and_2_out);
  and and_7 (and_7_out, D2, and_3_out);
  and and_8 (and_8_out, D3, and_4_out);
  or or_1 (Y, and_5_out, and_6_out, and_7_out, and_8_out);
endmodule

module mux3_bit4_to_1 (
  input  [2:0] IN0,
  input  [2:0] IN1,
  input  [2:0] IN2,
  input  [2:0] IN3,
  input  [1:0] S,
  output [2:0] Y
);

  mux1_bit4_to_1 mux1_bit4_to_1_1 (.D0(IN0[0]), .D1(IN1[0]), .D2(IN2[0]), .D3(IN3[0]), .S1(S[0]), .S2(S[1]), .Y(Y[0]));
  mux1_bit4_to_1 mux1_bit4_to_1_2 (.D0(IN0[1]), .D1(IN1[1]), .D2(IN2[1]), .D3(IN3[1]), .S1(S[0]), .S2(S[1]), .Y(Y[1]));
  mux1_bit4_to_1 mux1_bit4_to_1_3 (.D0(IN0[2]), .D1(IN1[2]), .D2(IN2[2]), .D3(IN3[2]), .S1(S[0]), .S2(S[1]), .Y(Y[2]));
endmodule

module switch_radix_display (
);

  wire and_1_out, and_2_out, and_3_out, and_4_out, and_5_out, and_6_out, and_7_out, and_8_out, and_9_out,
       decoder_1_out0, decoder_1_out1, decoder_1_out2, decoder_1_out3, decoder_1_out4, decoder_1_out5,
       decoder_1_out6, decoder_1_out7, decoder_1_out8, decoder_1_out9, decoder_1_out10, decoder_1_out11,
       decoder_1_out12, decoder_1_out13, decoder_1_out14, decoder_1_out15, dipswitch_1_sw5, not_1_out,
       or_1_out, or_2_out, or_3_out, or_4_out, or_5_out, or_6_out, or_7_out, or_8_out, or_9_out, or_10_out,
       or_11_out, or_12_out, or_13_out, or_14_out, or_15_out, or_16_out, or_17_out, or_18_out, or_19_out,
       or_20_out, or_21_out, or_22_out, or_23_out;
  wire [3:0] dipswitch_1_sw4;

  DipSwitch dipswitch_1 (
    .sw1(dipswitch_1_sw4[3]), .sw2(dipswitch_1_sw4[2]), .sw3(dipswitch_1_sw4[1]), .sw4(dipswitch_1_sw4[0]),
    .sw5(dipswitch_1_sw5));  // open: sw6, sw7, sw8
  Decoder #(.select(4)) decoder_1 (
    .out0(decoder_1_out0), .out1(decoder_1_out1), .out2(decoder_1_out2), .out3(decoder_1_out3),
    .out4(decoder_1_out4), .out5(decoder_1_out5), .out6(decoder_1_out6), .out7(decoder_1_out7),
    .out8(decoder_1_out8), .out9(decoder_1_out9), .out10(decoder_1_out10), .out11(decoder_1_out11),
    .out12(decoder_1_out12), .out13(decoder_1_out13), .out14(decoder_1_out14), .out15(decoder_1_out15),
    .sel(dipswitch_1_sw4), .en(1'b1));
  not not_1 (not_1_out, dipswitch_1_sw5);
  or or_1 (or_1_out, decoder_1_out0, decoder_1_out2, decoder_1_out3, decoder_1_out5, decoder_1_out6, decoder_1_out7, decoder_1_out8, decoder_1_out9);
  or or_2 (or_2_out, decoder_1_out0, decoder_1_out1, decoder_1_out2, decoder_1_out3, decoder_1_out4, decoder_1_out7, decoder_1_out8, decoder_1_out9);
  or or_3 (or_3_out, decoder_1_out0, decoder_1_out1, decoder_1_out3, decoder_1_out4, decoder_1_out5, decoder_1_out6, decoder_1_out7, decoder_1_out8, decoder_1_out9);
  or or_4 (or_4_out, decoder_1_out0, decoder_1_out2, decoder_1_out3, decoder_1_out5, decoder_1_out6, decoder_1_out8, decoder_1_out9);
  or or_5 (or_5_out, decoder_1_out0, decoder_1_out2, decoder_1_out6, decoder_1_out8);
  or or_6 (or_6_out, decoder_1_out0, decoder_1_out4, decoder_1_out5, decoder_1_out6, decoder_1_out8, decoder_1_out9);
  or or_7 (or_7_out, decoder_1_out2, decoder_1_out3, decoder_1_out4, decoder_1_out5, decoder_1_out6, decoder_1_out8, decoder_1_out9);
  and and_1 (and_1_out, or_15_out, not_1_out);
  and and_2 (and_2_out, dipswitch_1_sw5, or_17_out);
  or or_8 (or_8_out, decoder_1_out10, decoder_1_out12, decoder_1_out14, decoder_1_out15);
  or or_9 (or_9_out, decoder_1_out10, decoder_1_out13);
  or or_10 (or_10_out, decoder_1_out10, decoder_1_out11, decoder_1_out13);
  or or_11 (or_11_out, decoder_1_out11, decoder_1_out12, decoder_1_out13, decoder_1_out14);
  or or_12 (or_12_out, decoder_1_out10, decoder_1_out11, decoder_1_out12, decoder_1_out13, decoder_1_out14, decoder_1_out15);
  or or_13 (or_13_out, decoder_1_out10, decoder_1_out11, decoder_1_out12, decoder_1_out14, decoder_1_out15);
  or or_14 (or_14_out, decoder_1_out10, decoder_1_out11, decoder_1_out13, decoder_1_out14, decoder_1_out15);
  or or_15 (or_15_out, decoder_1_out10, decoder_1_out13, decoder_1_out12, decoder_1_out14, decoder_1_out15, decoder_1_out11);
  _7_Segment_Display u_7_segment_display_1 (
    .g(or_16_out), .f(or_19_out), .a(or_18_out), .b(or_20_out), .e(or_23_out), .d(or_22_out), .c(or_21_out),
    .dp(and_1_out));
  or or_16 (or_16_out, or_7_out, and_9_out);
  or or_17 (or_17_out, or_8_out, or_9_out, or_10_out, or_11_out, or_12_out, or_13_out, or_14_out);
  or or_18 (or_18_out, or_1_out, and_3_out);
  or or_19 (or_19_out, or_6_out, and_8_out);
  or or_20 (or_20_out, or_2_out, and_4_out);
  or or_21 (or_21_out, and_5_out, or_3_out);
  or or_22 (or_22_out, or_4_out, and_6_out);
  or or_23 (or_23_out, or_5_out, and_7_out);
  and and_3 (and_3_out, or_8_out, and_2_out);
  and and_4 (and_4_out, or_9_out, and_2_out);
  and and_5 (and_5_out, or_10_out, and_2_out);
  and and_6 (and_6_out, or_11_out, and_2_out);
  and and_7 (and_7_out, or_12_out, and_2_out);
  and and_8 (and_8_out, or_13_out, and_2_out);
  and and_9 (and_9_out, or_14_out, and_2_out);
endmodule
