// Logisim project scpu.circ as structural Verilog: 16 circuits, main circuit Read_Only_memory_1to10
module Read_Only_memory_1to10 (
  input  A2,
  input  A1,
  input  A0,
  output Q7,
  output Q6,
  output Q5,
  output Q4,
  output Q3,
  output Q2,
  output Q1,
  output Q0
);

  wire and_1_out, and_2_out, and_3_out, and_4_out, and_5_out, and_6_out, and_7_out, and_8_out, and_9_out,
       and_10_out, and_11_out, and_12_out, and_13_out, and_14_out, and_15_out, and_16_out, and_17_out,
       and_18_out, and_19_out, and_20_out, and_21_out, and_22_out, and_23_out, and_24_out, and_25_out,
       and_26_out, and_27_out, and_28_out, and_29_out, and_30_out, and_31_out, and_32_out, and_33_out,
       and_34_out, and_35_out, and_36_out, and_37_out, and_38_out, and_39_out, and_40_out, and_41_out,
       and_42_out, and_43_out, and_44_out, and_45_out, and_46_out, and_47_out, and_48_out, and_49_out,
       and_50_out, and_51_out, and_52_out, and_53_out, and_54_out, and_55_out, and_56_out, and_57_out,
       and_58_out, and_59_out, and_60_out, and_61_out, and_62_out, and_63_out, and_64_out, decoder_1_out0,
       decoder_1_out1, decoder_1_out2, decoder_1_out3, decoder_1_out4, decoder_1_out5, decoder_1_out6,
       decoder_1_out7;

  Decoder #(.select(3)) decoder_1 (
    .out0(decoder_1_out0), .out1(decoder_1_out1), .out2(decoder_1_out2), .out3(decoder_1_out3),
    .out4(decoder_1_out4), .out5(decoder_1_out5), .out6(decoder_1_out6), .out7(decoder_1_out7),
    .sel({A2, A1, A0}), .en(1'b1));
  or or_1 (Q7, and_1_out, and_2_out, and_3_out, and_4_out, and_5_out, and_6_out, and_7_out, and_8_out);
  and and_1 (and_1_out, decoder_1_out0, 1'b1);
  and and_2 (and_2_out, decoder_1_out1, 1'b1);
  and and_3 (and_3_out, decoder_1_out2, 1'b1);
  and and_4 (and_4_out, decoder_1_out3, 1'b1);
  and and_5 (and_5_out, decoder_1_out4, 1'b0);
  and and_6 (and_6_out, decoder_1_out5, 1'b0);
  and and_7 (and_7_out, decoder_1_out6, 1'b1);
  and and_8 (and_8_out, decoder_1_out7, 1'b1);
  and and_9 (and_9_out, decoder_1_out0, 1'b0);
  and and_10 (and_10_out, decoder_1_out1, 1'b0);
  and and_11 (and_11_out, decoder_1_out2, 1'b0);
  and and_12 (and_12_out, decoder_1_out3, 1'b0);
  and and_13 (and_13_out, decoder_1_out4, 1'b0);
  and and_14 (and_14_out, decoder_1_out5, 1'b0);
  and and_15 (and_15_out, decoder_1_out6, 1'b1);
  and and_16 (and_16_out, decoder_1_out7, 1'b1);
  or or_2 (Q6, and_9_out, and_10_out, and_11_out, and_12_out, and_13_out, and_14_out, and_15_out, and_16_out);
  and and_17 (and_17_out, decoder_1_out0, 1'b0);
  and and_18 (and_18_out, decoder_1_out1, 1'b0);
  and and_19 (and_19_out, decoder_1_out2, 1'b1);
  and and_20 (and_20_out, decoder_1_out3, 1'b1);
  and and_21 (and_21_out, decoder_1_out4, 1'b0);
  and and_22 (and_22_out, decoder_1_out5, 1'b1);
  and and_23 (and_23_out, decoder_1_out6, 1'b0);
  and and_24 (and_24_out, decoder_1_out7, 1'b0);
  or or_3 (Q5, and_17_out, and_18_out, and_19_out, and_20_out, and_21_out, and_22_out, and_23_out, and_24_out);
  and and_25 (and_25_out, decoder_1_out0, 1'b0);
  and and_26 (and_26_out, decoder_1_out1, 1'b1);
  and and_27 (and_27_out, decoder_1_out2, 1'b0);
  and and_28 (and_28_out, decoder_1_out3, 1'b1);
  and and_29 (and_29_out, decoder_1_out4, 1'b1);
  and and_30 (and_30_out, decoder_1_out5, 1'b0);
  and and_31 (and_31_out, decoder_1_out6, 1'b1);
  and and_32 (and_32_out, decoder_1_out7, 1'b1);
  and and_33 (and_33_out, decoder_1_out0, 1'b1);
  and and_34 (and_34_out, decoder_1_out1, 1'b0);
  and and_35 (and_35_out, decoder_1_out2, 1'b0);
  and and_36 (and_36_out, decoder_1_out3, 1'b0);
  and and_37 (and_37_out, decoder_1_out4, 1'b0);
  and and_38 (and_38_out, decoder_1_out5, 1'b1);
  and and_39 (and_39_out, decoder_1_out6, 1'b0);
  and and_40 (and_40_out, decoder_1_out7, 1'b1);
  or or_4 (Q4, and_25_out, and_26_out, and_27_out, and_28_out, and_29_out, and_30_out, and_31_out, and_32_out);
  and and_41 (and_41_out, decoder_1_out0, 1'b0);
  and and_42 (and_42_out, decoder_1_out1, 1'b0);
  and and_43 (and_43_out, decoder_1_out2, 1'b0);
  and and_44 (and_44_out, decoder_1_out3, 1'b0);
  and and_45 (and_45_out, decoder_1_out4, 1'b1);
  and and_46 (and_46_out, decoder_1_out5, 1'b0);
  and and_47 (and_47_out, decoder_1_out6, 1'b0);
  and and_48 (and_48_out, decoder_1_out7, 1'b1);
  or or_5 (Q3, and_33_out, and_34_out, and_35_out, and_36_out, and_37_out, and_38_out, and_39_out, and_40_out);
  and and_49 (and_49_out, decoder_1_out0, 1'b1);
  and and_50 (and_50_out, decoder_1_out1, 1'b0);
  and and_51 (and_51_out, decoder_1_out2, 1'b0);
  and and_52 (and_52_out, decoder_1_out3, 1'b0);
  and and_53 (and_53_out, decoder_1_out4, 1'b1);
  and and_54 (and_54_out, decoder_1_out5, 1'b0);
  and and_55 (and_55_out, decoder_1_out6, 1'b0);
  and and_56 (and_56_out, decoder_1_out7, 1'b1);
  and and_57 (and_57_out, decoder_1_out0, 1'b0);
  and and_58 (and_58_out, decoder_1_out1, 1'b0);
  and and_59 (and_59_out, decoder_1_out2, 1'b0);
  and and_60 (and_60_out, decoder_1_out3, 1'b1);
  and and_61 (and_61_out, decoder_1_out4, 1'b1);
  and and_62 (and_62_out, decoder_1_out5, 1'b1);
  and and_63 (and_63_out, decoder_1_out6, 1'b1);
  and and_64 (and_64_out, decoder_1_out7, 1'b1);
  or or_6 (Q2, and_41_out, and_42_out, and_43_out, and_44_out, and_45_out, and_46_out, and_47_out, and_48_out);
  or or_7 (Q1, and_49_out, and_50_out, and_51_out, and_52_out, and_53_out, and_54_out, and_55_out, and_56_out);
  or or_8 (Q0, and_57_out, and_58_out, and_59_out, and_60_out, and_61_out, and_62_out, and_63_out, and_64_out);
endmodule

module Random_access_memory (
  input  raddr2_1,
  input  raddr2_0,
  input  D7,
  input  D6,
  input  D4,
  input  D3,
  input  D5,
  input  D2,
  input  D1,
  input  D0,
  input  raddr1_1,
  input  raddr1_0,
  input  clk,
  input  WEN,
  input  waddr1,
  input  waddr0,
  input  reset,
  output rdata2_2,
  output rdata2_1,
  output rdata2_0,
  output rdata2_3,
  output rdata2_4,
  output rdata2_5,
  output rdata1_3,
  output rdata1_2,
  output rdata1_1,
  output rdata1_0,
  output rdata1_4,
  output rdata1_5,
  output Q7,
  output Q6,
  output Q5,
  output Q4,
  output Q3,
  output Q2,
  output Q1,
  output Q0
);

  wire and_1_out, and_2_out, and_3_out, and_4_out, and_5_out, and_6_out, and_7_out, and_8_out, and_9_out,
       and_10_out, and_11_out, and_12_out, and_13_out, and_14_out, and_15_out, and_16_out, and_17_out,
       and_18_out, and_19_out, and_20_out, and_21_out, and_22_out, and_23_out, and_24_out, and_25_out,
       and_26_out, and_27_out, and_28_out, and_29_out, and_30_out, and_31_out, and_32_out, and_33_out,
       and_34_out, and_35_out, and_36_out, and_37_out, and_38_out, and_39_out, and_40_out, and_41_out,
       and_42_out, and_43_out, and_44_out, and_45_out, and_46_out, and_47_out, and_48_out, and_49_out,
       and_50_out, and_51_out, and_52_out, and_53_out, and_54_out, and_55_out, and_56_out, and_57_out,
       and_58_out, and_59_out, and_60_out, and_61_out, and_62_out, and_63_out, and_64_out, and_65_out,
       and_66_out, and_67_out, and_68_out, and_69_out, and_70_out, and_71_out, and_72_out, and_73_out,
       and_74_out, and_75_out, and_76_out, and_77_out, and_78_out, and_79_out, and_80_out, and_81_out,
       and_82_out, and_83_out, and_84_out, and_85_out, and_86_out, and_87_out, and_88_out, and_89_out,
       and_90_out, and_91_out, and_92_out, decoder_1_out0, decoder_1_out1, decoder_1_out2, decoder_1_out3,
       decoder_2_out0, decoder_2_out1, decoder_2_out2, decoder_2_out3, decoder_3_out0, decoder_3_out1,
       decoder_3_out2, decoder_3_out3, enable_d_flip_flop_1_q, enable_d_flip_flop_2_q,
       enable_d_flip_flop_3_q, enable_d_flip_flop_4_q, enable_d_flip_flop_5_q, enable_d_flip_flop_6_q,
       enable_d_flip_flop_7_q, enable_d_flip_flop_8_q, enable_d_flip_flop_9_q, enable_d_flip_flop_10_q,
       enable_d_flip_flop_11_q, enable_d_flip_flop_12_q, enable_d_flip_flop_13_q, enable_d_flip_flop_14_q,
       enable_d_flip_flop_15_q, enable_d_flip_flop_16_q, enable_d_flip_flop_17_q, enable_d_flip_flop_18_q,
       enable_d_flip_flop_19_q, enable_d_flip_flop_20_q, enable_d_flip_flop_21_q, enable_d_flip_flop_22_q,
       enable_d_flip_flop_23_q, enable_d_flip_flop_24_q, enable_d_flip_flop_25_q, enable_d_flip_flop_26_q,
       enable_d_flip_flop_27_q, enable_d_flip_flop_28_q, enable_d_flip_flop_29_q, enable_d_flip_flop_30_q,
       enable_d_flip_flop_31_q, enable_d_flip_flop_32_q, not_1_out, or_1_out, or_2_out, or_3_out, or_4_out;

  Decoder #(.select(2)) decoder_1 (
    .out0(decoder_1_out0), .out1(decoder_1_out1), .out2(decoder_1_out2), .out3(decoder_1_out3),
    .sel({raddr1_1, raddr1_0}), .en(1'b1));
  Decoder #(.select(2)) decoder_2 (
    .out0(decoder_2_out0), .out1(decoder_2_out1), .out2(decoder_2_out2), .out3(decoder_2_out3),
    .sel({raddr2_1, raddr2_0}), .en(1'b1));
  Decoder #(.select(2)) decoder_3 (
    .out0(decoder_3_out0), .out1(decoder_3_out1), .out2(decoder_3_out2), .out3(decoder_3_out3),
    .sel({waddr1, waddr0}), .en(1'b1));
  not not_1 (not_1_out, reset);
  or or_1 (or_1_out, reset, and_1_out);
  and and_1 (and_1_out, decoder_3_out0, WEN);
  and and_2 (and_2_out, decoder_3_out1, WEN);
  or or_2 (or_2_out, reset, and_2_out);
  and and_3 (and_3_out, decoder_3_out2, WEN);
  or or_3 (or_3_out, reset, and_3_out);
  and and_4 (and_4_out, decoder_3_out3, WEN);
  or or_4 (or_4_out, reset, and_4_out);
  and and_5 (and_5_out, not_1_out, D7);
  Enable_D_flip_flop enable_d_flip_flop_1 (
    .CLK(clk), .D(and_5_out), .ENABLE(or_1_out), .Q(enable_d_flip_flop_1_q));  // open: NOTQ
  Enable_D_flip_flop enable_d_flip_flop_2 (
    .CLK(clk), .D(and_5_out), .ENABLE(or_2_out), .Q(enable_d_flip_flop_2_q));  // open: NOTQ
  Enable_D_flip_flop enable_d_flip_flop_3 (
    .CLK(clk), .D(and_5_out), .ENABLE(or_3_out), .Q(enable_d_flip_flop_3_q));  // open: NOTQ
  Enable_D_flip_flop enable_d_flip_flop_4 (
    .CLK(clk), .D(and_5_out), .ENABLE(or_4_out), .Q(enable_d_flip_flop_4_q));  // open: NOTQ
  and and_6 (and_6_out, D6, not_1_out);
  and and_7 (and_7_out, enable_d_flip_flop_1_q, decoder_3_out0);
  and and_8 (and_8_out, enable_d_flip_flop_2_q, decoder_3_out1);
  and and_9 (and_9_out, enable_d_flip_flop_3_q, decoder_3_out2);
  and and_10 (and_10_out, enable_d_flip_flop_4_q, decoder_3_out3);
  or or_5 (Q7, and_10_out, and_9_out, and_8_out, and_7_out);
  Enable_D_flip_flop enable_d_flip_flop_5 (
    .CLK(clk), .D(and_6_out), .ENABLE(or_1_out), .Q(enable_d_flip_flop_5_q));  // open: NOTQ
  Enable_D_flip_flop enable_d_flip_flop_6 (
    .CLK(clk), .D(and_6_out), .ENABLE(or_2_out), .Q(enable_d_flip_flop_6_q));  // open: NOTQ
  Enable_D_flip_flop enable_d_flip_flop_7 (
    .CLK(clk), .D(and_6_out), .ENABLE(or_3_out), .Q(enable_d_flip_flop_7_q));  // open: NOTQ
  Enable_D_flip_flop enable_d_flip_flop_8 (
    .CLK(clk), .D(and_6_out), .ENABLE(or_4_out), .Q(enable_d_flip_flop_8_q));  // open: NOTQ
  and and_11 (and_11_out, D5, not_1_out);
  and and_12 (and_12_out, enable_d_flip_flop_5_q, decoder_3_out0);
  and and_13 (and_13_out, enable_d_flip_flop_6_q, decoder_3_out1);
  and and_14 (and_14_out, enable_d_flip_flop_7_q, decoder_3_out2);
  and and_15 (and_15_out, enable_d_flip_flop_8_q, decoder_3_out3);
  or or_6 (Q6, and_15_out, and_14_out, and_13_out, and_12_out);
  Enable_D_flip_flop enable_d_flip_flop_9 (
    .CLK(clk), .D(and_11_out), .ENABLE(or_1_out), .Q(enable_d_flip_flop_9_q));  // open: NOTQ
  Enable_D_flip_flop enable_d_flip_flop_10 (
    .CLK(clk), .D(and_11_out), .ENABLE(or_2_out), .Q(enable_d_flip_flop_10_q));  // open: NOTQ
  Enable_D_flip_flop enable_d_flip_flop_11 (
    .CLK(clk), .D(and_11_out), .ENABLE(or_3_out), .Q(enable_d_flip_flop_11_q));  // open: NOTQ
  Enable_D_flip_flop enable_d_flip_flop_12 (
    .CLK(clk), .D(and_11_out), .ENABLE(or_4_out), .Q(enable_d_flip_flop_12_q));  // open: NOTQ
  and and_16 (and_16_out, decoder_2_out0, enable_d_flip_flop_9_q);
  and and_17 (and_17_out, decoder_2_out1, enable_d_flip_flop_10_q);
  and and_18 (and_18_out, decoder_2_out2, enable_d_flip_flop_11_q);
  and and_19 (and_19_out, decoder_2_out3, enable_d_flip_flop_12_q);
  and and_20 (and_20_out, decoder_1_out0, enable_d_flip_flop_9_q);
  and and_21 (and_21_out, decoder_1_out1, enable_d_flip_flop_10_q);
  and and_22 (and_22_out, decoder_1_out2, enable_d_flip_flop_11_q);
  and and_23 (and_23_out, decoder_1_out3, enable_d_flip_flop_12_q);
  and and_24 (and_24_out, D4, not_1_out);
  and and_25 (and_25_out, enable_d_flip_flop_9_q, decoder_3_out0);
  and and_26 (and_26_out, enable_d_flip_flop_10_q, decoder_3_out1);
  and and_27 (and_27_out, enable_d_flip_flop_11_q, decoder_3_out2);
  and and_28 (and_28_out, enable_d_flip_flop_12_q, decoder_3_out3);
  or or_7 (Q5, and_28_out, and_27_out, and_26_out, and_25_out);
  or or_8 (rdata2_5, and_16_out, and_17_out, and_18_out, and_19_out);
  or or_9 (rdata1_5, and_20_out, and_21_out, and_22_out, and_23_out);
  Enable_D_flip_flop enable_d_flip_flop_13 (
    .CLK(clk), .D(and_24_out), .ENABLE(or_1_out), .Q(enable_d_flip_flop_13_q));  // open: NOTQ
  Enable_D_flip_flop enable_d_flip_flop_14 (
    .CLK(clk), .D(and_24_out), .ENABLE(or_2_out), .Q(enable_d_flip_flop_14_q));  // open: NOTQ
  Enable_D_flip_flop enable_d_flip_flop_15 (
    .CLK(clk), .D(and_24_out), .ENABLE(or_3_out), .Q(enable_d_flip_flop_15_q));  // open: NOTQ
  Enable_D_flip_flop enable_d_flip_flop_16 (
    .CLK(clk), .D(and_24_out), .ENABLE(or_4_out), .Q(enable_d_flip_flop_16_q));  // open: NOTQ
  and and_29 (and_29_out, decoder_2_out0, enable_d_flip_flop_13_q);
  and and_30 (and_30_out, decoder_2_out1, enable_d_flip_flop_14_q);
  and and_31 (and_31_out, decoder_2_out2, enable_d_flip_flop_15_q);
  and and_32 (and_32_out, decoder_2_out3, enable_d_flip_flop_16_q);
  and and_33 (and_33_out, decoder_1_out0, enable_d_flip_flop_13_q);
  and and_34 (and_34_out, decoder_1_out1, enable_d_flip_flop_14_q);
  and and_35 (and_35_out, decoder_1_out2, enable_d_flip_flop_15_q);
  and and_36 (and_36_out, decoder_1_out3, enable_d_flip_flop_16_q);
  and and_37 (and_37_out, enable_d_flip_flop_13_q, decoder_3_out0);
  and and_38 (and_38_out, enable_d_flip_flop_14_q, decoder_3_out1);
  and and_39 (and_39_out, enable_d_flip_flop_15_q, decoder_3_out2);
  and and_40 (and_40_out, enable_d_flip_flop_16_q, decoder_3_out3);
  or or_10 (Q4, and_40_out, and_39_out, and_38_out, and_37_out);
  or or_11 (rdata1_4, and_33_out, and_34_out, and_35_out, and_36_out);
  and and_41 (and_41_out, D3, not_1_out);
  or or_12 (rdata2_4, and_29_out, and_30_out, and_31_out, and_32_out);
  Enable_D_flip_flop enable_d_flip_flop_17 (
    .CLK(clk), .D(and_41_out), .ENABLE(or_1_out), .Q(enable_d_flip_flop_17_q));  // open: NOTQ
  Enable_D_flip_flop enable_d_flip_flop_18 (
    .CLK(clk), .D(and_41_out), .ENABLE(or_2_out), .Q(enable_d_flip_flop_18_q));  // open: NOTQ
  Enable_D_flip_flop enable_d_flip_flop_19 (
    .CLK(clk), .D(and_41_out), .ENABLE(or_3_out), .Q(enable_d_flip_flop_19_q));  // open: NOTQ
  Enable_D_flip_flop enable_d_flip_flop_20 (
    .CLK(clk), .D(and_41_out), .ENABLE(or_4_out), .Q(enable_d_flip_flop_20_q));  // open: NOTQ
  and and_42 (and_42_out, decoder_2_out0, enable_d_flip_flop_17_q);
  and and_43 (and_43_out, decoder_2_out1, enable_d_flip_flop_18_q);
  and and_44 (and_44_out, decoder_2_out2, enable_d_flip_flop_19_q);
  and and_45 (and_45_out, decoder_2_out3, enable_d_flip_flop_20_q);
  and and_46 (and_46_out, decoder_1_out0, enable_d_flip_flop_17_q);
  and and_47 (and_47_out, decoder_1_out1, enable_d_flip_flop_18_q);
  and and_48 (and_48_out, decoder_1_out2, enable_d_flip_flop_19_q);
  and and_49 (and_49_out, decoder_1_out3, enable_d_flip_flop_20_q);
  and and_50 (and_50_out, D2, not_1_out);
  and and_51 (and_51_out, enable_d_flip_flop_17_q, decoder_3_out0);
  and and_52 (and_52_out, enable_d_flip_flop_18_q, decoder_3_out1);
  and and_53 (and_53_out, enable_d_flip_flop_19_q, decoder_3_out2);
  and and_54 (and_54_out, enable_d_flip_flop_20_q, decoder_3_out3);
  or or_13 (rdata2_3, and_42_out, and_43_out, and_44_out, and_45_out);
  or or_14 (Q3, and_54_out, and_53_out, and_52_out, and_51_out);
  or or_15 (rdata1_3, and_46_out, and_47_out, and_48_out, and_49_out);
  Enable_D_flip_flop enable_d_flip_flop_21 (
    .CLK(clk), .D(and_50_out), .ENABLE(or_1_out), .Q(enable_d_flip_flop_21_q));  // open: NOTQ
  Enable_D_flip_flop enable_d_flip_flop_22 (
    .CLK(clk), .D(and_50_out), .ENABLE(or_2_out), .Q(enable_d_flip_flop_22_q));  // open: NOTQ
  Enable_D_flip_flop enable_d_flip_flop_23 (
    .CLK(clk), .D(and_50_out), .ENABLE(or_3_out), .Q(enable_d_flip_flop_23_q));  // open: NOTQ
  Enable_D_flip_flop enable_d_flip_flop_24 (
    .CLK(clk), .D(and_50_out), .ENABLE(or_4_out), .Q(enable_d_flip_flop_24_q));  // open: NOTQ
  and and_55 (and_55_out, decoder_2_out0, enable_d_flip_flop_21_q);
  and and_56 (and_56_out, decoder_2_out1, enable_d_flip_flop_22_q);
  and and_57 (and_57_out, decoder_2_out2, enable_d_flip_flop_23_q);
  and and_58 (and_58_out, decoder_2_out3, enable_d_flip_flop_24_q);
  and and_59 (and_59_out, decoder_1_out0, enable_d_flip_flop_21_q);
  and and_60 (and_60_out, decoder_1_out1, enable_d_flip_flop_22_q);
  and and_61 (and_61_out, decoder_1_out2, enable_d_flip_flop_23_q);
  and and_62 (and_62_out, decoder_1_out3, enable_d_flip_flop_24_q);
  and and_63 (and_63_out, D1, not_1_out);
  and and_64 (and_64_out, enable_d_flip_flop_21_q, decoder_3_out0);
  and and_65 (and_65_out, enable_d_flip_flop_22_q, decoder_3_out1);
  and and_66 (and_66_out, enable_d_flip_flop_23_q, decoder_3_out2);
  and and_67 (and_67_out, enable_d_flip_flop_24_q, decoder_3_out3);
  or or_16 (Q2, and_67_out, and_66_out, and_65_out, and_64_out);
  or or_17 (rdata2_2, and_55_out, and_56_out, and_57_out, and_58_out);
  or or_18 (rdata1_2, and_59_out, and_60_out, and_61_out, and_62_out);
  Enable_D_flip_flop enable_d_flip_flop_25 (
    .CLK(clk), .D(and_63_out), .ENABLE(or_1_out), .Q(enable_d_flip_flop_25_q));  // open: NOTQ
  Enable_D_flip_flop enable_d_flip_flop_26 (
    .CLK(clk), .D(and_63_out), .ENABLE(or_2_out), .Q(enable_d_flip_flop_26_q));  // open: NOTQ
  Enable_D_flip_flop enable_d_flip_flop_27 (
    .CLK(clk), .D(and_63_out), .ENABLE(or_3_out), .Q(enable_d_flip_flop_27_q));  // open: NOTQ
  Enable_D_flip_flop enable_d_flip_flop_28 (
    .CLK(clk), .D(and_63_out), .ENABLE(or_4_out), .Q(enable_d_flip_flop_28_q));  // open: NOTQ
  and and_68 (and_68_out, decoder_2_out0, enable_d_flip_flop_25_q);
  and and_69 (and_69_out, decoder_2_out1, enable_d_flip_flop_26_q);
  and and_70 (and_70_out, decoder_2_out2, enable_d_flip_flop_27_q);
  and and_71 (and_71_out, decoder_2_out3, enable_d_flip_flop_28_q);
  and and_72 (and_72_out, decoder_1_out0, enable_d_flip_flop_25_q);
  and and_73 (and_73_out, decoder_1_out1, enable_d_flip_flop_26_q);
  and and_74 (and_74_out, decoder_1_out2, enable_d_flip_flop_27_q);
  and and_75 (and_75_out, decoder_1_out3, enable_d_flip_flop_28_q);
  and and_76 (and_76_out, D0, not_1_out);
  and and_77 (and_77_out, enable_d_flip_flop_25_q, decoder_3_out0);
  and and_78 (and_78_out, enable_d_flip_flop_26_q, decoder_3_out1);
  and and_79 (and_79_out, enable_d_flip_flop_27_q, decoder_3_out2);
  and and_80 (and_80_out, enable_d_flip_flop_28_q, decoder_3_out3);
  or or_19 (Q1, and_80_out, and_79_out, and_78_out, and_77_out);
  or or_20 (rdata2_1, and_68_out, and_69_out, and_70_out, and_71_out);
  or or_21 (rdata1_1, and_72_out, and_73_out, and_74_out, and_75_out);
  Enable_D_flip_flop enable_d_flip_flop_29 (
    .CLK(clk), .D(and_76_out), .ENABLE(or_1_out), .Q(enable_d_flip_flop_29_q));  // open: NOTQ
  Enable_D_flip_flop enable_d_flip_flop_30 (
    .CLK(clk), .D(and_76_out), .ENABLE(or_2_out), .Q(enable_d_flip_flop_30_q));  // open: NOTQ
  Enable_D_flip_flop enable_d_flip_flop_31 (
    .CLK(clk), .D(and_76_out), .ENABLE(or_3_out), .Q(enable_d_flip_flop_31_q));  // open: NOTQ
  Enable_D_flip_flop enable_d_flip_flop_32 (
    .CLK(clk), .D(and_76_out), .ENABLE(or_4_out), .Q(enable_d_flip_flop_32_q));  // open: NOTQ
  and and_81 (and_81_out, decoder_2_out0, enable_d_flip_flop_29_q);
  and and_82 (and_82_out, decoder_2_out1, enable_d_flip_flop_30_q);
  and and_83 (and_83_out, decoder_2_out2, enable_d_flip_flop_31_q);
  and and_84 (and_84_out, decoder_2_out3, enable_d_flip_flop_32_q);
  and and_85 (and_85_out, decoder_1_out0, enable_d_flip_flop_29_q);
  and and_86 (and_86_out, decoder_1_out1, enable_d_flip_flop_30_q);
  and and_87 (and_87_out, decoder_1_out2, enable_d_flip_flop_31_q);
  and and_88 (and_88_out, decoder_1_out3, enable_d_flip_flop_32_q);
  and and_89 (and_89_out, enable_d_flip_flop_29_q, decoder_3_out0);
  and and_90 (and_90_out, enable_d_flip_flop_30_q, decoder_3_out1);
  and and_91 (and_91_out, enable_d_flip_flop_31_q, decoder_3_out2);
  and and_92 (and_92_out, enable_d_flip_flop_32_q, decoder_3_out3);
  or or_22 (rdata2_0, and_81_out, and_82_out, and_83_out, and_84_out);
  or or_23 (rdata1_0, and_85_out, and_86_out, and_87_out, and_88_out);
  or or_24 (Q0, and_92_out, and_91_out, and_90_out, and_89_out);
endmodule

module li_scpu (
  input  RESET3,
  input  RESET2,
  input  RESET1
);

  wire and_1_out, CLK_out, not_1_out, read_only_memory_1to10_1_q0, read_only_memory_1to10_1_q1,
       read_only_memory_1to10_1_q2, read_only_memory_1to10_1_q3, read_only_memory_1to10_1_q4,
       read_only_memory_1to10_1_q5, read_only_memory_1to10_1_q6, read_only_memory_1to10_1_q7;
  wire [2:0] counter_4bit_1_out_7;
  wire [3:0] random_access_memory_1_q0;

  Read_Only_memory_1to10 read_only_memory_1to10_1 (
    .A2(RESET3), .A1(counter_4bit_1_out_7[2]), .A0(counter_4bit_1_out_7[1]),
    .Q7(read_only_memory_1to10_1_q7), .Q6(read_only_memory_1to10_1_q6), .Q5(read_only_memory_1to10_1_q5),
    .Q4(read_only_memory_1to10_1_q4), .Q3(read_only_memory_1to10_1_q3), .Q2(read_only_memory_1to10_1_q2),
    .Q1(read_only_memory_1to10_1_q1), .Q0(read_only_memory_1to10_1_q0));
  not not_1 (not_1_out, read_only_memory_1to10_1_q6);
  and and_1 (and_1_out, not_1_out, read_only_memory_1to10_1_q7);
  Clock CLK (.out(CLK_out));
  Counter_4bit counter_4bit_1 (
    .in_1(CLK_out), .in_2(RESET1), .in_3(1'b1), .out_5(counter_4bit_1_out_7[2]),
    .out_6(counter_4bit_1_out_7[1]), .out_7(counter_4bit_1_out_7[0]));  // open: out_4
  Random_access_memory random_access_memory_1 (
    .D3(read_only_memory_1to10_1_q3), .D2(read_only_memory_1to10_1_q2), .D1(read_only_memory_1to10_1_q1),
    .D0(read_only_memory_1to10_1_q0), .clk(RESET2), .WEN(and_1_out), .waddr1(read_only_memory_1to10_1_q5),
    .waddr0(read_only_memory_1to10_1_q4), .reset(1'b1), .Q3(random_access_memory_1_q0[3]),
    .Q2(random_access_memory_1_q0[2]), .Q1(random_access_memory_1_q0[1]), .Q0(random_access_memory_1_q0[0]));  // open: raddr2_1, raddr2_0, D7, D6, D4, D5, raddr1_1, raddr1_0, rdata2_2, rdata2_1, rdata2_0, rdata2_3, rdata2_4, rdata2_5, rdata1_3, rdata1_2, rdata1_1, rdata1_0, rdata1_4, rdata1_5, Q7, Q6, Q5, Q4
  // Probe on counter_4bit_1_out_7
  // Probe on random_access_memory_1_q0
endmodule

module add_li_scpu (
  input  RESET1
);

  wire CLK_out, or_1_out, or_2_out, or_3_out, or_4_out, or_5_out, or_6_out, or_7_out;
  wire [1:0] read_only_memory_1to10_1_q6;
  wire [2:0] counter_4bit_1_out_7;
  wire [5:0] adder_1_out, and_1_out, and_2_out, and_3_out, and_4_out, random_access_memory_1_q0,
       random_access_memory_1_rdata1_0, random_access_memory_1_rdata2_0, read_only_memory_1to10_1_q0;
  wire [5:5] decoder_1_out0, decoder_1_out2;

  Clock CLK (.out(CLK_out));
  Read_Only_memory_1to10 read_only_memory_1to10_1 (
    .A2(counter_4bit_1_out_7[2]), .A1(counter_4bit_1_out_7[1]), .A0(counter_4bit_1_out_7[0]),
    .Q7(read_only_memory_1to10_1_q6[1]), .Q6(read_only_memory_1to10_1_q6[0]),
    .Q5(read_only_memory_1to10_1_q0[5]), .Q4(read_only_memory_1to10_1_q0[4]),
    .Q3(read_only_memory_1to10_1_q0[3]), .Q2(read_only_memory_1to10_1_q0[2]),
    .Q1(read_only_memory_1to10_1_q0[1]), .Q0(read_only_memory_1to10_1_q0[0]));
  Decoder #(.select(2)) decoder_1 (
    .out0(decoder_1_out0[5]), .out2(decoder_1_out2[5]), .sel(read_only_memory_1to10_1_q6), .en(1'b1));  // open: out1, out3
  assign and_1_out = read_only_memory_1to10_1_q0 & {6{decoder_1_out0[5]}};  // AND_Gate and_1, 6 bits wide
  assign and_2_out = {6{decoder_1_out2[5]}} & read_only_memory_1to10_1_q0;  // AND_Gate and_2, 6 bits wide
  or or_1 (or_1_out, and_1_out[4], and_2_out[4]);
  or or_2 (or_2_out, and_1_out[5], and_2_out[5]);
  or or_3 (or_3_out, decoder_1_out2[5], decoder_1_out0[5]);
  or or_4 (or_4_out, and_3_out[3], and_4_out[3]);
  or or_5 (or_5_out, and_3_out[2], and_4_out[2]);
  or or_6 (or_6_out, and_3_out[1], and_4_out[1]);
  or or_7 (or_7_out, and_3_out[0], and_4_out[0]);
  Counter_4bit counter_4bit_1 (
    .in_1(CLK_out), .in_2(RESET1), .in_3(1'b1), .out_5(counter_4bit_1_out_7[2]),
    .out_6(counter_4bit_1_out_7[1]), .out_7(counter_4bit_1_out_7[0]));  // open: out_4
  assign and_3_out = {2'b00, and_2_out[3:0]} & {6{decoder_1_out2[5]}};  // AND_Gate and_3, 6 bits wide
  assign and_4_out = {6{decoder_1_out0[5]}} & adder_1_out;  // AND_Gate and_4, 6 bits wide
  // Probe on counter_4bit_1_out_7
  Random_access_memory random_access_memory_1 (
    .raddr2_1(and_1_out[1]), .raddr2_0(and_1_out[0]), .D4(and_4_out[4]), .D3(or_4_out), .D5(and_4_out[5]),
    .D2(or_5_out), .D1(or_6_out), .D0(or_7_out), .raddr1_1(and_1_out[3]), .raddr1_0(and_1_out[2]),
    .clk(CLK_out), .WEN(or_3_out), .waddr1(or_1_out), .waddr0(or_2_out),
    .rdata2_2(random_access_memory_1_rdata2_0[2]), .rdata2_1(random_access_memory_1_rdata2_0[1]),
    .rdata2_0(random_access_memory_1_rdata2_0[0]), .rdata2_3(random_access_memory_1_rdata2_0[3]),
    .rdata2_4(random_access_memory_1_rdata2_0[4]), .rdata2_5(random_access_memory_1_rdata2_0[5]),
    .rdata1_3(random_access_memory_1_rdata1_0[3]), .rdata1_2(random_access_memory_1_rdata1_0[2]),
    .rdata1_1(random_access_memory_1_rdata1_0[1]), .rdata1_0(random_access_memory_1_rdata1_0[0]),
    .rdata1_4(random_access_memory_1_rdata1_0[4]), .rdata1_5(random_access_memory_1_rdata1_0[5]),
    .Q5(random_access_memory_1_q0[5]), .Q4(random_access_memory_1_q0[4]), .Q3(random_access_memory_1_q0[3]),
    .Q2(random_access_memory_1_q0[2]), .Q1(random_access_memory_1_q0[1]), .Q0(random_access_memory_1_q0[0]));  // open: D7, D6, reset, Q7, Q6
  Adder #(.width(6)) adder_1 (
    .a(random_access_memory_1_rdata2_0), .b(random_access_memory_1_rdata1_0), .out(adder_1_out), .cin(1'b0));  // open: cout
  // Probe on random_access_memory_1_q0
  // Probe on adder_1_out
endmodule

module bner0_add_li_scpu (
  input  RESET1,
  input  RESET2
);

  wire and_8_out, CLK_out, comparator_1_eq, not_3_out, not_4_out, not_5_out, not_6_out, not_8_out, or_3_out,
       or_4_out, or_5_out, or_6_out, or_7_out, or_8_out, or_10_out, or_11_out, or_12_out, xor_1_out,
       xor_2_out, xor_3_out, xor_4_out;
  wire [1:0] and_10_out, and_11_out, or_9_out, read_only_memory_1to10_1_q6;
  wire [1:1] decoder_1_out3;
  wire [3:0] adder_1_out, and_1_out, and_2_out, and_3_out, and_4_out, and_14_out, and_15_out, not_1_out,
       not_2_out, not_7_out, or_1_out, or_2_out, or_13_out, register_4bit_1_q3;
  wire [3:3] and_5_out, and_16_out;
  wire [5:0] adder_2_out, and_6_out, and_7_out, and_9_out, and_12_out, and_13_out,
       random_access_memory_1_rdata1_0, random_access_memory_1_rdata2_0, read_only_memory_1to10_1_q0;
  wire [5:5] decoder_1_out0, decoder_1_out2;
  wire [7:0] random_access_memory_1_q0;

  assign not_1_out = ~{4{and_5_out[3]}};  // NOT_Gate not_1, 4 bits wide
  assign not_2_out = ~{4{and_5_out[3]}};  // NOT_Gate not_2, 4 bits wide
  assign and_1_out = register_4bit_1_q3 & not_2_out;  // AND_Gate and_1, 4 bits wide
  assign and_2_out = {4{and_5_out[3]}} & 4'b0000;  // AND_Gate and_2, 4 bits wide
  assign and_3_out = 4'b0001 & not_1_out;  // AND_Gate and_3, 4 bits wide
  assign and_4_out = {4{and_5_out[3]}} & 4'b0000;  // AND_Gate and_4, 4 bits wide
  assign or_1_out = and_3_out | and_4_out;  // OR_Gate or_1, 4 bits wide
  assign or_2_out = and_1_out | and_2_out;  // OR_Gate or_2, 4 bits wide
  Read_Only_memory_1to10 read_only_memory_1to10_1 (
    .A2(register_4bit_1_q3[2]), .A1(register_4bit_1_q3[1]), .A0(register_4bit_1_q3[0]),
    .Q7(read_only_memory_1to10_1_q6[1]), .Q6(read_only_memory_1to10_1_q6[0]),
    .Q5(read_only_memory_1to10_1_q0[5]), .Q4(read_only_memory_1to10_1_q0[4]),
    .Q3(read_only_memory_1to10_1_q0[3]), .Q2(read_only_memory_1to10_1_q0[2]),
    .Q1(read_only_memory_1to10_1_q0[1]), .Q0(read_only_memory_1to10_1_q0[0]));
  and and_5 (and_5_out[3], not_3_out, not_4_out, not_5_out, not_6_out);
  not not_3 (not_3_out, xor_1_out);
  not not_4 (not_4_out, xor_2_out);
  not not_5 (not_5_out, xor_3_out);
  not not_6 (not_6_out, xor_4_out);
  Decoder #(.select(2)) decoder_1 (
    .out0(decoder_1_out0[5]), .out2(decoder_1_out2[5]), .out3(decoder_1_out3[1]),
    .sel(read_only_memory_1to10_1_q6), .en(1'b1));  // open: out1
  Clock CLK (.out(CLK_out));
  xor xor_1 (xor_1_out, register_4bit_1_q3[3], 1'b1);
  xor xor_2 (xor_2_out, register_4bit_1_q3[2], 1'b1);
  xor xor_3 (xor_3_out, register_4bit_1_q3[1], 1'b1);
  xor xor_4 (xor_4_out, register_4bit_1_q3[0], 1'b1);
  assign and_6_out = read_only_memory_1to10_1_q0 & {6{decoder_1_out0[5]}};  // AND_Gate and_6, 6 bits wide
  assign and_7_out = {6{decoder_1_out2[5]}} & read_only_memory_1to10_1_q0;  // AND_Gate and_7, 6 bits wide
  or or_3 (or_3_out, and_6_out[4], and_7_out[4]);
  or or_4 (or_4_out, and_6_out[5], and_7_out[5]);
  Adder #(.width(4)) adder_1 (.a(or_2_out), .b(or_1_out), .out(adder_1_out), .cin(1'b0));  // open: cout
  and and_8 (and_8_out, decoder_1_out3[1], 1'b0);
  or or_5 (or_5_out, decoder_1_out2[5], and_8_out, decoder_1_out0[5]);
  // Probe on register_4bit_1_q3[2:0]
  assign and_9_out = {6{decoder_1_out3[1]}} & read_only_memory_1to10_1_q0;  // AND_Gate and_9, 6 bits wide
  or or_6 (or_6_out, and_9_out[1], and_6_out[1]);
  or or_7 (or_7_out, and_12_out[3], and_13_out[3]);
  or or_8 (or_8_out, and_12_out[2], and_13_out[2]);
  assign and_10_out = {2{decoder_1_out3[1]}} & 2'b00;  // AND_Gate and_10, 2 bits wide
  assign or_9_out = and_10_out | and_11_out;  // OR_Gate or_9, 2 bits wide
  assign and_11_out = and_6_out[3:2] & {2{decoder_1_out0[5]}};  // AND_Gate and_11, 2 bits wide
  or or_10 (or_10_out, and_12_out[1], and_13_out[1]);
  or or_11 (or_11_out, and_12_out[0], and_13_out[0]);
  or or_12 (or_12_out, and_9_out[0], and_6_out[0]);
  assign not_7_out = ~{4{and_16_out[3]}};  // NOT_Gate not_7, 4 bits wide
  assign and_12_out = {2'b00, and_7_out[3:0]} & {6{decoder_1_out2[5]}};  // AND_Gate and_12, 6 bits wide
  assign and_13_out = {6{decoder_1_out0[5]}} & adder_2_out;  // AND_Gate and_13, 6 bits wide
  Register_4bit register_4bit_1 (
    .clk(CLK_out), .RESET(RESET1), .D3(or_13_out[3]), .D2(or_13_out[2]), .D1(or_13_out[1]),
    .D0(or_13_out[0]), .enable(1'b1), .Q3(register_4bit_1_q3[3]), .Q2(register_4bit_1_q3[2]),
    .Q1(register_4bit_1_q3[1]), .Q0(register_4bit_1_q3[0]));
  Random_access_memory random_access_memory_1 (
    .raddr2_1(or_6_out), .raddr2_0(or_12_out), .D4(and_13_out[4]), .D3(or_7_out), .D5(and_13_out[5]),
    .D2(or_8_out), .D1(or_10_out), .D0(or_11_out), .raddr1_1(or_9_out[1]), .raddr1_0(or_9_out[0]),
    .clk(CLK_out), .WEN(or_5_out), .waddr1(or_4_out), .waddr0(or_3_out), .reset(RESET2),
    .rdata2_2(random_access_memory_1_rdata2_0[2]), .rdata2_1(random_access_memory_1_rdata2_0[1]),
    .rdata2_0(random_access_memory_1_rdata2_0[0]), .rdata2_3(random_access_memory_1_rdata2_0[3]),
    .rdata2_4(random_access_memory_1_rdata2_0[4]), .rdata2_5(random_access_memory_1_rdata2_0[5]),
    .rdata1_3(random_access_memory_1_rdata1_0[3]), .rdata1_2(random_access_memory_1_rdata1_0[2]),
    .rdata1_1(random_access_memory_1_rdata1_0[1]), .rdata1_0(random_access_memory_1_rdata1_0[0]),
    .rdata1_4(random_access_memory_1_rdata1_0[4]), .rdata1_5(random_access_memory_1_rdata1_0[5]),
    .Q7(random_access_memory_1_q0[7]), .Q6(random_access_memory_1_q0[6]), .Q5(random_access_memory_1_q0[5]),
    .Q4(random_access_memory_1_q0[4]), .Q3(random_access_memory_1_q0[3]), .Q2(random_access_memory_1_q0[2]),
    .Q1(random_access_memory_1_q0[1]), .Q0(random_access_memory_1_q0[0]));  // open: D7, D6
  assign and_14_out = adder_1_out & not_7_out;  // AND_Gate and_14, 4 bits wide
  assign and_15_out = {4{and_16_out[3]}} & and_9_out[5:2];  // AND_Gate and_15, 4 bits wide
  // Probe on random_access_memory_1_rdata2_0
  assign or_13_out = and_14_out | and_15_out;  // OR_Gate or_13, 4 bits wide
  // Probe on random_access_memory_1_rdata1_0
  Adder #(.width(6)) adder_2 (
    .a(random_access_memory_1_rdata2_0), .b(random_access_memory_1_rdata1_0), .out(adder_2_out), .cin(1'b0));  // open: cout
  // Probe on random_access_memory_1_q0
  Comparator #(.width(6)) comparator_1 (
    .a(random_access_memory_1_rdata2_0), .b(random_access_memory_1_rdata1_0), .eq(comparator_1_eq));  // open: gt, lt
  not not_8 (not_8_out, comparator_1_eq);
  // Probe on adder_2_out
  and and_16 (and_16_out[3], decoder_1_out3[1], not_8_out);
endmodule

module sum_of_odd_from_1_to10 (
  input  RESET1,
  input  RESET2
);

  wire and_8_out, CLK_out, comparator_1_eq, not_3_out, not_4_out, not_5_out, not_6_out, not_8_out, or_3_out,
       or_4_out, or_5_out, or_6_out, or_7_out, or_8_out, or_10_out, or_11_out, or_12_out, xor_1_out,
       xor_2_out, xor_3_out, xor_4_out;
  wire [1:0] and_10_out, and_11_out, or_9_out, read_only_memory_odd_1to10_1_q6;
  wire [1:1] decoder_1_out3;
  wire [3:0] adder_1_out, and_1_out, and_2_out, and_3_out, and_4_out, and_14_out, and_15_out, not_1_out,
       not_2_out, not_7_out, or_1_out, or_2_out, or_13_out, register_4bit_1_q3;
  wire [3:3] and_5_out, and_16_out;
  wire [5:0] adder_2_out, and_6_out, and_7_out, and_9_out, and_12_out, and_13_out,
       random_access_memory_1_rdata1_0, random_access_memory_1_rdata2_0, read_only_memory_odd_1to10_1_q0;
  wire [5:5] decoder_1_out0, decoder_1_out2;
  wire [7:0] random_access_memory_1_q0;

  assign not_1_out = ~{4{and_5_out[3]}};  // NOT_Gate not_1, 4 bits wide
  assign not_2_out = ~{4{and_5_out[3]}};  // NOT_Gate not_2, 4 bits wide
  assign and_1_out = register_4bit_1_q3 & not_2_out;  // AND_Gate and_1, 4 bits wide
  assign and_2_out = {4{and_5_out[3]}} & 4'b0000;  // AND_Gate and_2, 4 bits wide
  assign and_3_out = 4'b0001 & not_1_out;  // AND_Gate and_3, 4 bits wide
  assign and_4_out = {4{and_5_out[3]}} & 4'b0000;  // AND_Gate and_4, 4 bits wide
  assign or_1_out = and_3_out | and_4_out;  // OR_Gate or_1, 4 bits wide
  assign or_2_out = and_1_out | and_2_out;  // OR_Gate or_2, 4 bits wide
  Read_Only_memory_odd_1to10 read_only_memory_odd_1to10_1 (
    .A2(register_4bit_1_q3[2]), .A1(register_4bit_1_q3[1]), .A0(register_4bit_1_q3[0]),
    .Q7(read_only_memory_odd_1to10_1_q6[1]), .Q6(read_only_memory_odd_1to10_1_q6[0]),
    .Q5(read_only_memory_odd_1to10_1_q0[5]), .Q4(read_only_memory_odd_1to10_1_q0[4]),
    .Q3(read_only_memory_odd_1to10_1_q0[3]), .Q2(read_only_memory_odd_1to10_1_q0[2]),
    .Q1(read_only_memory_odd_1to10_1_q0[1]), .Q0(read_only_memory_odd_1to10_1_q0[0]));
  and and_5 (and_5_out[3], not_3_out, not_4_out, not_5_out, not_6_out);
  not not_3 (not_3_out, xor_1_out);
  not not_4 (not_4_out, xor_2_out);
  not not_5 (not_5_out, xor_3_out);
  not not_6 (not_6_out, xor_4_out);
  Decoder #(.select(2)) decoder_1 (
    .out0(decoder_1_out0[5]), .out2(decoder_1_out2[5]), .out3(decoder_1_out3[1]),
    .sel(read_only_memory_odd_1to10_1_q6), .en(1'b1));  // open: out1
  Clock CLK (.out(CLK_out));
  xor xor_1 (xor_1_out, register_4bit_1_q3[3], 1'b1);
  xor xor_2 (xor_2_out, register_4bit_1_q3[2], 1'b1);
  xor xor_3 (xor_3_out, register_4bit_1_q3[1], 1'b1);
  xor xor_4 (xor_4_out, register_4bit_1_q3[0], 1'b1);
  assign and_6_out = read_only_memory_odd_1to10_1_q0 & {6{decoder_1_out0[5]}};  // AND_Gate and_6, 6 bits wide
  assign and_7_out = {6{decoder_1_out2[5]}} & read_only_memory_odd_1to10_1_q0;  // AND_Gate and_7, 6 bits wide
  or or_3 (or_3_out, and_6_out[4], and_7_out[4]);
  or or_4 (or_4_out, and_6_out[5], and_7_out[5]);
  Adder #(.width(4)) adder_1 (.a(or_2_out), .b(or_1_out), .out(adder_1_out), .cin(1'b0));  // open: cout
  and and_8 (and_8_out, decoder_1_out3[1], 1'b0);
  or or_5 (or_5_out, decoder_1_out2[5], and_8_out, decoder_1_out0[5]);
  // Probe on register_4bit_1_q3[2:0]
  assign and_9_out = {6{decoder_1_out3[1]}} & read_only_memory_odd_1to10_1_q0;  // AND_Gate and_9, 6 bits wide
  or or_6 (or_6_out, and_9_out[1], and_6_out[1]);
  or or_7 (or_7_out, and_12_out[3], and_13_out[3]);
  or or_8 (or_8_out, and_12_out[2], and_13_out[2]);
  assign and_10_out = {2{decoder_1_out3[1]}} & 2'b00;  // AND_Gate and_10, 2 bits wide
  assign or_9_out = and_10_out | and_11_out;  // OR_Gate or_9, 2 bits wide
  assign and_11_out = and_6_out[3:2] & {2{decoder_1_out0[5]}};  // AND_Gate and_11, 2 bits wide
  or or_10 (or_10_out, and_12_out[1], and_13_out[1]);
  or or_11 (or_11_out, and_12_out[0], and_13_out[0]);
  or or_12 (or_12_out, and_9_out[0], and_6_out[0]);
  assign not_7_out = ~{4{and_16_out[3]}};  // NOT_Gate not_7, 4 bits wide
  assign and_12_out = {2'b00, and_7_out[3:0]} & {6{decoder_1_out2[5]}};  // AND_Gate and_12, 6 bits wide
  assign and_13_out = {6{decoder_1_out0[5]}} & adder_2_out;  // AND_Gate and_13, 6 bits wide
  Register_4bit register_4bit_1 (
    .clk(CLK_out), .RESET(RESET1), .D3(or_13_out[3]), .D2(or_13_out[2]), .D1(or_13_out[1]),
    .D0(or_13_out[0]), .enable(1'b1), .Q3(register_4bit_1_q3[3]), .Q2(register_4bit_1_q3[2]),
    .Q1(register_4bit_1_q3[1]), .Q0(register_4bit_1_q3[0]));
  Random_access_memory random_access_memory_1 (
    .raddr2_1(or_6_out), .raddr2_0(or_12_out), .D4(and_13_out[4]), .D3(or_7_out), .D5(and_13_out[5]),
    .D2(or_8_out), .D1(or_10_out), .D0(or_11_out), .raddr1_1(or_9_out[1]), .raddr1_0(or_9_out[0]),
    .clk(CLK_out), .WEN(or_5_out), .waddr1(or_4_out), .waddr0(or_3_out), .reset(RESET2),
    .rdata2_2(random_access_memory_1_rdata2_0[2]), .rdata2_1(random_access_memory_1_rdata2_0[1]),
    .rdata2_0(random_access_memory_1_rdata2_0[0]), .rdata2_3(random_access_memory_1_rdata2_0[3]),
    .rdata2_4(random_access_memory_1_rdata2_0[4]), .rdata2_5(random_access_memory_1_rdata2_0[5]),
    .rdata1_3(random_access_memory_1_rdata1_0[3]), .rdata1_2(random_access_memory_1_rdata1_0[2]),
    .rdata1_1(random_access_memory_1_rdata1_0[1]), .rdata1_0(random_access_memory_1_rdata1_0[0]),
    .rdata1_4(random_access_memory_1_rdata1_0[4]), .rdata1_5(random_access_memory_1_rdata1_0[5]),
    .Q7(random_access_memory_1_q0[7]), .Q6(random_access_memory_1_q0[6]), .Q5(random_access_memory_1_q0[5]),
    .Q4(random_access_memory_1_q0[4]), .Q3(random_access_memory_1_q0[3]), .Q2(random_access_memory_1_q0[2]),
    .Q1(random_access_memory_1_q0[1]), .Q0(random_access_memory_1_q0[0]));  // open: D7, D6
  assign and_14_out = adder_1_out & not_7_out;  // AND_Gate and_14, 4 bits wide
  assign and_15_out = {4{and_16_out[3]}} & and_9_out[5:2];  // AND_Gate and_15, 4 bits wide
  // Probe on random_access_memory_1_rdata2_0
  assign or_13_out = and_14_out | and_15_out;  // OR_Gate or_13, 4 bits wide
  // Probe on random_access_memory_1_rdata1_0
  Adder #(.width(6)) adder_2 (
    .a(random_access_memory_1_rdata2_0), .b(random_access_memory_1_rdata1_0), .out(adder_2_out), .cin(1'b0));  // open: cout
  // Probe on random_access_memory_1_q0
  Comparator #(.width(6)) comparator_1 (
    .a(random_access_memory_1_rdata2_0), .b(random_access_memory_1_rdata1_0), .eq(comparator_1_eq));  // open: gt, lt
  not not_8 (not_8_out, comparator_1_eq);
  // Probe on adder_2_out
  and and_16 (and_16_out[3], decoder_1_out3[1], not_8_out);
endmodule

module Read_Only_memory_odd_1to10 (
  input  A2,
  input  A1,
  input  A0,
  output Q7,
  output Q6,
  output Q5,
  output Q4,
  output Q3,
  output Q2,
  output Q1,
  output Q0
);

  wire and_1_out, and_2_out, and_3_out, and_4_out, and_5_out, and_6_out, and_7_out, and_8_out, and_9_out,
       and_10_out, and_11_out, and_12_out, and_13_out, and_14_out, and_15_out, and_16_out, and_17_out,
       and_18_out, and_19_out, and_20_out, and_21_out, and_22_out, and_23_out, and_24_out, and_25_out,
       and_26_out, and_27_out, and_28_out, and_29_out, and_30_out, and_31_out, and_32_out, and_33_out,
       and_34_out, and_35_out, and_36_out, and_37_out, and_38_out, and_39_out, and_40_out, and_41_out,
       and_42_out, and_43_out, and_44_out, and_45_out, and_46_out, and_47_out, and_48_out, and_49_out,
       and_50_out, and_51_out, and_52_out, and_53_out, and_54_out, and_55_out, and_56_out, and_57_out,
       and_58_out, and_59_out, and_60_out, and_61_out, and_62_out, and_63_out, and_64_out, decoder_1_out0,
       decoder_1_out1, decoder_1_out2, decoder_1_out3, decoder_1_out4, decoder_1_out5, decoder_1_out6,
       decoder_1_out7;

  Decoder #(.select(3)) decoder_1 (
    .out0(decoder_1_out0), .out1(decoder_1_out1), .out2(decoder_1_out2), .out3(decoder_1_out3),
    .out4(decoder_1_out4), .out5(decoder_1_out5), .out6(decoder_1_out6), .out7(decoder_1_out7),
    .sel({A2, A1, A0}), .en(1'b1));
  or or_1 (Q7, and_1_out, and_2_out, and_3_out, and_4_out, and_5_out, and_6_out, and_7_out, and_8_out);
  and and_1 (and_1_out, decoder_1_out0, 1'b1);
  and and_2 (and_2_out, decoder_1_out1, 1'b1);
  and and_3 (and_3_out, decoder_1_out2, 1'b1);
  and and_4 (and_4_out, decoder_1_out3, 1'b1);
  and and_5 (and_5_out, decoder_1_out4, 1'b0);
  and and_6 (and_6_out, decoder_1_out5, 1'b0);
  and and_7 (and_7_out, decoder_1_out6, 1'b1);
  and and_8 (and_8_out, decoder_1_out7, 1'b1);
  and and_9 (and_9_out, decoder_1_out0, 1'b0);
  and and_10 (and_10_out, decoder_1_out1, 1'b0);
  and and_11 (and_11_out, decoder_1_out2, 1'b0);
  and and_12 (and_12_out, decoder_1_out3, 1'b0);
  and and_13 (and_13_out, decoder_1_out4, 1'b0);
  and and_14 (and_14_out, decoder_1_out5, 1'b0);
  and and_15 (and_15_out, decoder_1_out6, 1'b1);
  and and_16 (and_16_out, decoder_1_out7, 1'b1);
  or or_2 (Q6, and_9_out, and_10_out, and_11_out, and_12_out, and_13_out, and_14_out, and_15_out, and_16_out);
  and and_17 (and_17_out, decoder_1_out0, 1'b0);
  and and_18 (and_18_out, decoder_1_out1, 1'b0);
  and and_19 (and_19_out, decoder_1_out2, 1'b1);
  and and_20 (and_20_out, decoder_1_out3, 1'b1);
  and and_21 (and_21_out, decoder_1_out4, 1'b1);
  and and_22 (and_22_out, decoder_1_out5, 1'b0);
  and and_23 (and_23_out, decoder_1_out6, 1'b0);
  and and_24 (and_24_out, decoder_1_out7, 1'b0);
  or or_3 (Q5, and_17_out, and_18_out, and_19_out, and_20_out, and_21_out, and_22_out, and_23_out, and_24_out);
  and and_25 (and_25_out, decoder_1_out0, 1'b0);
  and and_26 (and_26_out, decoder_1_out1, 1'b1);
  and and_27 (and_27_out, decoder_1_out2, 1'b0);
  and and_28 (and_28_out, decoder_1_out3, 1'b1);
  and and_29 (and_29_out, decoder_1_out4, 1'b0);
  and and_30 (and_30_out, decoder_1_out5, 1'b1);
  and and_31 (and_31_out, decoder_1_out6, 1'b1);
  and and_32 (and_32_out, decoder_1_out7, 1'b1);
  and and_33 (and_33_out, decoder_1_out0, 1'b1);
  and and_34 (and_34_out, decoder_1_out1, 1'b0);
  and and_35 (and_35_out, decoder_1_out2, 1'b0);
  and and_36 (and_36_out, decoder_1_out3, 1'b0);
  and and_37 (and_37_out, decoder_1_out4, 1'b1);
  and and_38 (and_38_out, decoder_1_out5, 1'b0);
  and and_39 (and_39_out, decoder_1_out6, 1'b0);
  and and_40 (and_40_out, decoder_1_out7, 1'b1);
  or or_4 (Q4, and_25_out, and_26_out, and_27_out, and_28_out, and_29_out, and_30_out, and_31_out, and_32_out);
  and and_41 (and_41_out, decoder_1_out0, 1'b0);
  and and_42 (and_42_out, decoder_1_out1, 1'b0);
  and and_43 (and_43_out, decoder_1_out2, 1'b0);
  and and_44 (and_44_out, decoder_1_out3, 1'b0);
  and and_45 (and_45_out, decoder_1_out4, 1'b0);
  and and_46 (and_46_out, decoder_1_out5, 1'b1);
  and and_47 (and_47_out, decoder_1_out6, 1'b0);
  and and_48 (and_48_out, decoder_1_out7, 1'b1);
  or or_5 (Q3, and_33_out, and_34_out, and_35_out, and_36_out, and_37_out, and_38_out, and_39_out, and_40_out);
  and and_49 (and_49_out, decoder_1_out0, 1'b1);
  and and_50 (and_50_out, decoder_1_out1, 1'b0);
  and and_51 (and_51_out, decoder_1_out2, 1'b0);
  and and_52 (and_52_out, decoder_1_out3, 1'b1);
  and and_53 (and_53_out, decoder_1_out4, 1'b0);
  and and_54 (and_54_out, decoder_1_out5, 1'b1);
  and and_55 (and_55_out, decoder_1_out6, 1'b0);
  and and_56 (and_56_out, decoder_1_out7, 1'b1);
  and and_57 (and_57_out, decoder_1_out0, 1'b1);
  and and_58 (and_58_out, decoder_1_out1, 1'b1);
  and and_59 (and_59_out, decoder_1_out2, 1'b0);
  and and_60 (and_60_out, decoder_1_out3, 1'b0);
  and and_61 (and_61_out, decoder_1_out4, 1'b1);
  and and_62 (and_62_out, decoder_1_out5, 1'b1);
  and and_63 (and_63_out, decoder_1_out6, 1'b1);
  and and_64 (and_64_out, decoder_1_out7, 1'b1);
  or or_6 (Q2, and_41_out, and_42_out, and_43_out, and_44_out, and_45_out, and_46_out, and_47_out, and_48_out);
  or or_7 (Q1, and_49_out, and_50_out, and_51_out, and_52_out, and_53_out, and_54_out, and_55_out, and_56_out);
  or or_8 (Q0, and_57_out, and_58_out, and_59_out, and_60_out, and_61_out, and_62_out, and_63_out, and_64_out);
endmodule

module Enhanced_instruction (
  input  reset2,
  input  RESET1
);

  wire and_10_out, CLK_out, comparator_1_eq, not_3_out, not_4_out, not_5_out, not_6_out, not_9_out, or_3_out,
       or_5_out, or_6_out, or_7_out, or_9_out, or_10_out, or_11_out, or_12_out, or_13_out, or_14_out,
       or_15_out, xor_1_out, xor_2_out, xor_3_out, xor_4_out;
  wire [1:0] and_11_out, and_12_out, enhance_rom_1_q6, not_7_out, or_4_out;
  wire [3:0] adder_1_out, adder_3_out, and_1_out, and_2_out, and_3_out, and_4_out, and_13_out, and_14_out,
       not_1_out, not_2_out, not_8_out, or_1_out, or_2_out, or_8_out, register_4bit_1_q0;
  wire [3:3] and_5_out, and_16_out;
  wire [5:0] adder_2_out, and_6_out, and_7_out, and_8_out, and_9_out, and_15_out, enhance_rom_1_q0,
       random_access_memory_1_rdata1_0, random_access_memory_1_rdata2_0;
  wire [5:5] decoder_1_out0, decoder_1_out1, decoder_1_out2, decoder_1_out3;
  wire [7:0] multiplexer_1_out, random_access_memory_1_q0;

  assign not_1_out = ~{4{and_5_out[3]}};  // NOT_Gate not_1, 4 bits wide
  assign not_2_out = ~{4{and_5_out[3]}};  // NOT_Gate not_2, 4 bits wide
  assign and_1_out = register_4bit_1_q0 & not_2_out;  // AND_Gate and_1, 4 bits wide
  assign and_2_out = {4{and_5_out[3]}} & 4'b0000;  // AND_Gate and_2, 4 bits wide
  assign and_3_out = 4'b0001 & not_1_out;  // AND_Gate and_3, 4 bits wide
  assign and_4_out = {4{and_5_out[3]}} & 4'b0000;  // AND_Gate and_4, 4 bits wide
  assign or_1_out = and_3_out | and_4_out;  // OR_Gate or_1, 4 bits wide
  assign or_2_out = and_1_out | and_2_out;  // OR_Gate or_2, 4 bits wide
  Decoder #(.select(2)) decoder_1 (
    .out0(decoder_1_out0[5]), .out1(decoder_1_out1[5]), .out2(decoder_1_out2[5]), .out3(decoder_1_out3[5]),
    .sel(enhance_rom_1_q6), .en(1'b1));
  Enhance_ROM enhance_rom_1 (
    .A2(register_4bit_1_q0[2]), .A1(register_4bit_1_q0[1]), .A0(register_4bit_1_q0[0]),
    .Q7(enhance_rom_1_q6[1]), .Q6(enhance_rom_1_q6[0]), .Q5(enhance_rom_1_q0[5]), .Q4(enhance_rom_1_q0[4]),
    .Q3(enhance_rom_1_q0[3]), .Q2(enhance_rom_1_q0[2]), .Q1(enhance_rom_1_q0[1]), .Q0(enhance_rom_1_q0[0]));
  and and_5 (and_5_out[3], not_3_out, not_4_out, not_5_out, not_6_out);
  Clock CLK (.out(CLK_out));
  not not_3 (not_3_out, xor_1_out);
  not not_4 (not_4_out, xor_2_out);
  not not_5 (not_5_out, xor_3_out);
  not not_6 (not_6_out, xor_4_out);
  assign and_6_out = {6{decoder_1_out0[5]}} & enhance_rom_1_q0;  // AND_Gate and_6, 6 bits wide
  assign and_7_out = {6{decoder_1_out1[5]}} & enhance_rom_1_q0;  // AND_Gate and_7, 6 bits wide
  assign and_8_out = enhance_rom_1_q0 & {6{decoder_1_out2[5]}};  // AND_Gate and_8, 6 bits wide
  assign and_9_out = enhance_rom_1_q0 & {6{decoder_1_out3[5]}};  // AND_Gate and_9, 6 bits wide
  xor xor_1 (xor_1_out, register_4bit_1_q0[3], 1'b1);
  xor xor_2 (xor_2_out, register_4bit_1_q0[2], 1'b1);
  xor xor_3 (xor_3_out, register_4bit_1_q0[1], 1'b1);
  xor xor_4 (xor_4_out, register_4bit_1_q0[0], 1'b1);
  Adder #(.width(4)) adder_1 (.a(or_2_out), .b(or_1_out), .out(adder_1_out), .cin(1'b0));  // open: cout
  and and_10 (and_10_out, 1'b0, decoder_1_out3[5]);
  or or_3 (or_3_out, decoder_1_out0[5], decoder_1_out2[5], and_10_out);
  // Probe on register_4bit_1_q0[2:0]
  Multiplexer #(.select(2), .width(8)) multiplexer_1 (
    .in0({{6{1'b0}}, and_8_out[1:0]}), .in1({4'b0000, and_8_out[1:0], 2'b00}),
    .in2({2'b00, and_8_out[1:0], 4'b0000}), .in3({and_8_out[1:0], {6{1'b0}}}), .out(multiplexer_1_out),
    .sel(and_8_out[3:2]));
  assign not_7_out = ~{2{decoder_1_out3[5]}};  // NOT_Gate not_7, 2 bits wide
  assign and_11_out = {2{decoder_1_out3[5]}} & 2'b00;  // AND_Gate and_11, 2 bits wide
  assign and_12_out = not_7_out & and_6_out[3:2];  // AND_Gate and_12, 2 bits wide
  assign not_8_out = ~{4{and_16_out[3]}};  // NOT_Gate not_8, 4 bits wide
  assign or_4_out = and_11_out | and_12_out;  // OR_Gate or_4, 2 bits wide
  Register_4bit register_4bit_1 (
    .clk(CLK_out), .RESET(RESET1), .D3(or_8_out[3]), .D2(or_8_out[2]), .D1(or_8_out[1]), .D0(or_8_out[0]),
    .enable(1'b1), .Q3(register_4bit_1_q0[3]), .Q2(register_4bit_1_q0[2]), .Q1(register_4bit_1_q0[1]),
    .Q0(register_4bit_1_q0[0]));
  or or_5 (or_5_out, and_15_out[0], multiplexer_1_out[0]);
  assign and_13_out = adder_1_out & not_8_out;  // AND_Gate and_13, 4 bits wide
  assign and_14_out = {4{and_16_out[3]}} & adder_3_out;  // AND_Gate and_14, 4 bits wide
  or or_6 (or_6_out, multiplexer_1_out[1], and_15_out[1]);
  or or_7 (or_7_out, multiplexer_1_out[2], and_15_out[2]);
  assign or_8_out = and_13_out | and_14_out;  // OR_Gate or_8, 4 bits wide
  or or_9 (or_9_out, multiplexer_1_out[3], and_15_out[3]);
  or or_10 (or_10_out, multiplexer_1_out[4], and_15_out[4]);
  or or_11 (or_11_out, multiplexer_1_out[5], and_15_out[5]);
  or or_12 (or_12_out, and_6_out[0], and_9_out[0]);
  or or_13 (or_13_out, and_6_out[1], and_9_out[1]);
  or or_14 (or_14_out, and_6_out[4], and_8_out[4]);
  or or_15 (or_15_out, and_8_out[5], and_6_out[5]);
  Random_access_memory random_access_memory_1 (
    .raddr2_1(or_13_out), .raddr2_0(or_12_out), .D7(multiplexer_1_out[7]), .D6(multiplexer_1_out[6]),
    .D4(or_10_out), .D3(or_9_out), .D5(or_11_out), .D2(or_7_out), .D1(or_6_out), .D0(or_5_out),
    .raddr1_1(or_4_out[1]), .raddr1_0(or_4_out[0]), .clk(CLK_out), .WEN(or_3_out), .waddr1(or_15_out),
    .waddr0(or_14_out), .reset(reset2), .rdata2_2(random_access_memory_1_rdata2_0[2]),
    .rdata2_1(random_access_memory_1_rdata2_0[1]), .rdata2_0(random_access_memory_1_rdata2_0[0]),
    .rdata2_3(random_access_memory_1_rdata2_0[3]), .rdata2_4(random_access_memory_1_rdata2_0[4]),
    .rdata2_5(random_access_memory_1_rdata2_0[5]), .rdata1_3(random_access_memory_1_rdata1_0[3]),
    .rdata1_2(random_access_memory_1_rdata1_0[2]), .rdata1_1(random_access_memory_1_rdata1_0[1]),
    .rdata1_0(random_access_memory_1_rdata1_0[0]), .rdata1_4(random_access_memory_1_rdata1_0[4]),
    .rdata1_5(random_access_memory_1_rdata1_0[5]), .Q7(random_access_memory_1_q0[7]),
    .Q6(random_access_memory_1_q0[6]), .Q5(random_access_memory_1_q0[5]), .Q4(random_access_memory_1_q0[4]),
    .Q3(random_access_memory_1_q0[3]), .Q2(random_access_memory_1_q0[2]), .Q1(random_access_memory_1_q0[1]),
    .Q0(random_access_memory_1_q0[0]));
  assign and_15_out = adder_2_out & {6{decoder_1_out0[5]}};  // AND_Gate and_15, 6 bits wide
  // Probe on random_access_memory_1_rdata2_0
  Adder #(.width(6)) adder_2 (
    .a(random_access_memory_1_rdata2_0), .b(random_access_memory_1_rdata1_0), .out(adder_2_out), .cin(1'b0));  // open: cout
  // Probe on random_access_memory_1_rdata1_0
  not not_9 (not_9_out, comparator_1_eq);
  Comparator #(.width(6)) comparator_1 (
    .a(random_access_memory_1_rdata1_0), .b(random_access_memory_1_rdata2_0), .eq(comparator_1_eq));  // open: gt, lt
  // Probe on random_access_memory_1_q0
  Adder #(.width(4)) adder_3 (.a(and_9_out[5:2]), .b(register_4bit_1_q0), .out(adder_3_out), .cin(1'b0));  // open: cout
  and and_16 (and_16_out[3], decoder_1_out3[5], not_9_out);
endmodule

module Enhance_ROM (
  input  A2,
  input  A1,
  input  A0,
  output Q7,
  output Q6,
  output Q5,
  output Q4,
  output Q3,
  output Q2,
  output Q1,
  output Q0
);

  wire and_1_out, and_2_out, and_3_out, and_4_out, and_5_out, and_6_out, and_7_out, and_8_out, and_9_out,
       and_10_out, and_11_out, and_12_out, and_13_out, and_14_out, and_15_out, and_16_out, and_17_out,
       and_18_out, and_19_out, and_20_out, and_21_out, and_22_out, and_23_out, and_24_out, and_25_out,
       and_26_out, and_27_out, and_28_out, and_29_out, and_30_out, and_31_out, and_32_out, and_33_out,
       and_34_out, and_35_out, and_36_out, and_37_out, and_38_out, and_39_out, and_40_out, and_41_out,
       and_42_out, and_43_out, and_44_out, and_45_out, and_46_out, and_47_out, and_48_out, and_49_out,
       and_50_out, and_51_out, and_52_out, and_53_out, and_54_out, and_55_out, and_56_out, and_57_out,
       and_58_out, and_59_out, and_60_out, and_61_out, and_62_out, and_63_out, and_64_out, decoder_1_out0,
       decoder_1_out1, decoder_1_out2, decoder_1_out3, decoder_1_out4, decoder_1_out5, decoder_1_out6,
       decoder_1_out7;

  Decoder #(.select(3)) decoder_1 (
    .out0(decoder_1_out0), .out1(decoder_1_out1), .out2(decoder_1_out2), .out3(decoder_1_out3),
    .out4(decoder_1_out4), .out5(decoder_1_out5), .out6(decoder_1_out6), .out7(decoder_1_out7),
    .sel({A2, A1, A0}), .en(1'b1));
  or or_1 (Q7, and_1_out, and_2_out, and_3_out, and_4_out, and_5_out, and_6_out, and_7_out, and_8_out);
  and and_1 (and_1_out, decoder_1_out0, 1'b1);
  and and_2 (and_2_out, decoder_1_out1, 1'b1);
  and and_3 (and_3_out, decoder_1_out2, 1'b0);
  and and_4 (and_4_out, decoder_1_out3, 1'b1);
  and and_5 (and_5_out, decoder_1_out4, 1'b0);
  and and_6 (and_6_out, decoder_1_out5, 1'b0);
  and and_7 (and_7_out, decoder_1_out6, 1'b1);
  and and_8 (and_8_out, decoder_1_out7, 1'b1);
  and and_9 (and_9_out, decoder_1_out0, 1'b0);
  and and_10 (and_10_out, decoder_1_out1, 1'b0);
  and and_11 (and_11_out, decoder_1_out2, 1'b0);
  and and_12 (and_12_out, decoder_1_out3, 1'b0);
  and and_13 (and_13_out, decoder_1_out4, 1'b0);
  and and_14 (and_14_out, decoder_1_out5, 1'b0);
  and and_15 (and_15_out, decoder_1_out6, 1'b1);
  and and_16 (and_16_out, decoder_1_out7, 1'b1);
  or or_2 (Q6, and_9_out, and_10_out, and_11_out, and_12_out, and_13_out, and_14_out, and_15_out, and_16_out);
  and and_17 (and_17_out, decoder_1_out0, 1'b0);
  and and_18 (and_18_out, decoder_1_out1, 1'b1);
  and and_19 (and_19_out, decoder_1_out2, 1'b0);
  and and_20 (and_20_out, decoder_1_out3, 1'b1);
  and and_21 (and_21_out, decoder_1_out4, 1'b1);
  and and_22 (and_22_out, decoder_1_out5, 1'b0);
  and and_23 (and_23_out, decoder_1_out6, 1'b1);
  and and_24 (and_24_out, decoder_1_out7, 1'b0);
  or or_3 (Q5, and_17_out, and_18_out, and_19_out, and_20_out, and_21_out, and_22_out, and_23_out, and_24_out);
  and and_25 (and_25_out, decoder_1_out0, 1'b0);
  and and_26 (and_26_out, decoder_1_out1, 1'b1);
  and and_27 (and_27_out, decoder_1_out2, 1'b0);
  and and_28 (and_28_out, decoder_1_out3, 1'b1);
  and and_29 (and_29_out, decoder_1_out4, 1'b0);
  and and_30 (and_30_out, decoder_1_out5, 1'b1);
  and and_31 (and_31_out, decoder_1_out6, 1'b1);
  and and_32 (and_32_out, decoder_1_out7, 1'b0);
  and and_33 (and_33_out, decoder_1_out0, 1'b0);
  and and_34 (and_34_out, decoder_1_out1, 1'b0);
  and and_35 (and_35_out, decoder_1_out2, 1'b0);
  and and_36 (and_36_out, decoder_1_out3, 1'b0);
  and and_37 (and_37_out, decoder_1_out4, 1'b1);
  and and_38 (and_38_out, decoder_1_out5, 1'b0);
  and and_39 (and_39_out, decoder_1_out6, 1'b1);
  and and_40 (and_40_out, decoder_1_out7, 1'b0);
  or or_4 (Q4, and_25_out, and_26_out, and_27_out, and_28_out, and_29_out, and_30_out, and_31_out, and_32_out);
  and and_41 (and_41_out, decoder_1_out0, 1'b1);
  and and_42 (and_42_out, decoder_1_out1, 1'b0);
  and and_43 (and_43_out, decoder_1_out2, 1'b0);
  and and_44 (and_44_out, decoder_1_out3, 1'b0);
  and and_45 (and_45_out, decoder_1_out4, 1'b0);
  and and_46 (and_46_out, decoder_1_out5, 1'b1);
  and and_47 (and_47_out, decoder_1_out6, 1'b0);
  and and_48 (and_48_out, decoder_1_out7, 1'b0);
  or or_5 (Q3, and_33_out, and_34_out, and_35_out, and_36_out, and_37_out, and_38_out, and_39_out, and_40_out);
  and and_49 (and_49_out, decoder_1_out0, 1'b1);
  and and_50 (and_50_out, decoder_1_out1, 1'b1);
  and and_51 (and_51_out, decoder_1_out2, 1'b1);
  and and_52 (and_52_out, decoder_1_out3, 1'b0);
  and and_53 (and_53_out, decoder_1_out4, 1'b0);
  and and_54 (and_54_out, decoder_1_out5, 1'b1);
  and and_55 (and_55_out, decoder_1_out6, 1'b0);
  and and_56 (and_56_out, decoder_1_out7, 1'b1);
  and and_57 (and_57_out, decoder_1_out0, 1'b0);
  and and_58 (and_58_out, decoder_1_out1, 1'b1);
  and and_59 (and_59_out, decoder_1_out2, 1'b1);
  and and_60 (and_60_out, decoder_1_out3, 1'b1);
  and and_61 (and_61_out, decoder_1_out4, 1'b1);
  and and_62 (and_62_out, decoder_1_out5, 1'b1);
  and and_63 (and_63_out, decoder_1_out6, 1'b1);
  and and_64 (and_64_out, decoder_1_out7, 1'b1);
  or or_6 (Q2, and_41_out, and_42_out, and_43_out, and_44_out, and_45_out, and_46_out, and_47_out, and_48_out);
  or or_7 (Q1, and_49_out, and_50_out, and_51_out, and_52_out, and_53_out, and_54_out, and_55_out, and_56_out);
  or or_8 (Q0, and_57_out, and_58_out, and_59_out, and_60_out, and_61_out, and_62_out, and_63_out, and_64_out);
endmodule

module io_scpu_led (
  input  reset2,
  input  RESET1
);

  wire and_10_out, and_18_out, CLK_out, comparator_1_eq, decoder_2_out0, not_3_out, not_4_out, not_5_out,
       not_6_out, not_9_out, or_3_out, or_5_out, or_6_out, or_7_out, or_9_out, or_10_out, or_11_out,
       or_12_out, or_13_out, or_14_out, or_15_out, xor_1_out, xor_2_out, xor_3_out, xor_4_out;
  wire [1:0] and_11_out, and_12_out, and_13_out, not_7_out, or_4_out, rom_general_1_q6;
  wire [3:0] adder_1_out, adder_3_out, and_1_out, and_2_out, and_3_out, and_4_out, and_14_out, and_15_out,
       not_1_out, not_2_out, not_8_out, or_1_out, or_2_out, or_8_out, register_4bit_1_q0;
  wire [3:3] and_5_out, and_17_out;
  wire [5:0] adder_2_out, and_6_out, and_7_out, and_8_out, and_9_out, and_16_out,
       random_access_memory_1_rdata1_0, random_access_memory_1_rdata2_0, rom_general_1_q0;
  wire [5:5] decoder_1_out0, decoder_1_out1, decoder_1_out2, decoder_1_out3;
  wire [7:0] multiplexer_1_out, random_access_memory_1_q0, register_8bit_1_q0;

  assign not_1_out = ~{4{and_5_out[3]}};  // NOT_Gate not_1, 4 bits wide
  assign not_2_out = ~{4{and_5_out[3]}};  // NOT_Gate not_2, 4 bits wide
  assign and_1_out = register_4bit_1_q0 & not_2_out;  // AND_Gate and_1, 4 bits wide
  assign and_2_out = {4{and_5_out[3]}} & 4'b0000;  // AND_Gate and_2, 4 bits wide
  assign and_3_out = 4'b0001 & not_1_out;  // AND_Gate and_3, 4 bits wide
  assign and_4_out = {4{and_5_out[3]}} & 4'b0000;  // AND_Gate and_4, 4 bits wide
  assign or_1_out = and_3_out | and_4_out;  // OR_Gate or_1, 4 bits wide
  assign or_2_out = and_1_out | and_2_out;  // OR_Gate or_2, 4 bits wide
  Decoder #(.select(2)) decoder_1 (
    .out0(decoder_1_out0[5]), .out1(decoder_1_out1[5]), .out2(decoder_1_out2[5]), .out3(decoder_1_out3[5]),
    .sel(rom_general_1_q6), .en(1'b1));
  ROM_general rom_general_1 (
    .A2(register_4bit_1_q0[2]), .A1(register_4bit_1_q0[1]), .A0(register_4bit_1_q0[0]), .MC0(8'h86),
    .MC1(8'hb3), .MC2(8'h3), .MC3(8'hb1), .MC4(8'h29), .MC5(8'h17), .MC6(8'hf9), .MC7(8'h68),
    .Q7(rom_general_1_q6[1]), .Q6(rom_general_1_q6[0]), .Q5(rom_general_1_q0[5]), .Q4(rom_general_1_q0[4]),
    .Q3(rom_general_1_q0[3]), .Q2(rom_general_1_q0[2]), .Q1(rom_general_1_q0[1]), .Q0(rom_general_1_q0[0]));
  and and_5 (and_5_out[3], not_3_out, not_4_out, not_5_out, not_6_out);
  Clock CLK (.out(CLK_out));
  not not_3 (not_3_out, xor_1_out);
  not not_4 (not_4_out, xor_2_out);
  not not_5 (not_5_out, xor_3_out);
  not not_6 (not_6_out, xor_4_out);
  assign and_6_out = {6{decoder_1_out0[5]}} & rom_general_1_q0;  // AND_Gate and_6, 6 bits wide
  assign and_7_out = {6{decoder_1_out1[5]}} & rom_general_1_q0;  // AND_Gate and_7, 6 bits wide
  assign and_8_out = rom_general_1_q0 & {6{decoder_1_out2[5]}};  // AND_Gate and_8, 6 bits wide
  assign and_9_out = rom_general_1_q0 & {6{decoder_1_out3[5]}};  // AND_Gate and_9, 6 bits wide
  xor xor_1 (xor_1_out, register_4bit_1_q0[3], 1'b1);
  xor xor_2 (xor_2_out, register_4bit_1_q0[2], 1'b1);
  xor xor_3 (xor_3_out, register_4bit_1_q0[1], 1'b1);
  xor xor_4 (xor_4_out, register_4bit_1_q0[0], 1'b1);
  and and_10 (and_10_out, 1'b0, decoder_1_out3[5]);
  Adder #(.width(4)) adder_1 (.a(or_2_out), .b(or_1_out), .out(adder_1_out), .cin(1'b0));  // open: cout
  Decoder #(.select(3)) decoder_2 (
    .out0(decoder_2_out0), .sel(and_7_out[2:0]), .en(1'b1));  // open: out1, out2, out3, out4, out5, out6, out7
  or or_3 (or_3_out, decoder_1_out0[5], decoder_1_out2[5], and_10_out);
  // Probe on register_4bit_1_q0[2:0]
  assign and_11_out = and_7_out[5:4] & {2{and_7_out[3]}};  // AND_Gate and_11, 2 bits wide
  Multiplexer #(.select(2), .width(8)) multiplexer_1 (
    .in0({{6{1'b0}}, and_8_out[1:0]}), .in1({4'b0000, and_8_out[1:0], 2'b00}),
    .in2({2'b00, and_8_out[1:0], 4'b0000}), .in3({and_8_out[1:0], {6{1'b0}}}), .out(multiplexer_1_out),
    .sel(and_8_out[3:2]));
  assign not_7_out = ~{2{decoder_1_out3[5]}};  // NOT_Gate not_7, 2 bits wide
  assign and_12_out = {2{decoder_1_out3[5]}} & 2'b00;  // AND_Gate and_12, 2 bits wide
  assign and_13_out = not_7_out & and_6_out[3:2];  // AND_Gate and_13, 2 bits wide
  assign not_8_out = ~{4{and_17_out[3]}};  // NOT_Gate not_8, 4 bits wide
  assign or_4_out = and_12_out | and_13_out;  // OR_Gate or_4, 2 bits wide
  Register_4bit register_4bit_1 (
    .clk(CLK_out), .RESET(RESET1), .D3(or_8_out[3]), .D2(or_8_out[2]), .D1(or_8_out[1]), .D0(or_8_out[0]),
    .enable(1'b1), .Q3(register_4bit_1_q0[3]), .Q2(register_4bit_1_q0[2]), .Q1(register_4bit_1_q0[1]),
    .Q0(register_4bit_1_q0[0]));
  or or_5 (or_5_out, and_16_out[0], multiplexer_1_out[0]);
  assign and_14_out = adder_1_out & not_8_out;  // AND_Gate and_14, 4 bits wide
  assign and_15_out = {4{and_17_out[3]}} & adder_3_out;  // AND_Gate and_15, 4 bits wide
  or or_6 (or_6_out, multiplexer_1_out[1], and_16_out[1]);
  or or_7 (or_7_out, multiplexer_1_out[2], and_16_out[2]);
  assign or_8_out = and_14_out | and_15_out;  // OR_Gate or_8, 4 bits wide
  or or_9 (or_9_out, multiplexer_1_out[3], and_16_out[3]);
  or or_10 (or_10_out, multiplexer_1_out[4], and_16_out[4]);
  or or_11 (or_11_out, multiplexer_1_out[5], and_16_out[5]);
  or or_12 (or_12_out, and_6_out[0], and_11_out[0], and_9_out[0]);
  or or_13 (or_13_out, and_6_out[1], and_11_out[1], and_9_out[1]);
  or or_14 (or_14_out, and_6_out[4], and_8_out[4]);
  or or_15 (or_15_out, and_8_out[5], and_6_out[5]);
  Random_access_memory random_access_memory_1 (
    .raddr2_1(or_13_out), .raddr2_0(or_12_out), .D7(multiplexer_1_out[7]), .D6(multiplexer_1_out[6]),
    .D4(or_10_out), .D3(or_9_out), .D5(or_11_out), .D2(or_7_out), .D1(or_6_out), .D0(or_5_out),
    .raddr1_1(or_4_out[1]), .raddr1_0(or_4_out[0]), .clk(CLK_out), .WEN(or_3_out), .waddr1(or_15_out),
    .waddr0(or_14_out), .reset(reset2), .rdata2_2(random_access_memory_1_rdata2_0[2]),
    .rdata2_1(random_access_memory_1_rdata2_0[1]), .rdata2_0(random_access_memory_1_rdata2_0[0]),
    .rdata2_3(random_access_memory_1_rdata2_0[3]), .rdata2_4(random_access_memory_1_rdata2_0[4]),
    .rdata2_5(random_access_memory_1_rdata2_0[5]), .rdata1_3(random_access_memory_1_rdata1_0[3]),
    .rdata1_2(random_access_memory_1_rdata1_0[2]), .rdata1_1(random_access_memory_1_rdata1_0[1]),
    .rdata1_0(random_access_memory_1_rdata1_0[0]), .rdata1_4(random_access_memory_1_rdata1_0[4]),
    .rdata1_5(random_access_memory_1_rdata1_0[5]), .Q7(random_access_memory_1_q0[7]),
    .Q6(random_access_memory_1_q0[6]), .Q5(random_access_memory_1_q0[5]), .Q4(random_access_memory_1_q0[4]),
    .Q3(random_access_memory_1_q0[3]), .Q2(random_access_memory_1_q0[2]), .Q1(random_access_memory_1_q0[1]),
    .Q0(random_access_memory_1_q0[0]));
  assign and_16_out = adder_2_out & {6{decoder_1_out0[5]}};  // AND_Gate and_16, 6 bits wide
  // Probe on random_access_memory_1_rdata2_0
  Adder #(.width(6)) adder_2 (
    .a(random_access_memory_1_rdata2_0), .b(random_access_memory_1_rdata1_0), .out(adder_2_out), .cin(1'b0));  // open: cout
  // Probe on random_access_memory_1_rdata1_0
  not not_9 (not_9_out, comparator_1_eq);
  Comparator #(.width(6)) comparator_1 (
    .a(random_access_memory_1_rdata1_0), .b(random_access_memory_1_rdata2_0), .eq(comparator_1_eq));  // open: gt, lt
  // Probe on random_access_memory_1_q0
  Adder #(.width(4)) adder_3 (.a(and_9_out[5:2]), .b(register_4bit_1_q0), .out(adder_3_out), .cin(1'b0));  // open: cout
  and and_17 (and_17_out[3], decoder_1_out3[5], not_9_out);
  and and_18 (and_18_out, decoder_2_out0, decoder_1_out1[5], and_7_out[3]);
  Register_8bit register_8bit_1 (
    .CLK(CLK_out), .RESET(RESET1), .D7(1'b0), .D6(1'b0), .D5(random_access_memory_1_rdata2_0[5]),
    .D4(random_access_memory_1_rdata2_0[4]), .D3(random_access_memory_1_rdata2_0[3]),
    .D2(random_access_memory_1_rdata2_0[2]), .D1(random_access_memory_1_rdata2_0[1]),
    .D0(random_access_memory_1_rdata2_0[0]), .ENABLE(and_18_out), .Q7(register_8bit_1_q0[7]),
    .Q6(register_8bit_1_q0[6]), .Q5(register_8bit_1_q0[5]), .Q4(register_8bit_1_q0[4]),
    .Q3(register_8bit_1_q0[3]), .Q2(register_8bit_1_q0[2]), .Q1(register_8bit_1_q0[1]),
    .Q0(register_8bit_1_q0[0]));
  // LedBar #(.inputtype("row")) ledbar_1: pin names not known; wires that end beside it: register_8bit_1_q0
endmodule

module ROM_general (
  input  A2,
  input  A1,
  input  A0,
  input  [7:0] MC0,
  input  [7:0] MC1,
  input  [7:0] MC2,
  input  [7:0] MC3,
  input  [7:0] MC4,
  input  [7:0] MC5,
  input  [7:0] MC6,
  input  [7:0] MC7,
  output Q7,
  output Q6,
  output Q5,
  output Q4,
  output Q3,
  output Q2,
  output Q1,
  output Q0
);

  wire and_1_out, and_2_out, and_3_out, and_4_out, and_5_out, and_6_out, and_7_out, and_8_out, and_9_out,
       and_10_out, and_11_out, and_12_out, and_13_out, and_14_out, and_15_out, and_16_out, and_17_out,
       and_18_out, and_19_out, and_20_out, and_21_out, and_22_out, and_23_out, and_24_out, and_25_out,
       and_26_out, and_27_out, and_28_out, and_29_out, and_30_out, and_31_out, and_32_out, and_33_out,
       and_34_out, and_35_out, and_36_out, and_37_out, and_38_out, and_39_out, and_40_out, and_41_out,
       and_42_out, and_43_out, and_44_out, and_45_out, and_46_out, and_47_out, and_48_out, and_49_out,
       and_50_out, and_51_out, and_52_out, and_53_out, and_54_out, and_55_out, and_56_out, and_57_out,
       and_58_out, and_59_out, and_60_out, and_61_out, and_62_out, and_63_out, and_64_out, decoder_1_out0,
       decoder_1_out1, decoder_1_out2, decoder_1_out3, decoder_1_out4, decoder_1_out5, decoder_1_out6,
       decoder_1_out7;

  Decoder #(.select(3)) decoder_1 (
    .out0(decoder_1_out0), .out1(decoder_1_out1), .out2(decoder_1_out2), .out3(decoder_1_out3),
    .out4(decoder_1_out4), .out5(decoder_1_out5), .out6(decoder_1_out6), .out7(decoder_1_out7),
    .sel({A2, A1, A0}), .en(1'b1));
  or or_1 (Q7, and_1_out, and_2_out, and_3_out, and_4_out, and_5_out, and_6_out, and_7_out, and_8_out);
  and and_1 (and_1_out, decoder_1_out0, MC0[7]);
  and and_2 (and_2_out, decoder_1_out1, MC1[7]);
  and and_3 (and_3_out, decoder_1_out2, MC2[7]);
  and and_4 (and_4_out, decoder_1_out3, MC3[7]);
  and and_5 (and_5_out, decoder_1_out4, MC4[7]);
  and and_6 (and_6_out, decoder_1_out5, MC5[7]);
  and and_7 (and_7_out, decoder_1_out6, MC6[7]);
  and and_8 (and_8_out, decoder_1_out7, MC7[7]);
  and and_9 (and_9_out, decoder_1_out0, MC0[6]);
  and and_10 (and_10_out, decoder_1_out1, MC1[6]);
  and and_11 (and_11_out, decoder_1_out2, MC2[6]);
  and and_12 (and_12_out, decoder_1_out3, MC3[6]);
  and and_13 (and_13_out, decoder_1_out4, MC4[6]);
  and and_14 (and_14_out, decoder_1_out5, MC5[6]);
  and and_15 (and_15_out, decoder_1_out6, MC6[6]);
  and and_16 (and_16_out, decoder_1_out7, MC7[6]);
  or or_2 (Q6, and_9_out, and_10_out, and_11_out, and_12_out, and_13_out, and_14_out, and_15_out, and_16_out);
  and and_17 (and_17_out, decoder_1_out0, MC0[5]);
  and and_18 (and_18_out, decoder_1_out1, MC1[5]);
  and and_19 (and_19_out, decoder_1_out2, MC2[5]);
  and and_20 (and_20_out, decoder_1_out3, MC3[5]);
  and and_21 (and_21_out, decoder_1_out4, MC4[5]);
  and and_22 (and_22_out, decoder_1_out5, MC5[5]);
  and and_23 (and_23_out, decoder_1_out6, MC6[5]);
  and and_24 (and_24_out, decoder_1_out7, MC7[5]);
  or or_3 (Q5, and_17_out, and_18_out, and_19_out, and_20_out, and_21_out, and_22_out, and_23_out, and_24_out);
  and and_25 (and_25_out, decoder_1_out0, MC0[4]);
  and and_26 (and_26_out, decoder_1_out1, MC1[4]);
  and and_27 (and_27_out, decoder_1_out2, MC2[4]);
  and and_28 (and_28_out, decoder_1_out3, MC3[4]);
  and and_29 (and_29_out, decoder_1_out4, MC4[4]);
  and and_30 (and_30_out, decoder_1_out5, MC5[4]);
  and and_31 (and_31_out, decoder_1_out6, MC6[4]);
  and and_32 (and_32_out, decoder_1_out7, MC7[4]);
  and and_33 (and_33_out, decoder_1_out0, MC0[3]);
  and and_34 (and_34_out, decoder_1_out1, MC1[3]);
  and and_35 (and_35_out, decoder_1_out2, MC2[3]);
  and and_36 (and_36_out, decoder_1_out3, MC3[3]);
  and and_37 (and_37_out, decoder_1_out4, MC4[3]);
  and and_38 (and_38_out, decoder_1_out5, MC5[3]);
  and and_39 (and_39_out, decoder_1_out6, MC6[3]);
  and and_40 (and_40_out, decoder_1_out7, MC7[3]);
  or or_4 (Q4, and_25_out, and_26_out, and_27_out, and_28_out, and_29_out, and_30_out, and_31_out, and_32_out);
  and and_41 (and_41_out, decoder_1_out0, MC0[2]);
  and and_42 (and_42_out, decoder_1_out1, MC1[2]);
  and and_43 (and_43_out, decoder_1_out2, MC2[2]);
  and and_44 (and_44_out, decoder_1_out3, MC3[2]);
  and and_45 (and_45_out, decoder_1_out4, MC4[2]);
  and and_46 (and_46_out, decoder_1_out5, MC5[2]);
  and and_47 (and_47_out, decoder_1_out6, MC6[2]);
  and and_48 (and_48_out, decoder_1_out7, MC7[2]);
  or or_5 (Q3, and_33_out, and_34_out, and_35_out, and_36_out, and_37_out, and_38_out, and_39_out, and_40_out);
  and and_49 (and_49_out, decoder_1_out0, MC0[1]);
  and and_50 (and_50_out, decoder_1_out1, MC1[1]);
  and and_51 (and_51_out, decoder_1_out2, MC2[1]);
  and and_52 (and_52_out, decoder_1_out3, MC3[1]);
  and and_53 (and_53_out, decoder_1_out4, MC4[1]);
  and and_54 (and_54_out, decoder_1_out5, MC5[1]);
  and and_55 (and_55_out, decoder_1_out6, MC6[1]);
  and and_56 (and_56_out, decoder_1_out7, MC7[1]);
  and and_57 (and_57_out, decoder_1_out0, MC0[0]);
  and and_58 (and_58_out, decoder_1_out1, MC1[0]);
  and and_59 (and_59_out, decoder_1_out2, MC2[0]);
  and and_60 (and_60_out, decoder_1_out3, MC3[0]);
  and and_61 (and_61_out, decoder_1_out4, MC4[0]);
  and and_62 (and_62_out, decoder_1_out5, MC5[0]);
  and and_63 (and_63_out, decoder_1_out6, MC6[0]);
  and and_64 (and_64_out, decoder_1_out7, MC7[0]);
  or or_6 (Q2, and_41_out, and_42_out, and_43_out, and_44_out, and_45_out, and_46_out, and_47_out, and_48_out);
  or or_7 (Q1, and_49_out, and_50_out, and_51_out, and_52_out, and_53_out, and_54_out, and_55_out, and_56_out);
  or or_8 (Q0, and_57_out, and_58_out, and_59_out, and_60_out, and_61_out, and_62_out, and_63_out, and_64_out);
endmodule

module io_scpu_hex_digit_display (
  input  reset2,
  input  RESET1
);

  wire and_10_out, and_18_out, CLK_out, comparator_1_eq, decoder_2_out1, not_3_out, not_4_out, not_5_out,
       not_6_out, not_9_out, or_3_out, or_5_out, or_6_out, or_7_out, or_9_out, or_10_out, or_11_out,
       or_12_out, or_13_out, or_14_out, or_15_out, xor_1_out, xor_2_out, xor_3_out, xor_4_out;
  wire [1:0] and_11_out, and_12_out, and_13_out, not_7_out, or_4_out, rom_general_1_q6;
  wire [3:0] adder_1_out, adder_3_out, and_1_out, and_2_out, and_3_out, and_4_out, and_14_out, and_15_out,
       not_1_out, not_2_out, not_8_out, or_1_out, or_2_out, or_8_out, register_4bit_1_q0, register_8bit_1_q0,
       register_8bit_1_q4;
  wire [3:3] and_5_out, and_17_out;
  wire [5:0] adder_2_out, and_6_out, and_7_out, and_8_out, and_9_out, and_16_out,
       random_access_memory_1_rdata1_0, random_access_memory_1_rdata2_0, rom_general_1_q0;
  wire [5:5] decoder_1_out0, decoder_1_out1, decoder_1_out2, decoder_1_out3;
  wire [7:0] multiplexer_1_out, random_access_memory_1_q0;

  assign not_1_out = ~{4{and_5_out[3]}};  // NOT_Gate not_1, 4 bits wide
  assign not_2_out = ~{4{and_5_out[3]}};  // NOT_Gate not_2, 4 bits wide
  assign and_1_out = register_4bit_1_q0 & not_2_out;  // AND_Gate and_1, 4 bits wide
  assign and_2_out = {4{and_5_out[3]}} & 4'b0000;  // AND_Gate and_2, 4 bits wide
  assign and_3_out = 4'b0001 & not_1_out;  // AND_Gate and_3, 4 bits wide
  assign and_4_out = {4{and_5_out[3]}} & 4'b0000;  // AND_Gate and_4, 4 bits wide
  assign or_1_out = and_3_out | and_4_out;  // OR_Gate or_1, 4 bits wide
  assign or_2_out = and_1_out | and_2_out;  // OR_Gate or_2, 4 bits wide
  Decoder #(.select(2)) decoder_1 (
    .out0(decoder_1_out0[5]), .out1(decoder_1_out1[5]), .out2(decoder_1_out2[5]), .out3(decoder_1_out3[5]),
    .sel(rom_general_1_q6), .en(1'b1));
  ROM_general rom_general_1 (
    .A2(register_4bit_1_q0[2]), .A1(register_4bit_1_q0[1]), .A0(register_4bit_1_q0[0]), .MC0(8'h86),
    .MC1(8'hb3), .MC2(8'h3), .MC3(8'hb1), .MC4(8'h29), .MC5(8'h17), .MC6(8'hf9), .MC7(8'h69),
    .Q7(rom_general_1_q6[1]), .Q6(rom_general_1_q6[0]), .Q5(rom_general_1_q0[5]), .Q4(rom_general_1_q0[4]),
    .Q3(rom_general_1_q0[3]), .Q2(rom_general_1_q0[2]), .Q1(rom_general_1_q0[1]), .Q0(rom_general_1_q0[0]));
  and and_5 (and_5_out[3], not_3_out, not_4_out, not_5_out, not_6_out);
  Clock CLK (.out(CLK_out));
  not not_3 (not_3_out, xor_1_out);
  not not_4 (not_4_out, xor_2_out);
  not not_5 (not_5_out, xor_3_out);
  not not_6 (not_6_out, xor_4_out);
  assign and_6_out = {6{decoder_1_out0[5]}} & rom_general_1_q0;  // AND_Gate and_6, 6 bits wide
  assign and_7_out = {6{decoder_1_out1[5]}} & rom_general_1_q0;  // AND_Gate and_7, 6 bits wide
  assign and_8_out = rom_general_1_q0 & {6{decoder_1_out2[5]}};  // AND_Gate and_8, 6 bits wide
  assign and_9_out = rom_general_1_q0 & {6{decoder_1_out3[5]}};  // AND_Gate and_9, 6 bits wide
  xor xor_1 (xor_1_out, register_4bit_1_q0[3], 1'b1);
  xor xor_2 (xor_2_out, register_4bit_1_q0[2], 1'b1);
  xor xor_3 (xor_3_out, register_4bit_1_q0[1], 1'b1);
  xor xor_4 (xor_4_out, register_4bit_1_q0[0], 1'b1);
  Adder #(.width(4)) adder_1 (.a(or_2_out), .b(or_1_out), .out(adder_1_out), .cin(1'b0));  // open: cout
  and and_10 (and_10_out, 1'b0, decoder_1_out3[5]);
  Decoder #(.select(3)) decoder_2 (
    .out1(decoder_2_out1), .sel(and_7_out[2:0]), .en(1'b1));  // open: out0, out2, out3, out4, out5, out6, out7
  or or_3 (or_3_out, decoder_1_out0[5], decoder_1_out2[5], and_10_out);
  // Probe on register_4bit_1_q0[2:0]
  assign and_11_out = and_7_out[5:4] & {2{and_7_out[3]}};  // AND_Gate and_11, 2 bits wide
  Multiplexer #(.select(2), .width(8)) multiplexer_1 (
    .in0({{6{1'b0}}, and_8_out[1:0]}), .in1({4'b0000, and_8_out[1:0], 2'b00}),
    .in2({2'b00, and_8_out[1:0], 4'b0000}), .in3({and_8_out[1:0], {6{1'b0}}}), .out(multiplexer_1_out),
    .sel(and_8_out[3:2]));
  assign not_7_out = ~{2{decoder_1_out3[5]}};  // NOT_Gate not_7, 2 bits wide
  assign and_12_out = {2{decoder_1_out3[5]}} & 2'b00;  // AND_Gate and_12, 2 bits wide
  assign and_13_out = not_7_out & and_6_out[3:2];  // AND_Gate and_13, 2 bits wide
  assign not_8_out = ~{4{and_17_out[3]}};  // NOT_Gate not_8, 4 bits wide
  assign or_4_out = and_12_out | and_13_out;  // OR_Gate or_4, 2 bits wide
  Register_4bit register_4bit_1 (
    .clk(CLK_out), .RESET(RESET1), .D3(or_8_out[3]), .D2(or_8_out[2]), .D1(or_8_out[1]), .D0(or_8_out[0]),
    .enable(1'b1), .Q3(register_4bit_1_q0[3]), .Q2(register_4bit_1_q0[2]), .Q1(register_4bit_1_q0[1]),
    .Q0(register_4bit_1_q0[0]));
  or or_5 (or_5_out, and_16_out[0], multiplexer_1_out[0]);
  assign and_14_out = adder_1_out & not_8_out;  // AND_Gate and_14, 4 bits wide
  assign and_15_out = {4{and_17_out[3]}} & adder_3_out;  // AND_Gate and_15, 4 bits wide
  or or_6 (or_6_out, multiplexer_1_out[1], and_16_out[1]);
  or or_7 (or_7_out, multiplexer_1_out[2], and_16_out[2]);
  assign or_8_out = and_14_out | and_15_out;  // OR_Gate or_8, 4 bits wide
  or or_9 (or_9_out, multiplexer_1_out[3], and_16_out[3]);
  or or_10 (or_10_out, multiplexer_1_out[4], and_16_out[4]);
  or or_11 (or_11_out, multiplexer_1_out[5], and_16_out[5]);
  or or_12 (or_12_out, and_6_out[0], and_11_out[0], and_9_out[0]);
  or or_13 (or_13_out, and_6_out[1], and_11_out[1], and_9_out[1]);
  or or_14 (or_14_out, and_6_out[4], and_8_out[4]);
  or or_15 (or_15_out, and_8_out[5], and_6_out[5]);
  Random_access_memory random_access_memory_1 (
    .raddr2_1(or_13_out), .raddr2_0(or_12_out), .D7(multiplexer_1_out[7]), .D6(multiplexer_1_out[6]),
    .D4(or_10_out), .D3(or_9_out), .D5(or_11_out), .D2(or_7_out), .D1(or_6_out), .D0(or_5_out),
    .raddr1_1(or_4_out[1]), .raddr1_0(or_4_out[0]), .clk(CLK_out), .WEN(or_3_out), .waddr1(or_15_out),
    .waddr0(or_14_out), .reset(reset2), .rdata2_2(random_access_memory_1_rdata2_0[2]),
    .rdata2_1(random_access_memory_1_rdata2_0[1]), .rdata2_0(random_access_memory_1_rdata2_0[0]),
    .rdata2_3(random_access_memory_1_rdata2_0[3]), .rdata2_4(random_access_memory_1_rdata2_0[4]),
    .rdata2_5(random_access_memory_1_rdata2_0[5]), .rdata1_3(random_access_memory_1_rdata1_0[3]),
    .rdata1_2(random_access_memory_1_rdata1_0[2]), .rdata1_1(random_access_memory_1_rdata1_0[1]),
    .rdata1_0(random_access_memory_1_rdata1_0[0]), .rdata1_4(random_access_memory_1_rdata1_0[4]),
    .rdata1_5(random_access_memory_1_rdata1_0[5]), .Q7(random_access_memory_1_q0[7]),
    .Q6(random_access_memory_1_q0[6]), .Q5(random_access_memory_1_q0[5]), .Q4(random_access_memory_1_q0[4]),
    .Q3(random_access_memory_1_q0[3]), .Q2(random_access_memory_1_q0[2]), .Q1(random_access_memory_1_q0[1]),
    .Q0(random_access_memory_1_q0[0]));
  assign and_16_out = adder_2_out & {6{decoder_1_out0[5]}};  // AND_Gate and_16, 6 bits wide
  // Probe on random_access_memory_1_rdata2_0
  Adder #(.width(6)) adder_2 (
    .a(random_access_memory_1_rdata2_0), .b(random_access_memory_1_rdata1_0), .out(adder_2_out), .cin(1'b0));  // open: cout
  // Probe on random_access_memory_1_rdata1_0
  not not_9 (not_9_out, comparator_1_eq);
  Comparator #(.width(6)) comparator_1 (
    .a(random_access_memory_1_rdata1_0), .b(random_access_memory_1_rdata2_0), .eq(comparator_1_eq));  // open: gt, lt
  // Probe on random_access_memory_1_q0
  Adder #(.width(4)) adder_3 (.a(and_9_out[5:2]), .b(register_4bit_1_q0), .out(adder_3_out), .cin(1'b0));  // open: cout
  and and_17 (and_17_out[3], decoder_1_out3[5], not_9_out);
  and and_18 (and_18_out, decoder_2_out1, decoder_1_out1[5], and_7_out[3]);
  Register_8bit register_8bit_1 (
    .CLK(CLK_out), .RESET(RESET1), .D7(1'b0), .D6(1'b0), .D5(random_access_memory_1_rdata2_0[5]),
    .D4(random_access_memory_1_rdata2_0[4]), .D3(random_access_memory_1_rdata2_0[3]),
    .D2(random_access_memory_1_rdata2_0[2]), .D1(random_access_memory_1_rdata2_0[1]),
    .D0(random_access_memory_1_rdata2_0[0]), .ENABLE(and_18_out), .Q7(register_8bit_1_q4[3]),
    .Q6(register_8bit_1_q4[2]), .Q5(register_8bit_1_q4[1]), .Q4(register_8bit_1_q4[0]),
    .Q3(register_8bit_1_q0[3]), .Q2(register_8bit_1_q0[2]), .Q1(register_8bit_1_q0[1]),
    .Q0(register_8bit_1_q0[0]));
  Hex_Digit_Display #(.decimalPoint("false")) hex_digit_display_1 (.value(register_8bit_1_q4));
  Hex_Digit_Display #(.decimalPoint("false")) hex_digit_display_2 (.value(register_8bit_1_q0));
endmodule

module io_scpu_dip_switch (
  input  reset2,
  input  RESET1
);

  wire and_10_out, and_11_out, and_22_out, CLK_out, comparator_1_eq, decoder_2_out0, decoder_2_out1,
       not_3_out, not_4_out, not_5_out, not_6_out, not_10_out, or_3_out, or_5_out, or_6_out, or_7_out,
       or_9_out, or_10_out, or_11_out, or_12_out, or_13_out, or_14_out, or_15_out, or_16_out, or_17_out,
       xor_1_out, xor_2_out, xor_3_out, xor_4_out;
  wire [1:0] and_12_out, and_13_out, and_14_out, and_15_out, not_8_out, or_4_out, rom_general_1_q6;
  wire [1:1] not_7_out;
  wire [3:0] adder_1_out, adder_3_out, and_1_out, and_2_out, and_3_out, and_4_out, and_16_out, and_17_out,
       not_1_out, not_2_out, not_9_out, or_1_out, or_2_out, or_8_out, register_4bit_1_q0, register_8bit_1_q0,
       register_8bit_1_q4;
  wire [3:3] and_5_out, and_21_out;
  wire [5:0] adder_2_out, and_6_out, and_7_out, and_8_out, and_9_out, and_20_out,
       random_access_memory_1_rdata1_0, random_access_memory_1_rdata2_0, rom_general_1_q0;
  wire [5:5] decoder_1_out0, decoder_1_out1, decoder_1_out2, decoder_1_out3;
  wire [7:0] and_19_out, dipswitch_1_sw8, multiplexer_1_out, random_access_memory_1_q0;
  wire [7:7] and_18_out;

  assign not_1_out = ~{4{and_5_out[3]}};  // NOT_Gate not_1, 4 bits wide
  assign not_2_out = ~{4{and_5_out[3]}};  // NOT_Gate not_2, 4 bits wide
  assign and_1_out = register_4bit_1_q0 & not_2_out;  // AND_Gate and_1, 4 bits wide
  assign and_2_out = {4{and_5_out[3]}} & 4'b0000;  // AND_Gate and_2, 4 bits wide
  assign and_3_out = 4'b0001 & not_1_out;  // AND_Gate and_3, 4 bits wide
  assign and_4_out = {4{and_5_out[3]}} & 4'b0000;  // AND_Gate and_4, 4 bits wide
  assign or_1_out = and_3_out | and_4_out;  // OR_Gate or_1, 4 bits wide
  assign or_2_out = and_1_out | and_2_out;  // OR_Gate or_2, 4 bits wide
  Decoder #(.select(2)) decoder_1 (
    .out0(decoder_1_out0[5]), .out1(decoder_1_out1[5]), .out2(decoder_1_out2[5]), .out3(decoder_1_out3[5]),
    .sel(rom_general_1_q6), .en(1'b1));
  ROM_general rom_general_1 (
    .A2(register_4bit_1_q0[2]), .A1(register_4bit_1_q0[1]), .A0(register_4bit_1_q0[0]), .MC0(8'h40),
    .MC1(8'hb1), .MC2(8'h3), .MC3(8'h29), .MC4(8'h17), .MC5(8'hf9), .MC6(8'h69), .MC7(8'hc3),
    .Q7(rom_general_1_q6[1]), .Q6(rom_general_1_q6[0]), .Q5(rom_general_1_q0[5]), .Q4(rom_general_1_q0[4]),
    .Q3(rom_general_1_q0[3]), .Q2(rom_general_1_q0[2]), .Q1(rom_general_1_q0[1]), .Q0(rom_general_1_q0[0]));
  and and_5 (and_5_out[3], not_3_out, not_4_out, not_5_out, not_6_out);
  DipSwitch dipswitch_1 (
    .sw1(dipswitch_1_sw8[7]), .sw2(dipswitch_1_sw8[6]), .sw3(dipswitch_1_sw8[5]), .sw4(dipswitch_1_sw8[4]),
    .sw5(dipswitch_1_sw8[3]), .sw6(dipswitch_1_sw8[2]), .sw7(dipswitch_1_sw8[1]), .sw8(dipswitch_1_sw8[0]));
  Clock CLK (.out(CLK_out));
  not not_3 (not_3_out, xor_1_out);
  not not_4 (not_4_out, xor_2_out);
  not not_5 (not_5_out, xor_3_out);
  not not_6 (not_6_out, xor_4_out);
  assign and_6_out = {6{decoder_1_out0[5]}} & rom_general_1_q0;  // AND_Gate and_6, 6 bits wide
  assign and_7_out = {6{decoder_1_out1[5]}} & rom_general_1_q0;  // AND_Gate and_7, 6 bits wide
  assign and_8_out = rom_general_1_q0 & {6{decoder_1_out2[5]}};  // AND_Gate and_8, 6 bits wide
  assign and_9_out = rom_general_1_q0 & {6{decoder_1_out3[5]}};  // AND_Gate and_9, 6 bits wide
  xor xor_1 (xor_1_out, register_4bit_1_q0[3], 1'b1);
  xor xor_2 (xor_2_out, register_4bit_1_q0[2], 1'b1);
  xor xor_3 (xor_3_out, register_4bit_1_q0[1], 1'b1);
  xor xor_4 (xor_4_out, register_4bit_1_q0[0], 1'b1);
  Adder #(.width(4)) adder_1 (.a(or_2_out), .b(or_1_out), .out(adder_1_out), .cin(1'b0));  // open: cout
  not not_7 (not_7_out[1], and_7_out[3]);
  Decoder #(.select(3)) decoder_2 (
    .out0(decoder_2_out0), .out1(decoder_2_out1), .sel(and_7_out[2:0]), .en(1'b1));  // open: out2, out3, out4, out5, out6, out7
  or or_3 (or_3_out, decoder_1_out2[5], decoder_1_out0[5], and_10_out, and_11_out);
  and and_10 (and_10_out, 1'b0, decoder_1_out3[5]);
  // Probe on register_4bit_1_q0[2:0]
  and and_11 (and_11_out, decoder_1_out1[5], not_7_out[1]);
  assign and_12_out = {2{not_7_out[1]}} & and_7_out[5:4];  // AND_Gate and_12, 2 bits wide
  assign and_13_out = and_7_out[5:4] & {2{and_7_out[3]}};  // AND_Gate and_13, 2 bits wide
  Multiplexer #(.select(2), .width(8)) multiplexer_1 (
    .in0({{6{1'b0}}, and_8_out[1:0]}), .in1({4'b0000, and_8_out[1:0], 2'b00}),
    .in2({2'b00, and_8_out[1:0], 4'b0000}), .in3({and_8_out[1:0], {6{1'b0}}}), .out(multiplexer_1_out),
    .sel(and_8_out[3:2]));
  assign not_8_out = ~{2{decoder_1_out3[5]}};  // NOT_Gate not_8, 2 bits wide
  assign and_14_out = {2{decoder_1_out3[5]}} & 2'b00;  // AND_Gate and_14, 2 bits wide
  assign and_15_out = not_8_out & and_6_out[3:2];  // AND_Gate and_15, 2 bits wide
  assign not_9_out = ~{4{and_21_out[3]}};  // NOT_Gate not_9, 4 bits wide
  assign or_4_out = and_14_out | and_15_out;  // OR_Gate or_4, 2 bits wide
  Register_4bit register_4bit_1 (
    .clk(CLK_out), .RESET(RESET1), .D3(or_8_out[3]), .D2(or_8_out[2]), .D1(or_8_out[1]), .D0(or_8_out[0]),
    .enable(1'b1), .Q3(register_4bit_1_q0[3]), .Q2(register_4bit_1_q0[2]), .Q1(register_4bit_1_q0[1]),
    .Q0(register_4bit_1_q0[0]));
  or or_5 (or_5_out, and_20_out[0], and_19_out[0], multiplexer_1_out[0]);
  assign and_16_out = adder_1_out & not_9_out;  // AND_Gate and_16, 4 bits wide
  assign and_17_out = {4{and_21_out[3]}} & adder_3_out;  // AND_Gate and_17, 4 bits wide
  or or_6 (or_6_out, multiplexer_1_out[1], and_19_out[1], and_20_out[1]);
  or or_7 (or_7_out, multiplexer_1_out[2], and_19_out[2], and_20_out[2]);
  assign or_8_out = and_16_out | and_17_out;  // OR_Gate or_8, 4 bits wide
  and and_18 (and_18_out[7], decoder_1_out1[5], not_7_out[1], decoder_2_out0);
  or or_9 (or_9_out, and_19_out[6], multiplexer_1_out[6]);
  or or_10 (or_10_out, multiplexer_1_out[3], and_19_out[3], and_20_out[3]);
  or or_11 (or_11_out, multiplexer_1_out[4], and_19_out[4], and_20_out[4]);
  or or_12 (or_12_out, multiplexer_1_out[5], and_19_out[5], and_20_out[5]);
  or or_13 (or_13_out, and_6_out[0], and_13_out[0], and_9_out[0]);
  or or_14 (or_14_out, and_6_out[1], and_13_out[1], and_9_out[1]);
  or or_15 (or_15_out, multiplexer_1_out[7], and_19_out[7]);
  assign and_19_out = dipswitch_1_sw8 & {8{and_18_out[7]}};  // AND_Gate and_19, 8 bits wide
  or or_16 (or_16_out, and_6_out[4], and_12_out[0], and_8_out[4]);
  or or_17 (or_17_out, and_8_out[5], and_12_out[1], and_6_out[5]);
  Random_access_memory random_access_memory_1 (
    .raddr2_1(or_14_out), .raddr2_0(or_13_out), .D7(or_15_out), .D6(or_9_out), .D4(or_11_out),
    .D3(or_10_out), .D5(or_12_out), .D2(or_7_out), .D1(or_6_out), .D0(or_5_out), .raddr1_1(or_4_out[1]),
    .raddr1_0(or_4_out[0]), .clk(CLK_out), .WEN(or_3_out), .waddr1(or_17_out), .waddr0(or_16_out),
    .reset(reset2), .rdata2_2(random_access_memory_1_rdata2_0[2]),
    .rdata2_1(random_access_memory_1_rdata2_0[1]), .rdata2_0(random_access_memory_1_rdata2_0[0]),
    .rdata2_3(random_access_memory_1_rdata2_0[3]), .rdata2_4(random_access_memory_1_rdata2_0[4]),
    .rdata2_5(random_access_memory_1_rdata2_0[5]), .rdata1_3(random_access_memory_1_rdata1_0[3]),
    .rdata1_2(random_access_memory_1_rdata1_0[2]), .rdata1_1(random_access_memory_1_rdata1_0[1]),
    .rdata1_0(random_access_memory_1_rdata1_0[0]), .rdata1_4(random_access_memory_1_rdata1_0[4]),
    .rdata1_5(random_access_memory_1_rdata1_0[5]), .Q7(random_access_memory_1_q0[7]),
    .Q6(random_access_memory_1_q0[6]), .Q5(random_access_memory_1_q0[5]), .Q4(random_access_memory_1_q0[4]),
    .Q3(random_access_memory_1_q0[3]), .Q2(random_access_memory_1_q0[2]), .Q1(random_access_memory_1_q0[1]),
    .Q0(random_access_memory_1_q0[0]));
  assign and_20_out = adder_2_out & {6{decoder_1_out0[5]}};  // AND_Gate and_20, 6 bits wide
  // Probe on random_access_memory_1_rdata2_0
  Adder #(.width(6)) adder_2 (
    .a(random_access_memory_1_rdata2_0), .b(random_access_memory_1_rdata1_0), .out(adder_2_out), .cin(1'b0));  // open: cout
  // Probe on random_access_memory_1_rdata1_0
  not not_10 (not_10_out, comparator_1_eq);
  Comparator #(.width(6)) comparator_1 (
    .a(random_access_memory_1_rdata1_0), .b(random_access_memory_1_rdata2_0), .eq(comparator_1_eq));  // open: gt, lt
  // Probe on random_access_memory_1_q0
  Adder #(.width(4)) adder_3 (.a(and_9_out[5:2]), .b(register_4bit_1_q0), .out(adder_3_out), .cin(1'b0));  // open: cout
  and and_21 (and_21_out[3], decoder_1_out3[5], not_10_out);
  and and_22 (and_22_out, decoder_2_out1, decoder_1_out1[5], and_7_out[3]);
  Register_8bit register_8bit_1 (
    .CLK(CLK_out), .RESET(RESET1), .D7(1'b0), .D6(1'b0), .D5(random_access_memory_1_rdata2_0[5]),
    .D4(random_access_memory_1_rdata2_0[4]), .D3(random_access_memory_1_rdata2_0[3]),
    .D2(random_access_memory_1_rdata2_0[2]), .D1(random_access_memory_1_rdata2_0[1]),
    .D0(random_access_memory_1_rdata2_0[0]), .ENABLE(and_22_out), .Q7(register_8bit_1_q4[3]),
    .Q6(register_8bit_1_q4[2]), .Q5(register_8bit_1_q4[1]), .Q4(register_8bit_1_q4[0]),
    .Q3(register_8bit_1_q0[3]), .Q2(register_8bit_1_q0[2]), .Q1(register_8bit_1_q0[1]),
    .Q0(register_8bit_1_q0[0]));
  Hex_Digit_Display #(.decimalPoint("false")) hex_digit_display_1 (.value(register_8bit_1_q4));
  Hex_Digit_Display #(.decimalPoint("false")) hex_digit_display_2 (.value(register_8bit_1_q0));
endmodule

module io_scpu_button (
  input  reset2,
  input  RESET1
);

  wire and_10_out, and_11_out, and_24_out, and_25_out, CLK_out, comparator_1_eq, decoder_2_out0,
       decoder_2_out1, not_3_out, not_4_out, not_5_out, not_6_out, not_10_out, or_3_out, or_5_out, or_6_out,
       or_7_out, or_9_out, or_10_out, or_11_out, or_12_out, or_13_out, or_14_out, or_15_out, or_16_out,
       or_17_out, xor_1_out, xor_2_out, xor_3_out, xor_4_out;
  wire [1:0] and_12_out, and_13_out, and_14_out, and_15_out, not_8_out, or_4_out;
  wire [1:1] not_7_out;
  wire [3:0] adder_1_out, adder_3_out, and_1_out, and_2_out, and_3_out, and_4_out, and_16_out, and_17_out,
       not_1_out, not_2_out, not_9_out, or_1_out, or_2_out, or_8_out, register_4bit_1_q0, register_8bit_1_q0,
       register_8bit_1_q4;
  wire [3:3] and_5_out, and_23_out;
  wire [5:0] adder_2_out, and_6_out, and_7_out, and_8_out, and_9_out, and_22_out,
       random_access_memory_1_rdata1_0, random_access_memory_1_rdata2_0;
  wire [5:5] decoder_1_out0, decoder_1_out1, decoder_1_out2, decoder_1_out3;
  wire [7:0] A0_out, and_20_out, and_21_out, dipswitch_1_sw8, ledbar_1_p1, multiplexer_1_out, or_18_out,
       random_access_memory_1_q0, rom_1_data;
  wire [7:7] and_18_out, and_19_out;

  assign not_1_out = ~{4{and_5_out[3]}};  // NOT_Gate not_1, 4 bits wide
  ROM #(.addrWidth(4)) rom_1 (.addr(register_4bit_1_q0), .data(rom_1_data));
  assign not_2_out = ~{4{and_5_out[3]}};  // NOT_Gate not_2, 4 bits wide
  assign and_1_out = register_4bit_1_q0 & not_2_out;  // AND_Gate and_1, 4 bits wide
  assign and_2_out = {4{and_5_out[3]}} & 4'b0000;  // AND_Gate and_2, 4 bits wide
  assign and_3_out = 4'b0001 & not_1_out;  // AND_Gate and_3, 4 bits wide
  assign and_4_out = {4{and_5_out[3]}} & 4'b0000;  // AND_Gate and_4, 4 bits wide
  assign or_1_out = and_3_out | and_4_out;  // OR_Gate or_1, 4 bits wide
  Button A7 (.out(A0_out[7]));
  Button A6 (.out(A0_out[6]));
  Button A5 (.out(A0_out[5]));
  Button A4 (.out(A0_out[4]));
  Button A3 (.out(A0_out[3]));
  Button A2 (.out(A0_out[2]));
  Button A1 (.out(A0_out[1]));
  Button A0 (.out(A0_out[0]));
  assign or_2_out = and_1_out | and_2_out;  // OR_Gate or_2, 4 bits wide
  Decoder #(.select(2)) decoder_1 (
    .out0(decoder_1_out0[5]), .out1(decoder_1_out1[5]), .out2(decoder_1_out2[5]), .out3(decoder_1_out3[5]),
    .sel(rom_1_data[7:6]), .en(1'b1));
  and and_5 (and_5_out[3], not_3_out, not_4_out, not_5_out, not_6_out);
  DipSwitch dipswitch_1 (
    .sw1(dipswitch_1_sw8[7]), .sw2(dipswitch_1_sw8[6]), .sw3(dipswitch_1_sw8[5]), .sw4(dipswitch_1_sw8[4]),
    .sw5(dipswitch_1_sw8[3]), .sw6(dipswitch_1_sw8[2]), .sw7(dipswitch_1_sw8[1]), .sw8(dipswitch_1_sw8[0]));
  Clock CLK (.out(CLK_out));
  not not_3 (not_3_out, xor_1_out);
  not not_4 (not_4_out, xor_2_out);
  not not_5 (not_5_out, xor_3_out);
  not not_6 (not_6_out, xor_4_out);
  assign and_6_out = {6{decoder_1_out0[5]}} & rom_1_data[5:0];  // AND_Gate and_6, 6 bits wide
  assign and_7_out = {6{decoder_1_out1[5]}} & rom_1_data[5:0];  // AND_Gate and_7, 6 bits wide
  assign and_8_out = rom_1_data[5:0] & {6{decoder_1_out2[5]}};  // AND_Gate and_8, 6 bits wide
  assign and_9_out = rom_1_data[5:0] & {6{decoder_1_out3[5]}};  // AND_Gate and_9, 6 bits wide
  xor xor_1 (xor_1_out, register_4bit_1_q0[3], 1'b1);
  xor xor_2 (xor_2_out, register_4bit_1_q0[2], 1'b1);
  xor xor_3 (xor_3_out, register_4bit_1_q0[1], 1'b1);
  xor xor_4 (xor_4_out, register_4bit_1_q0[0], 1'b1);
  Adder #(.width(4)) adder_1 (.a(or_2_out), .b(or_1_out), .out(adder_1_out), .cin(1'b0));  // open: cout
  and and_10 (and_10_out, 1'b0, decoder_1_out3[5]);
  not not_7 (not_7_out[1], and_7_out[3]);
  Decoder #(.select(3)) decoder_2 (
    .out0(decoder_2_out0), .out1(decoder_2_out1), .sel(and_7_out[2:0]), .en(1'b1));  // open: out2, out3, out4, out5, out6, out7
  or or_3 (or_3_out, decoder_1_out2[5], decoder_1_out0[5], and_10_out, and_11_out);
  // Probe on register_4bit_1_q0
  and and_11 (and_11_out, decoder_1_out1[5], not_7_out[1]);
  assign and_12_out = {2{not_7_out[1]}} & and_7_out[5:4];  // AND_Gate and_12, 2 bits wide
  assign and_13_out = and_7_out[5:4] & {2{and_7_out[3]}};  // AND_Gate and_13, 2 bits wide
  Multiplexer #(.select(2), .width(8)) multiplexer_1 (
    .in0({{6{1'b0}}, and_8_out[1:0]}), .in1({4'b0000, and_8_out[1:0], 2'b00}),
    .in2({2'b00, and_8_out[1:0], 4'b0000}), .in3({and_8_out[1:0], {6{1'b0}}}), .out(multiplexer_1_out),
    .sel(and_8_out[3:2]));
  assign not_8_out = ~{2{decoder_1_out3[5]}};  // NOT_Gate not_8, 2 bits wide
  assign and_14_out = {2{decoder_1_out3[5]}} & 2'b00;  // AND_Gate and_14, 2 bits wide
  assign and_15_out = not_8_out & and_6_out[3:2];  // AND_Gate and_15, 2 bits wide
  assign not_9_out = ~{4{and_23_out[3]}};  // NOT_Gate not_9, 4 bits wide
  assign or_4_out = and_14_out | and_15_out;  // OR_Gate or_4, 2 bits wide
  Register_4bit register_4bit_1 (
    .clk(CLK_out), .RESET(RESET1), .D3(or_8_out[3]), .D2(or_8_out[2]), .D1(or_8_out[1]), .D0(or_8_out[0]),
    .enable(1'b1), .Q3(register_4bit_1_q0[3]), .Q2(register_4bit_1_q0[2]), .Q1(register_4bit_1_q0[1]),
    .Q0(register_4bit_1_q0[0]));
  or or_5 (or_5_out, and_22_out[0], or_18_out[0], multiplexer_1_out[0]);
  assign and_16_out = adder_1_out & not_9_out;  // AND_Gate and_16, 4 bits wide
  assign and_17_out = {4{and_23_out[3]}} & adder_3_out;  // AND_Gate and_17, 4 bits wide
  or or_6 (or_6_out, multiplexer_1_out[1], or_18_out[1], and_22_out[1]);
  or or_7 (or_7_out, multiplexer_1_out[2], or_18_out[2], and_22_out[2]);
  assign or_8_out = and_16_out | and_17_out;  // OR_Gate or_8, 4 bits wide
  and and_18 (and_18_out[7], decoder_1_out1[5], not_7_out[1], decoder_2_out1);
  and and_19 (and_19_out[7], decoder_1_out1[5], not_7_out[1], decoder_2_out0);
  or or_9 (or_9_out, or_18_out[6], multiplexer_1_out[6]);
  or or_10 (or_10_out, multiplexer_1_out[3], or_18_out[3], and_22_out[3]);
  or or_11 (or_11_out, multiplexer_1_out[4], or_18_out[4], and_22_out[4]);
  or or_12 (or_12_out, multiplexer_1_out[5], or_18_out[5], and_22_out[5]);
  or or_13 (or_13_out, and_6_out[0], and_13_out[0], and_9_out[0]);
  or or_14 (or_14_out, and_6_out[1], and_13_out[1], and_9_out[1]);
  or or_15 (or_15_out, multiplexer_1_out[7], or_18_out[7]);
  assign and_20_out = A0_out & {8{and_18_out[7]}};  // AND_Gate and_20, 8 bits wide
  assign and_21_out = dipswitch_1_sw8 & {8{and_19_out[7]}};  // AND_Gate and_21, 8 bits wide
  or or_16 (or_16_out, and_6_out[4], and_12_out[0], and_8_out[4]);
  or or_17 (or_17_out, and_8_out[5], and_12_out[1], and_6_out[5]);
  assign or_18_out = and_20_out | and_21_out;  // OR_Gate or_18, 8 bits wide
  // LedBar #(.inputtype("row")) ledbar_1: pin names not known; wires that end beside it: ledbar_1_p1
  Random_access_memory random_access_memory_1 (
    .raddr2_1(or_14_out), .raddr2_0(or_13_out), .D7(or_15_out), .D6(or_9_out), .D4(or_11_out),
    .D3(or_10_out), .D5(or_12_out), .D2(or_7_out), .D1(or_6_out), .D0(or_5_out), .raddr1_1(or_4_out[1]),
    .raddr1_0(or_4_out[0]), .clk(CLK_out), .WEN(or_3_out), .waddr1(or_17_out), .waddr0(or_16_out),
    .reset(reset2), .rdata2_2(random_access_memory_1_rdata2_0[2]),
    .rdata2_1(random_access_memory_1_rdata2_0[1]), .rdata2_0(random_access_memory_1_rdata2_0[0]),
    .rdata2_3(random_access_memory_1_rdata2_0[3]), .rdata2_4(random_access_memory_1_rdata2_0[4]),
    .rdata2_5(random_access_memory_1_rdata2_0[5]), .rdata1_3(random_access_memory_1_rdata1_0[3]),
    .rdata1_2(random_access_memory_1_rdata1_0[2]), .rdata1_1(random_access_memory_1_rdata1_0[1]),
    .rdata1_0(random_access_memory_1_rdata1_0[0]), .rdata1_4(random_access_memory_1_rdata1_0[4]),
    .rdata1_5(random_access_memory_1_rdata1_0[5]), .Q7(random_access_memory_1_q0[7]),
    .Q6(random_access_memory_1_q0[6]), .Q5(random_access_memory_1_q0[5]), .Q4(random_access_memory_1_q0[4]),
    .Q3(random_access_memory_1_q0[3]), .Q2(random_access_memory_1_q0[2]), .Q1(random_access_memory_1_q0[1]),
    .Q0(random_access_memory_1_q0[0]));
  assign and_22_out = adder_2_out & {6{decoder_1_out0[5]}};  // AND_Gate and_22, 6 bits wide
  // Probe on random_access_memory_1_rdata2_0
  Adder #(.width(6)) adder_2 (
    .a(random_access_memory_1_rdata2_0), .b(random_access_memory_1_rdata1_0), .out(adder_2_out), .cin(1'b0));  // open: cout
  // Probe on random_access_memory_1_rdata1_0
  not not_10 (not_10_out, comparator_1_eq);
  Comparator #(.width(6)) comparator_1 (
    .a(random_access_memory_1_rdata1_0), .b(random_access_memory_1_rdata2_0), .eq(comparator_1_eq));  // open: gt, lt
  // Probe on random_access_memory_1_q0
  Adder #(.width(4)) adder_3 (.a(and_9_out[5:2]), .b(register_4bit_1_q0), .out(adder_3_out), .cin(1'b0));  // open: cout
  and and_23 (and_23_out[3], decoder_1_out3[5], not_10_out);
  and and_24 (and_24_out, decoder_1_out1[5], and_7_out[3], decoder_2_out0);
  and and_25 (and_25_out, decoder_2_out1, decoder_1_out1[5], and_7_out[3]);
  Register_8bit register_8bit_1 (
    .CLK(CLK_out), .RESET(RESET1), .D7(1'b0), .D6(1'b0), .D5(random_access_memory_1_rdata2_0[5]),
    .D4(random_access_memory_1_rdata2_0[4]), .D3(random_access_memory_1_rdata2_0[3]),
    .D2(random_access_memory_1_rdata2_0[2]), .D1(random_access_memory_1_rdata2_0[1]),
    .D0(random_access_memory_1_rdata2_0[0]), .ENABLE(and_25_out), .Q7(register_8bit_1_q4[3]),
    .Q6(register_8bit_1_q4[2]), .Q5(register_8bit_1_q4[1]), .Q4(register_8bit_1_q4[0]),
    .Q3(register_8bit_1_q0[3]), .Q2(register_8bit_1_q0[2]), .Q1(register_8bit_1_q0[1]),
    .Q0(register_8bit_1_q0[0]));
  Register_8bit register_8bit_2 (
    .CLK(CLK_out), .RESET(RESET1), .D7(1'b0), .D6(1'b0), .D5(random_access_memory_1_rdata2_0[5]),
    .D4(random_access_memory_1_rdata2_0[4]), .D3(random_access_memory_1_rdata2_0[3]),
    .D2(random_access_memory_1_rdata2_0[2]), .D1(random_access_memory_1_rdata2_0[1]),
    .D0(random_access_memory_1_rdata2_0[0]), .ENABLE(and_24_out), .Q7(ledbar_1_p1[7]), .Q6(ledbar_1_p1[6]),
    .Q5(ledbar_1_p1[5]), .Q4(ledbar_1_p1[4]), .Q3(ledbar_1_p1[3]), .Q2(ledbar_1_p1[2]), .Q1(ledbar_1_p1[1]),
    .Q0(ledbar_1_p1[0]));
  Hex_Digit_Display #(.decimalPoint("false")) hex_digit_display_1 (.value(register_8bit_1_q4));
  Hex_Digit_Display #(.decimalPoint("false")) hex_digit_display_2 (.value(register_8bit_1_q0));

  // Notes on the sheet:
  //   contents of rom_1 (hex, n*v repeats v):
  //   40 b1 3 29 17 58 f5 80 71 cb f9 69 c1
endmodule
module Single_step_summation_program (
  input  reset2,
  input  RESET1
);

  wire and_10_out, and_11_out, and_24_out, and_25_out, CLK_out, comparator_1_eq, decoder_2_out0,
       decoder_2_out1, not_3_out, not_4_out, not_5_out, not_6_out, not_10_out, or_3_out, or_5_out, or_6_out,
       or_7_out, or_9_out, or_10_out, or_11_out, or_12_out, or_13_out, or_14_out, or_15_out, or_16_out,
       or_17_out, xor_1_out, xor_2_out, xor_3_out, xor_4_out;
  wire [1:0] and_12_out, and_13_out, and_14_out, and_15_out, not_8_out, or_4_out;
  wire [1:1] not_7_out;
  wire [3:0] adder_1_out, adder_3_out, and_1_out, and_2_out, and_3_out, and_4_out, and_16_out, and_17_out,
       not_1_out, not_2_out, not_9_out, or_1_out, or_2_out, or_8_out, register_4bit_1_q0, register_8bit_1_q0,
       register_8bit_1_q4;
  wire [3:3] and_5_out, and_23_out;
  wire [5:0] adder_2_out, and_6_out, and_7_out, and_8_out, and_9_out, and_22_out,
       random_access_memory_1_rdata1_0, random_access_memory_1_rdata2_0;
  wire [5:5] decoder_1_out0, decoder_1_out1, decoder_1_out2, decoder_1_out3;
  wire [7:0] A0_out, and_20_out, and_21_out, dipswitch_1_sw8, ledbar_1_p1, multiplexer_1_out, or_18_out,
       random_access_memory_1_q0, rom_1_data;
  wire [7:7] and_18_out, and_19_out;

  assign not_1_out = ~{4{and_5_out[3]}};  // NOT_Gate not_1, 4 bits wide
  ROM #(.addrWidth(4)) rom_1 (.addr(register_4bit_1_q0), .data(rom_1_data));
  assign not_2_out = ~{4{and_5_out[3]}};  // NOT_Gate not_2, 4 bits wide
  assign and_1_out = register_4bit_1_q0 & not_2_out;  // AND_Gate and_1, 4 bits wide
  assign and_2_out = {4{and_5_out[3]}} & 4'b0000;  // AND_Gate and_2, 4 bits wide
  assign and_3_out = 4'b0001 & not_1_out;  // AND_Gate and_3, 4 bits wide
  assign and_4_out = {4{and_5_out[3]}} & 4'b0000;  // AND_Gate and_4, 4 bits wide
  assign or_1_out = and_3_out | and_4_out;  // OR_Gate or_1, 4 bits wide
  Button A7 (.out(A0_out[7]));
  Button A6 (.out(A0_out[6]));
  Button A5 (.out(A0_out[5]));
  Button A4 (.out(A0_out[4]));
  Button A3 (.out(A0_out[3]));
  Button A2 (.out(A0_out[2]));
  Button A1 (.out(A0_out[1]));
  Button A0 (.out(A0_out[0]));
  assign or_2_out = and_1_out | and_2_out;  // OR_Gate or_2, 4 bits wide
  Decoder #(.select(2)) decoder_1 (
    .out0(decoder_1_out0[5]), .out1(decoder_1_out1[5]), .out2(decoder_1_out2[5]), .out3(decoder_1_out3[5]),
    .sel(rom_1_data[7:6]), .en(1'b1));
  and and_5 (and_5_out[3], not_3_out, not_4_out, not_5_out, not_6_out);
  DipSwitch dipswitch_1 (
    .sw1(dipswitch_1_sw8[7]), .sw2(dipswitch_1_sw8[6]), .sw3(dipswitch_1_sw8[5]), .sw4(dipswitch_1_sw8[4]),
    .sw5(dipswitch_1_sw8[3]), .sw6(dipswitch_1_sw8[2]), .sw7(dipswitch_1_sw8[1]), .sw8(dipswitch_1_sw8[0]));
  Clock CLK (.out(CLK_out));
  not not_3 (not_3_out, xor_1_out);
  not not_4 (not_4_out, xor_2_out);
  not not_5 (not_5_out, xor_3_out);
  not not_6 (not_6_out, xor_4_out);
  assign and_6_out = {6{decoder_1_out0[5]}} & rom_1_data[5:0];  // AND_Gate and_6, 6 bits wide
  assign and_7_out = {6{decoder_1_out1[5]}} & rom_1_data[5:0];  // AND_Gate and_7, 6 bits wide
  assign and_8_out = rom_1_data[5:0] & {6{decoder_1_out2[5]}};  // AND_Gate and_8, 6 bits wide
  assign and_9_out = rom_1_data[5:0] & {6{decoder_1_out3[5]}};  // AND_Gate and_9, 6 bits wide
  xor xor_1 (xor_1_out, register_4bit_1_q0[3], 1'b1);
  xor xor_2 (xor_2_out, register_4bit_1_q0[2], 1'b1);
  xor xor_3 (xor_3_out, register_4bit_1_q0[1], 1'b1);
  xor xor_4 (xor_4_out, register_4bit_1_q0[0], 1'b1);
  Adder #(.width(4)) adder_1 (.a(or_2_out), .b(or_1_out), .out(adder_1_out), .cin(1'b0));  // open: cout
  and and_10 (and_10_out, 1'b0, decoder_1_out3[5]);
  not not_7 (not_7_out[1], and_7_out[3]);
  Decoder #(.select(3)) decoder_2 (
    .out0(decoder_2_out0), .out1(decoder_2_out1), .sel(and_7_out[2:0]), .en(1'b1));  // open: out2, out3, out4, out5, out6, out7
  or or_3 (or_3_out, decoder_1_out2[5], decoder_1_out0[5], and_10_out, and_11_out);
  // Probe on register_4bit_1_q0
  and and_11 (and_11_out, decoder_1_out1[5], not_7_out[1]);
  assign and_12_out = {2{not_7_out[1]}} & and_7_out[5:4];  // AND_Gate and_12, 2 bits wide
  assign and_13_out = and_7_out[5:4] & {2{and_7_out[3]}};  // AND_Gate and_13, 2 bits wide
  Multiplexer #(.select(2), .width(8)) multiplexer_1 (
    .in0({{6{1'b0}}, and_8_out[1:0]}), .in1({4'b0000, and_8_out[1:0], 2'b00}),
    .in2({2'b00, and_8_out[1:0], 4'b0000}), .in3({and_8_out[1:0], {6{1'b0}}}), .out(multiplexer_1_out),
    .sel(and_8_out[3:2]));
  assign not_8_out = ~{2{decoder_1_out3[5]}};  // NOT_Gate not_8, 2 bits wide
  assign and_14_out = {2{decoder_1_out3[5]}} & 2'b00;  // AND_Gate and_14, 2 bits wide
  assign and_15_out = not_8_out & and_6_out[3:2];  // AND_Gate and_15, 2 bits wide
  assign not_9_out = ~{4{and_23_out[3]}};  // NOT_Gate not_9, 4 bits wide
  assign or_4_out = and_14_out | and_15_out;  // OR_Gate or_4, 2 bits wide
  Register_4bit register_4bit_1 (
    .clk(CLK_out), .RESET(RESET1), .D3(or_8_out[3]), .D2(or_8_out[2]), .D1(or_8_out[1]), .D0(or_8_out[0]),
    .enable(1'b1), .Q3(register_4bit_1_q0[3]), .Q2(register_4bit_1_q0[2]), .Q1(register_4bit_1_q0[1]),
    .Q0(register_4bit_1_q0[0]));
  or or_5 (or_5_out, and_22_out[0], or_18_out[0], multiplexer_1_out[0]);
  assign and_16_out = adder_1_out & not_9_out;  // AND_Gate and_16, 4 bits wide
  assign and_17_out = {4{and_23_out[3]}} & adder_3_out;  // AND_Gate and_17, 4 bits wide
  or or_6 (or_6_out, multiplexer_1_out[1], or_18_out[1], and_22_out[1]);
  or or_7 (or_7_out, multiplexer_1_out[2], or_18_out[2], and_22_out[2]);
  assign or_8_out = and_16_out | and_17_out;  // OR_Gate or_8, 4 bits wide
  and and_18 (and_18_out[7], decoder_1_out1[5], not_7_out[1], decoder_2_out1);
  and and_19 (and_19_out[7], decoder_1_out1[5], not_7_out[1], decoder_2_out0);
  or or_9 (or_9_out, or_18_out[6], multiplexer_1_out[6]);
  or or_10 (or_10_out, multiplexer_1_out[3], or_18_out[3], and_22_out[3]);
  or or_11 (or_11_out, multiplexer_1_out[4], or_18_out[4], and_22_out[4]);
  or or_12 (or_12_out, multiplexer_1_out[5], or_18_out[5], and_22_out[5]);
  or or_13 (or_13_out, and_6_out[0], and_13_out[0], and_9_out[0]);
  or or_14 (or_14_out, and_6_out[1], and_13_out[1], and_9_out[1]);
  or or_15 (or_15_out, multiplexer_1_out[7], or_18_out[7]);
  assign and_20_out = A0_out & {8{and_18_out[7]}};  // AND_Gate and_20, 8 bits wide
  assign and_21_out = dipswitch_1_sw8 & {8{and_19_out[7]}};  // AND_Gate and_21, 8 bits wide
  or or_16 (or_16_out, and_6_out[4], and_12_out[0], and_8_out[4]);
  or or_17 (or_17_out, and_8_out[5], and_12_out[1], and_6_out[5]);
  assign or_18_out = and_20_out | and_21_out;  // OR_Gate or_18, 8 bits wide
  // LedBar #(.inputtype("row")) ledbar_1: pin names not known; wires that end beside it: ledbar_1_p1
  Random_access_memory random_access_memory_1 (
    .raddr2_1(or_14_out), .raddr2_0(or_13_out), .D7(or_15_out), .D6(or_9_out), .D4(or_11_out),
    .D3(or_10_out), .D5(or_12_out), .D2(or_7_out), .D1(or_6_out), .D0(or_5_out), .raddr1_1(or_4_out[1]),
    .raddr1_0(or_4_out[0]), .clk(CLK_out), .WEN(or_3_out), .waddr1(or_17_out), .waddr0(or_16_out),
    .reset(reset2), .rdata2_2(random_access_memory_1_rdata2_0[2]),
    .rdata2_1(random_access_memory_1_rdata2_0[1]), .rdata2_0(random_access_memory_1_rdata2_0[0]),
    .rdata2_3(random_access_memory_1_rdata2_0[3]), .rdata2_4(random_access_memory_1_rdata2_0[4]),
    .rdata2_5(random_access_memory_1_rdata2_0[5]), .rdata1_3(random_access_memory_1_rdata1_0[3]),
    .rdata1_2(random_access_memory_1_rdata1_0[2]), .rdata1_1(random_access_memory_1_rdata1_0[1]),
    .rdata1_0(random_access_memory_1_rdata1_0[0]), .rdata1_4(random_access_memory_1_rdata1_0[4]),
    .rdata1_5(random_access_memory_1_rdata1_0[5]), .Q7(random_access_memory_1_q0[7]),
    .Q6(random_access_memory_1_q0[6]), .Q5(random_access_memory_1_q0[5]), .Q4(random_access_memory_1_q0[4]),
    .Q3(random_access_memory_1_q0[3]), .Q2(random_access_memory_1_q0[2]), .Q1(random_access_memory_1_q0[1]),
    .Q0(random_access_memory_1_q0[0]));
  assign and_22_out = adder_2_out & {6{decoder_1_out0[5]}};  // AND_Gate and_22, 6 bits wide
  // Probe on random_access_memory_1_rdata2_0
  Adder #(.width(6)) adder_2 (
    .a(random_access_memory_1_rdata2_0), .b(random_access_memory_1_rdata1_0), .out(adder_2_out), .cin(1'b0));  // open: cout
  // Probe on random_access_memory_1_rdata1_0
  not not_10 (not_10_out, comparator_1_eq);
  Comparator #(.width(6)) comparator_1 (
    .a(random_access_memory_1_rdata1_0), .b(random_access_memory_1_rdata2_0), .eq(comparator_1_eq));  // open: gt, lt
  // Probe on random_access_memory_1_q0
  Adder #(.width(4)) adder_3 (.a(and_9_out[5:2]), .b(register_4bit_1_q0), .out(adder_3_out), .cin(1'b0));  // open: cout
  and and_23 (and_23_out[3], decoder_1_out3[5], not_10_out);
  and and_24 (and_24_out, decoder_1_out1[5], and_7_out[3], decoder_2_out0);
  and and_25 (and_25_out, decoder_2_out1, decoder_1_out1[5], and_7_out[3]);
  Register_8bit register_8bit_1 (
    .CLK(CLK_out), .RESET(RESET1), .D7(1'b0), .D6(1'b0), .D5(random_access_memory_1_rdata2_0[5]),
    .D4(random_access_memory_1_rdata2_0[4]), .D3(random_access_memory_1_rdata2_0[3]),
    .D2(random_access_memory_1_rdata2_0[2]), .D1(random_access_memory_1_rdata2_0[1]),
    .D0(random_access_memory_1_rdata2_0[0]), .ENABLE(and_25_out), .Q7(register_8bit_1_q4[3]),
    .Q6(register_8bit_1_q4[2]), .Q5(register_8bit_1_q4[1]), .Q4(register_8bit_1_q4[0]),
    .Q3(register_8bit_1_q0[3]), .Q2(register_8bit_1_q0[2]), .Q1(register_8bit_1_q0[1]),
    .Q0(register_8bit_1_q0[0]));
  Register_8bit register_8bit_2 (
    .CLK(CLK_out), .RESET(RESET1), .D7(1'b0), .D6(1'b0), .D5(random_access_memory_1_rdata2_0[5]),
    .D4(random_access_memory_1_rdata2_0[4]), .D3(random_access_memory_1_rdata2_0[3]),
    .D2(random_access_memory_1_rdata2_0[2]), .D1(random_access_memory_1_rdata2_0[1]),
    .D0(random_access_memory_1_rdata2_0[0]), .ENABLE(and_24_out), .Q7(ledbar_1_p1[7]), .Q6(ledbar_1_p1[6]),
    .Q5(ledbar_1_p1[5]), .Q4(ledbar_1_p1[4]), .Q3(ledbar_1_p1[3]), .Q2(ledbar_1_p1[2]), .Q1(ledbar_1_p1[1]),
    .Q0(ledbar_1_p1[0]));
  Hex_Digit_Display #(.decimalPoint("false")) hex_digit_display_1 (.value(register_8bit_1_q4));
  Hex_Digit_Display #(.decimalPoint("false")) hex_digit_display_2 (.value(register_8bit_1_q0));

  // Notes on the sheet:
  //   contents of rom_1 (hex, n*v repeats v):
  //   b1 40 17 29 58 69 41 ff 40 e5 c3 c3
endmodule

module Single2_step_summation_program (
  input  reset2,
  input  RESET1
);

  wire and_10_out, and_11_out, and_24_out, and_25_out, CLK_out, comparator_1_eq, decoder_2_out0,
       decoder_2_out1, not_3_out, not_4_out, not_5_out, not_6_out, not_10_out, or_3_out, or_5_out, or_6_out,
       or_7_out, or_9_out, or_10_out, or_11_out, or_12_out, or_13_out, or_14_out, or_15_out, or_16_out,
       or_17_out, xor_1_out, xor_2_out, xor_3_out, xor_4_out;
  wire [1:0] and_12_out, and_13_out, and_14_out, and_15_out, not_8_out, or_4_out;
  wire [1:1] not_7_out;
  wire [3:0] adder_1_out, adder_3_out, and_1_out, and_2_out, and_3_out, and_4_out, and_16_out, and_17_out,
       not_1_out, not_2_out, not_9_out, or_1_out, or_2_out, or_8_out, register_4bit_1_q0, register_8bit_1_q0,
       register_8bit_1_q4;
  wire [3:3] and_5_out, and_23_out;
  wire [5:0] adder_2_out, and_6_out, and_7_out, and_8_out, and_9_out, and_22_out,
       random_access_memory_1_rdata1_0, random_access_memory_1_rdata2_0;
  wire [5:5] decoder_1_out0, decoder_1_out1, decoder_1_out2, decoder_1_out3;
  wire [7:0] A0_out, and_20_out, and_21_out, dipswitch_1_sw8, ledbar_1_p1, multiplexer_1_out, or_18_out,
       random_access_memory_1_q0, rom_1_data;
  wire [7:7] and_18_out, and_19_out;

  assign not_1_out = ~{4{and_5_out[3]}};  // NOT_Gate not_1, 4 bits wide
  ROM #(.addrWidth(4)) rom_1 (.addr(register_4bit_1_q0), .data(rom_1_data));
  assign not_2_out = ~{4{and_5_out[3]}};  // NOT_Gate not_2, 4 bits wide
  assign and_1_out = register_4bit_1_q0 & not_2_out;  // AND_Gate and_1, 4 bits wide
  assign and_2_out = {4{and_5_out[3]}} & 4'b0000;  // AND_Gate and_2, 4 bits wide
  assign and_3_out = 4'b0001 & not_1_out;  // AND_Gate and_3, 4 bits wide
  assign and_4_out = {4{and_5_out[3]}} & 4'b0000;  // AND_Gate and_4, 4 bits wide
  assign or_1_out = and_3_out | and_4_out;  // OR_Gate or_1, 4 bits wide
  Button A7 (.out(A0_out[7]));
  Button A6 (.out(A0_out[6]));
  Button A5 (.out(A0_out[5]));
  Button A4 (.out(A0_out[4]));
  Button A3 (.out(A0_out[3]));
  Button A2 (.out(A0_out[2]));
  Button A1 (.out(A0_out[1]));
  Button A0 (.out(A0_out[0]));
  assign or_2_out = and_1_out | and_2_out;  // OR_Gate or_2, 4 bits wide
  Decoder #(.select(2)) decoder_1 (
    .out0(decoder_1_out0[5]), .out1(decoder_1_out1[5]), .out2(decoder_1_out2[5]), .out3(decoder_1_out3[5]),
    .sel(rom_1_data[7:6]), .en(1'b1));
  and and_5 (and_5_out[3], not_3_out, not_4_out, not_5_out, not_6_out);
  DipSwitch dipswitch_1 (
    .sw1(dipswitch_1_sw8[7]), .sw2(dipswitch_1_sw8[6]), .sw3(dipswitch_1_sw8[5]), .sw4(dipswitch_1_sw8[4]),
    .sw5(dipswitch_1_sw8[3]), .sw6(dipswitch_1_sw8[2]), .sw7(dipswitch_1_sw8[1]), .sw8(dipswitch_1_sw8[0]));
  Clock CLK (.out(CLK_out));
  not not_3 (not_3_out, xor_1_out);
  not not_4 (not_4_out, xor_2_out);
  not not_5 (not_5_out, xor_3_out);
  not not_6 (not_6_out, xor_4_out);
  assign and_6_out = {6{decoder_1_out0[5]}} & rom_1_data[5:0];  // AND_Gate and_6, 6 bits wide
  assign and_7_out = {6{decoder_1_out1[5]}} & rom_1_data[5:0];  // AND_Gate and_7, 6 bits wide
  assign and_8_out = rom_1_data[5:0] & {6{decoder_1_out2[5]}};  // AND_Gate and_8, 6 bits wide
  assign and_9_out = rom_1_data[5:0] & {6{decoder_1_out3[5]}};  // AND_Gate and_9, 6 bits wide
  xor xor_1 (xor_1_out, register_4bit_1_q0[3], 1'b1);
  xor xor_2 (xor_2_out, register_4bit_1_q0[2], 1'b1);
  xor xor_3 (xor_3_out, register_4bit_1_q0[1], 1'b1);
  xor xor_4 (xor_4_out, register_4bit_1_q0[0], 1'b1);
  Adder #(.width(4)) adder_1 (.a(or_2_out), .b(or_1_out), .out(adder_1_out), .cin(1'b0));  // open: cout
  and and_10 (and_10_out, 1'b0, decoder_1_out3[5]);
  not not_7 (not_7_out[1], and_7_out[3]);
  Decoder #(.select(3)) decoder_2 (
    .out0(decoder_2_out0), .out1(decoder_2_out1), .sel(and_7_out[2:0]), .en(1'b1));  // open: out2, out3, out4, out5, out6, out7
  or or_3 (or_3_out, decoder_1_out2[5], decoder_1_out0[5], and_10_out, and_11_out);
  // Probe on register_4bit_1_q0
  and and_11 (and_11_out, decoder_1_out1[5], not_7_out[1]);
  assign and_12_out = {2{not_7_out[1]}} & and_7_out[5:4];  // AND_Gate and_12, 2 bits wide
  assign and_13_out = and_7_out[5:4] & {2{and_7_out[3]}};  // AND_Gate and_13, 2 bits wide
  Multiplexer #(.select(2), .width(8)) multiplexer_1 (
    .in0({{6{1'b0}}, and_8_out[1:0]}), .in1({4'b0000, and_8_out[1:0], 2'b00}),
    .in2({2'b00, and_8_out[1:0], 4'b0000}), .in3({and_8_out[1:0], {6{1'b0}}}), .out(multiplexer_1_out),
    .sel(and_8_out[3:2]));
  assign not_8_out = ~{2{decoder_1_out3[5]}};  // NOT_Gate not_8, 2 bits wide
  assign and_14_out = {2{decoder_1_out3[5]}} & 2'b00;  // AND_Gate and_14, 2 bits wide
  assign and_15_out = not_8_out & and_6_out[3:2];  // AND_Gate and_15, 2 bits wide
  assign not_9_out = ~{4{and_23_out[3]}};  // NOT_Gate not_9, 4 bits wide
  assign or_4_out = and_14_out | and_15_out;  // OR_Gate or_4, 2 bits wide
  Register_4bit register_4bit_1 (
    .clk(CLK_out), .RESET(RESET1), .D3(or_8_out[3]), .D2(or_8_out[2]), .D1(or_8_out[1]), .D0(or_8_out[0]),
    .enable(1'b1), .Q3(register_4bit_1_q0[3]), .Q2(register_4bit_1_q0[2]), .Q1(register_4bit_1_q0[1]),
    .Q0(register_4bit_1_q0[0]));
  or or_5 (or_5_out, and_22_out[0], or_18_out[0], multiplexer_1_out[0]);
  assign and_16_out = adder_1_out & not_9_out;  // AND_Gate and_16, 4 bits wide
  assign and_17_out = {4{and_23_out[3]}} & adder_3_out;  // AND_Gate and_17, 4 bits wide
  or or_6 (or_6_out, multiplexer_1_out[1], or_18_out[1], and_22_out[1]);
  or or_7 (or_7_out, multiplexer_1_out[2], or_18_out[2], and_22_out[2]);
  assign or_8_out = and_16_out | and_17_out;  // OR_Gate or_8, 4 bits wide
  and and_18 (and_18_out[7], decoder_1_out1[5], not_7_out[1], decoder_2_out1);
  and and_19 (and_19_out[7], decoder_1_out1[5], not_7_out[1], decoder_2_out0);
  or or_9 (or_9_out, or_18_out[6], multiplexer_1_out[6]);
  or or_10 (or_10_out, multiplexer_1_out[3], or_18_out[3], and_22_out[3]);
  or or_11 (or_11_out, multiplexer_1_out[4], or_18_out[4], and_22_out[4]);
  or or_12 (or_12_out, multiplexer_1_out[5], or_18_out[5], and_22_out[5]);
  or or_13 (or_13_out, and_6_out[0], and_13_out[0], and_9_out[0]);
  or or_14 (or_14_out, and_6_out[1], and_13_out[1], and_9_out[1]);
  or or_15 (or_15_out, multiplexer_1_out[7], or_18_out[7]);
  assign and_20_out = A0_out & {8{and_18_out[7]}};  // AND_Gate and_20, 8 bits wide
  assign and_21_out = dipswitch_1_sw8 & {8{and_19_out[7]}};  // AND_Gate and_21, 8 bits wide
  or or_16 (or_16_out, and_6_out[4], and_12_out[0], and_8_out[4]);
  or or_17 (or_17_out, and_8_out[5], and_12_out[1], and_6_out[5]);
  assign or_18_out = and_20_out | and_21_out;  // OR_Gate or_18, 8 bits wide
  // LedBar #(.inputtype("row")) ledbar_1: pin names not known; wires that end beside it: ledbar_1_p1
  Random_access_memory random_access_memory_1 (
    .raddr2_1(or_14_out), .raddr2_0(or_13_out), .D7(or_15_out), .D6(or_9_out), .D4(or_11_out),
    .D3(or_10_out), .D5(or_12_out), .D2(or_7_out), .D1(or_6_out), .D0(or_5_out), .raddr1_1(or_4_out[1]),
    .raddr1_0(or_4_out[0]), .clk(CLK_out), .WEN(or_3_out), .waddr1(or_17_out), .waddr0(or_16_out),
    .reset(reset2), .rdata2_2(random_access_memory_1_rdata2_0[2]),
    .rdata2_1(random_access_memory_1_rdata2_0[1]), .rdata2_0(random_access_memory_1_rdata2_0[0]),
    .rdata2_3(random_access_memory_1_rdata2_0[3]), .rdata2_4(random_access_memory_1_rdata2_0[4]),
    .rdata2_5(random_access_memory_1_rdata2_0[5]), .rdata1_3(random_access_memory_1_rdata1_0[3]),
    .rdata1_2(random_access_memory_1_rdata1_0[2]), .rdata1_1(random_access_memory_1_rdata1_0[1]),
    .rdata1_0(random_access_memory_1_rdata1_0[0]), .rdata1_4(random_access_memory_1_rdata1_0[4]),
    .rdata1_5(random_access_memory_1_rdata1_0[5]), .Q7(random_access_memory_1_q0[7]),
    .Q6(random_access_memory_1_q0[6]), .Q5(random_access_memory_1_q0[5]), .Q4(random_access_memory_1_q0[4]),
    .Q3(random_access_memory_1_q0[3]), .Q2(random_access_memory_1_q0[2]), .Q1(random_access_memory_1_q0[1]),
    .Q0(random_access_memory_1_q0[0]));
  assign and_22_out = adder_2_out & {6{decoder_1_out0[5]}};  // AND_Gate and_22, 6 bits wide
  // Probe on random_access_memory_1_rdata2_0
  Adder #(.width(6)) adder_2 (
    .a(random_access_memory_1_rdata2_0), .b(random_access_memory_1_rdata1_0), .out(adder_2_out), .cin(1'b0));  // open: cout
  // Probe on random_access_memory_1_rdata1_0
  not not_10 (not_10_out, comparator_1_eq);
  Comparator #(.width(6)) comparator_1 (
    .a(random_access_memory_1_rdata1_0), .b(random_access_memory_1_rdata2_0), .eq(comparator_1_eq));  // open: gt, lt
  // Probe on random_access_memory_1_q0
  Adder #(.width(4)) adder_3 (.a(and_9_out[5:2]), .b(register_4bit_1_q0), .out(adder_3_out), .cin(1'b0));  // open: cout
  and and_23 (and_23_out[3], decoder_1_out3[5], not_10_out);
  and and_24 (and_24_out, decoder_1_out1[5], and_7_out[3], decoder_2_out0);
  and and_25 (and_25_out, decoder_2_out1, decoder_1_out1[5], and_7_out[3]);
  Register_8bit register_8bit_1 (
    .CLK(CLK_out), .RESET(RESET1), .D7(1'b0), .D6(1'b0), .D5(random_access_memory_1_rdata2_0[5]),
    .D4(random_access_memory_1_rdata2_0[4]), .D3(random_access_memory_1_rdata2_0[3]),
    .D2(random_access_memory_1_rdata2_0[2]), .D1(random_access_memory_1_rdata2_0[1]),
    .D0(random_access_memory_1_rdata2_0[0]), .ENABLE(and_25_out), .Q7(register_8bit_1_q4[3]),
    .Q6(register_8bit_1_q4[2]), .Q5(register_8bit_1_q4[1]), .Q4(register_8bit_1_q4[0]),
    .Q3(register_8bit_1_q0[3]), .Q2(register_8bit_1_q0[2]), .Q1(register_8bit_1_q0[1]),
    .Q0(register_8bit_1_q0[0]));
  Register_8bit register_8bit_2 (
    .CLK(CLK_out), .RESET(RESET1), .D7(1'b0), .D6(1'b0), .D5(random_access_memory_1_rdata2_0[5]),
    .D4(random_access_memory_1_rdata2_0[4]), .D3(random_access_memory_1_rdata2_0[3]),
    .D2(random_access_memory_1_rdata2_0[2]), .D1(random_access_memory_1_rdata2_0[1]),
    .D0(random_access_memory_1_rdata2_0[0]), .ENABLE(and_24_out), .Q7(ledbar_1_p1[7]), .Q6(ledbar_1_p1[6]),
    .Q5(ledbar_1_p1[5]), .Q4(ledbar_1_p1[4]), .Q3(ledbar_1_p1[3]), .Q2(ledbar_1_p1[2]), .Q1(ledbar_1_p1[1]),
    .Q0(ledbar_1_p1[0]));
  Hex_Digit_Display #(.decimalPoint("false")) hex_digit_display_1 (.value(register_8bit_1_q4));
  Hex_Digit_Display #(.decimalPoint("false")) hex_digit_display_2 (.value(register_8bit_1_q0));

  // Notes on the sheet:
  //   contents of rom_1 (hex, n*v repeats v):
  //   b1 17 29 58 69 41 ff 41 cb fa 40 c9 c3
endmodule
