// Logisim project sequential_logic_circuit.circ as structural Verilog: 15 circuits, main circuit SR_latch_norgate
module SR_latch_norgate (
  output out_1,
  output out_2
);

  wire and_1_out, and_2_out, dipswitch_1_sw1, dipswitch_1_sw2, dipswitch_1_sw3;

  DipSwitch dipswitch_1 (
    .sw1(dipswitch_1_sw1), .sw2(dipswitch_1_sw2), .sw3(dipswitch_1_sw3));  // open: sw4, sw5, sw6, sw7, sw8
  and and_1 (and_1_out, dipswitch_1_sw1, dipswitch_1_sw2);
  and and_2 (and_2_out, dipswitch_1_sw2, dipswitch_1_sw3);
  nor nor_1 (out_1, and_1_out, out_2);
  nor nor_2 (out_2, out_1, and_2_out);
endmodule

module SR_latch_NANDgate (
  output out_1,
  output out_2
);

  wire and_1_out, and_2_out, dipswitch_1_sw1, dipswitch_1_sw2, dipswitch_1_sw3;

  DipSwitch dipswitch_1 (
    .sw1(dipswitch_1_sw1), .sw2(dipswitch_1_sw2), .sw3(dipswitch_1_sw3));  // open: sw4, sw5, sw6, sw7, sw8
  and and_1 (and_1_out, dipswitch_1_sw1, dipswitch_1_sw2);
  and and_2 (and_2_out, dipswitch_1_sw2, dipswitch_1_sw3);
  nand nand_1 (out_1, out_2, and_1_out);
  nand nand_2 (out_2, out_1, and_2_out);
endmodule

module D_latch_reset (
  input  RESET,
  input  WE,
  input  D,
  output Q,
  output QNOT
);

  wire and_1_out, and_2_out, and_3_out, not_1_out, not_2_out, or_1_out;

  not not_1 (not_1_out, RESET);
  and and_1 (and_1_out, not_1_out, D);
  or or_1 (or_1_out, RESET, WE);
  not not_2 (not_2_out, and_1_out);
  and and_2 (and_2_out, and_1_out, or_1_out);
  and and_3 (and_3_out, or_1_out, not_2_out);
  nor nor_1 (Q, and_3_out, QNOT);
  nor nor_2 (QNOT, Q, and_2_out);
endmodule

module Toggle_D_latch (
  input  in_1,
  input  in_2
);

  wire d_latch_reset_1_q, d_latch_reset_1_qnot;

  D_latch_reset d_latch_reset_1 (
    .RESET(in_1), .WE(in_2), .D(d_latch_reset_1_qnot), .Q(d_latch_reset_1_q), .QNOT(d_latch_reset_1_qnot));
  // Probe on d_latch_reset_1_q
endmodule

module Positive_D_flip_flop (
  input  clk,
  input  D,
  output Q,
  output NOTQ
);

  wire d_latch_1_q, not_1_out;

  not not_1 (not_1_out, clk);
  D_latch d_latch_1 (.WE(not_1_out), .D(D), .Q(d_latch_1_q));  // open: QNOT
  D_latch d_latch_2 (.WE(clk), .D(d_latch_1_q), .Q(Q), .QNOT(NOTQ));
endmodule

module D_latch (
  input  WE,
  input  D,
  output Q,
  output QNOT
);

  wire and_1_out, and_2_out, not_1_out;

  not not_1 (not_1_out, D);
  and and_1 (and_1_out, D, WE);
  and and_2 (and_2_out, WE, not_1_out);
  nor nor_1 (Q, and_2_out, QNOT);
  nor nor_2 (QNOT, Q, and_1_out);
endmodule

module D_flip_flop_reset (
  input  clk,
  input  RESET,
  input  D,
  output Q
);

  wire and_1_out, d_latch_1_q, not_1_out, not_2_out;

  not not_1 (not_1_out, RESET);
  and and_1 (and_1_out, not_1_out, D);
  not not_2 (not_2_out, clk);
  D_latch d_latch_1 (.WE(not_2_out), .D(and_1_out), .Q(d_latch_1_q));  // open: QNOT
  D_latch d_latch_2 (.WE(clk), .D(d_latch_1_q), .Q(Q));  // open: QNOT
endmodule

module Toggle_D_flip_flop (
);

  wire button_1_out, d_flip_flop_reset_1_q, not_1_out;

  Button button_1 (.out(button_1_out));
  // Probe on d_flip_flop_reset_1_q
  D_flip_flop_reset d_flip_flop_reset_1 (.clk(button_1_out), .RESET(1'b0), .D(not_1_out), .Q(d_flip_flop_reset_1_q));
  not not_1 (not_1_out, d_flip_flop_reset_1_q);
endmodule

module Negative_D_flip_flop (
  input  in_1,
  output out_2
);

  wire button_1_out, d_latch_1_q, not_1_out;

  Button button_1 (.out(button_1_out));
  not not_1 (not_1_out, button_1_out);
  D_latch d_latch_1 (.WE(button_1_out), .D(in_1), .Q(d_latch_1_q));  // open: QNOT
  D_latch d_latch_2 (.WE(not_1_out), .D(d_latch_1_q), .Q(out_2));  // open: QNOT
endmodule

module Enable_D_flip_flop (
  input  CLK,
  input  D,
  input  ENABLE,
  output Q,
  output NOTQ
);

  wire mux1_bit2_to_1_1_y, not_1_out;

  not not_1 (not_1_out, ENABLE);
  Positive_D_flip_flop positive_d_flip_flop_1 (.clk(CLK), .D(mux1_bit2_to_1_1_y), .Q(Q), .NOTQ(NOTQ));
  mux1_bit2_to_1 mux1_bit2_to_1_1 (.D0(D), .S(not_1_out), .D1(Q), .Y(mux1_bit2_to_1_1_y));
endmodule

module Register_4bit (
  input  clk,
  input  RESET,
  input  D3,
  input  D2,
  input  D1,
  input  D0,
  input  enable,
  output Q3,
  output Q2,
  output Q1,
  output Q0
);

  wire and_1_out, and_2_out, and_3_out, and_4_out, decoder_1_out0, decoder_1_out1, decoder_1_out2,
       decoder_1_out3, decoder_1_out4, decoder_1_out5, decoder_1_out6, decoder_1_out7, decoder_1_out8,
       decoder_1_out9, decoder_1_out10, decoder_1_out11, decoder_1_out12, decoder_1_out13, decoder_1_out14,
       decoder_1_out15, not_1_out;
  wire [7:0] or_1_out, wire0_1_out_2, wire1_1_out_2, wire2_1_out_2, wire3_1_out_2, wire4_1_out_2,
       wire5_1_out_2, wire6_1_out_2, wire7_1_out_2, wire8_1_out_2, wire9_1_out_2, wire10_1_out_2,
       wire11_1_out_2, wire12_1_out_2, wire13_1_out_2, wire14_1_out_2, wire15_1_out_2;

  not not_1 (not_1_out, RESET);
  and and_1 (and_1_out, not_1_out, D3);
  and and_2 (and_2_out, not_1_out, D2);
  and and_3 (and_3_out, not_1_out, D1);
  and and_4 (and_4_out, not_1_out, D0);
  Enable_D_flip_flop enable_d_flip_flop_1 (.CLK(clk), .D(and_1_out), .ENABLE(enable), .Q(Q3));  // open: NOTQ
  Enable_D_flip_flop enable_d_flip_flop_2 (.CLK(clk), .D(and_2_out), .ENABLE(enable), .Q(Q2));  // open: NOTQ
  Enable_D_flip_flop enable_d_flip_flop_3 (.CLK(clk), .D(and_3_out), .ENABLE(enable), .Q(Q1));  // open: NOTQ
  Enable_D_flip_flop enable_d_flip_flop_4 (.CLK(clk), .D(and_4_out), .ENABLE(enable), .Q(Q0));  // open: NOTQ
  Decoder #(.select(4)) decoder_1 (
    .out0(decoder_1_out0), .out1(decoder_1_out1), .out2(decoder_1_out2), .out3(decoder_1_out3),
    .out4(decoder_1_out4), .out5(decoder_1_out5), .out6(decoder_1_out6), .out7(decoder_1_out7),
    .out8(decoder_1_out8), .out9(decoder_1_out9), .out10(decoder_1_out10), .out11(decoder_1_out11),
    .out12(decoder_1_out12), .out13(decoder_1_out13), .out14(decoder_1_out14), .out15(decoder_1_out15),
    .sel({Q3, Q2, Q1, Q0}), .en(1'b1));
  wire0 wire0_1 (.in_1(decoder_1_out0), .out_2(wire0_1_out_2));
  wire1 wire1_1 (.in_1(decoder_1_out1), .out_2(wire1_1_out_2));
  wire2 wire2_1 (.in_1(decoder_1_out2), .out_2(wire2_1_out_2));
  wire3 wire3_1 (.in_1(decoder_1_out3), .out_2(wire3_1_out_2));
  wire4 wire4_1 (.in_1(decoder_1_out4), .out_2(wire4_1_out_2));
  wire5 wire5_1 (.in_1(decoder_1_out5), .out_2(wire5_1_out_2));
  wire6 wire6_1 (.in_1(decoder_1_out6), .out_2(wire6_1_out_2));
  wire7 wire7_1 (.in_1(decoder_1_out7), .out_2(wire7_1_out_2));
  wire8 wire8_1 (.in_1(decoder_1_out8), .out_2(wire8_1_out_2));
  wire9 wire9_1 (.in_1(decoder_1_out9), .out_2(wire9_1_out_2));
  wire10 wire10_1 (.in_1(decoder_1_out10), .out_2(wire10_1_out_2));
  wire11 wire11_1 (.in_1(decoder_1_out11), .out_2(wire11_1_out_2));
  wire12 wire12_1 (.in_1(decoder_1_out12), .out_2(wire12_1_out_2));
  wire13 wire13_1 (.in_1(decoder_1_out13), .out_2(wire13_1_out_2));
  wire14 wire14_1 (.in_1(decoder_1_out14), .out_2(wire14_1_out_2));
  wire15 wire15_1 (.in_1(decoder_1_out15), .out_2(wire15_1_out_2));
  assign or_1_out = wire0_1_out_2 | wire1_1_out_2 | wire2_1_out_2 | wire3_1_out_2 | wire4_1_out_2 | wire5_1_out_2 | wire6_1_out_2 | wire7_1_out_2 | wire8_1_out_2 | wire9_1_out_2 | wire10_1_out_2 | wire11_1_out_2 | wire12_1_out_2 | wire13_1_out_2 | wire14_1_out_2 | wire15_1_out_2;  // OR_Gate or_1, 8 bits wide
  _7_Segment_Display u_7_segment_display_1 (
    .g(or_1_out[6]), .f(or_1_out[5]), .a(or_1_out[0]), .b(or_1_out[1]), .e(or_1_out[4]), .d(or_1_out[3]),
    .c(or_1_out[2]), .dp(or_1_out[7]));
endmodule

module Counter_4bit (
  input  in_1,
  input  in_2,
  input  in_3,
  output out_4,
  output out_5,
  output out_6,
  output out_7
);

  wire adder_to_4_1_y0, adder_to_4_1_y1, adder_to_4_1_y2, adder_to_4_1_y3, not_3_out, not_4_out, not_5_out,
       not_6_out, xor_1_out, xor_2_out, xor_3_out, xor_4_out;
  wire [3:0] and_1_out, and_2_out, and_3_out, and_4_out, not_1_out, not_2_out, or_1_out, or_2_out;
  wire [3:3] and_5_out;

  assign not_1_out = ~{4{and_5_out[3]}};  // NOT_Gate not_1, 4 bits wide
  assign not_2_out = ~{4{and_5_out[3]}};  // NOT_Gate not_2, 4 bits wide
  assign and_1_out = 4'b0001 & not_1_out;  // AND_Gate and_1, 4 bits wide
  assign and_2_out = {4{and_5_out[3]}} & 4'b0000;  // AND_Gate and_2, 4 bits wide
  assign and_3_out = {out_4, out_5, out_6, out_7} & not_2_out;  // AND_Gate and_3, 4 bits wide
  assign and_4_out = {4{and_5_out[3]}} & 4'b0000;  // AND_Gate and_4, 4 bits wide
  assign or_1_out = and_1_out | and_2_out;  // OR_Gate or_1, 4 bits wide
  assign or_2_out = and_3_out | and_4_out;  // OR_Gate or_2, 4 bits wide
  and and_5 (and_5_out[3], not_3_out, not_4_out, not_5_out, not_6_out);
  not not_3 (not_3_out, xor_1_out);
  not not_4 (not_4_out, xor_2_out);
  not not_5 (not_5_out, xor_3_out);
  not not_6 (not_6_out, xor_4_out);
  xor xor_1 (xor_1_out, out_4, 1'b1);
  xor xor_2 (xor_2_out, out_5, 1'b1);
  xor xor_3 (xor_3_out, out_6, 1'b1);
  xor xor_4 (xor_4_out, out_7, 1'b1);
  adder_to_4 adder_to_4_1 (
    .A3(or_2_out[3]), .A2(or_2_out[2]), .A1(or_2_out[1]), .A0(or_2_out[0]), .B3(or_1_out[3]),
    .B2(or_1_out[2]), .B1(or_1_out[1]), .B0(or_1_out[0]), .Y3(adder_to_4_1_y3), .Y2(adder_to_4_1_y2),
    .Y1(adder_to_4_1_y1), .Y0(adder_to_4_1_y0));
  Register_4bit register_4bit_1 (
    .clk(in_1), .RESET(in_2), .D3(adder_to_4_1_y3), .D2(adder_to_4_1_y2), .D1(adder_to_4_1_y1),
    .D0(adder_to_4_1_y0), .enable(in_3), .Q3(out_4), .Q2(out_5), .Q1(out_6), .Q0(out_7));
endmodule

module Series_summation_circuit (
  input  in_1,
  input  in_2,
  output out_3,
  output out_4,
  output out_5,
  output out_6,
  output out_7,
  output out_8,
  output out_9,
  output out_10,
  output out_11,
  output out_12,
  output out_13,
  output out_14,
  output out_15,
  output out_16,
  output out_17,
  output out_18
);

  wire adder_to_8_1_p14, adder_to_8_1_p15, adder_to_8_1_p16, adder_to_8_1_p17, adder_to_8_1_p18,
       adder_to_8_1_p19, adder_to_8_1_p20, adder_to_8_1_p21, adder_to_8_2_p20, adder_to_8_2_p21,
       adder_to_8_2_p22, adder_to_8_2_p23, adder_to_8_2_p24, adder_to_8_2_p25, adder_to_8_2_p26,
       adder_to_8_2_p27, button_1_out;

  Button button_1 (.out(button_1_out));
  // adder_to_8 adder_to_8_1: pin names not known; wires that end beside it: 1'b1, out_10, out_9, out_8, out_5, 1'b0, out_4, 1'b0, out_6, 1'b0, 1'b0, 1'b0, out_3, adder_to_8_1_p14, adder_to_8_1_p15, adder_to_8_1_p16, adder_to_8_1_p17, adder_to_8_1_p18, adder_to_8_1_p19, adder_to_8_1_p20, adder_to_8_1_p21
  // adder_to_8 adder_to_8_2: pin names not known; wires that end beside it: 1'b0, out_7, 1'b0, out_18, out_10, out_9, out_8, out_5, out_17, out_4, out_16, out_6, out_13, out_12, out_11, out_3, out_15, out_7, out_14, adder_to_8_2_p20, adder_to_8_2_p21, adder_to_8_2_p22, adder_to_8_2_p23, adder_to_8_2_p24, adder_to_8_2_p25, adder_to_8_2_p26, adder_to_8_2_p27
  Register_8bit register_8bit_1 (
    .CLK(button_1_out), .RESET(in_1), .D7(adder_to_8_1_p17), .D6(adder_to_8_1_p21), .D5(adder_to_8_1_p14),
    .D4(adder_to_8_1_p15), .D3(adder_to_8_1_p19), .D2(adder_to_8_1_p16), .D1(adder_to_8_1_p18),
    .D0(adder_to_8_1_p20), .ENABLE(in_2), .Q7(out_3), .Q6(out_4), .Q5(out_5), .Q4(out_6), .Q3(out_7),
    .Q2(out_8), .Q1(out_9), .Q0(out_10));
  Register_8bit register_8bit_2 (
    .CLK(button_1_out), .RESET(in_1), .D7(adder_to_8_2_p23), .D6(adder_to_8_2_p27), .D5(adder_to_8_2_p20),
    .D4(adder_to_8_2_p21), .D3(adder_to_8_2_p25), .D2(adder_to_8_2_p22), .D1(adder_to_8_2_p24),
    .D0(adder_to_8_2_p26), .ENABLE(in_2), .Q7(out_11), .Q6(out_12), .Q5(out_13), .Q4(out_14), .Q3(out_15),
    .Q2(out_16), .Q1(out_17), .Q0(out_18));
endmodule

module Register_8bit (
  input  CLK,
  input  RESET,
  input  D7,
  input  D6,
  input  D5,
  input  D4,
  input  D3,
  input  D2,
  input  D1,
  input  D0,
  input  ENABLE,
  output Q7,
  output Q6,
  output Q5,
  output Q4,
  output Q3,
  output Q2,
  output Q1,
  output Q0
);

  Register_4bit register_4bit_1 (
    .clk(CLK), .RESET(RESET), .D3(D7), .D2(D6), .D1(D5), .D0(D4), .enable(ENABLE), .Q3(Q7), .Q2(Q6), .Q1(Q5),
    .Q0(Q4));
  Register_4bit register_4bit_2 (
    .clk(CLK), .RESET(RESET), .D3(D3), .D2(D2), .D1(D1), .D0(D0), .enable(ENABLE), .Q3(Q3), .Q2(Q2), .Q1(Q1),
    .Q0(Q0));
endmodule

module Digital_clock (
  input  in_1,
  input  in_2,
  input  in_3,
  input  in_4,
  input  in_5,
  input  in_6,
  input  in_7,
  input  in_8
);

  wire adder_to_4_1_y0, adder_to_4_1_y1, adder_to_4_1_y2, adder_to_4_1_y3, adder_to_4_2_y0, adder_to_4_2_y1,
       adder_to_4_2_y2, adder_to_4_2_y3, adder_to_4_3_y0, adder_to_4_3_y1, adder_to_4_3_y2, adder_to_4_3_y3,
       adder_to_4_4_y0, adder_to_4_4_y1, adder_to_4_4_y2, adder_to_4_4_y3, and_1_out, and_2_out, clock_1_out,
       decoder_1_out0, decoder_1_out1, decoder_1_out2, decoder_1_out3, decoder_1_out4, decoder_1_out5,
       decoder_1_out6, decoder_1_out7, decoder_1_out8, decoder_1_out9, decoder_1_out10, decoder_1_out11,
       decoder_1_out12, decoder_1_out13, decoder_1_out14, decoder_1_out15, decoder_2_out0, decoder_2_out1,
       decoder_2_out2, decoder_2_out3, decoder_2_out4, decoder_2_out5, decoder_2_out6, decoder_2_out7,
       decoder_2_out8, decoder_2_out9, decoder_2_out10, decoder_2_out11, decoder_2_out12, decoder_2_out13,
       decoder_2_out14, decoder_2_out15, decoder_3_out0, decoder_3_out1, decoder_3_out2, decoder_3_out3,
       decoder_3_out4, decoder_3_out5, decoder_3_out6, decoder_3_out7, decoder_3_out8, decoder_3_out9,
       decoder_3_out10, decoder_3_out11, decoder_3_out12, decoder_3_out13, decoder_3_out14, decoder_3_out15,
       decoder_4_out0, decoder_4_out1, decoder_4_out2, decoder_4_out3, decoder_4_out4, decoder_4_out5,
       decoder_4_out6, decoder_4_out7, decoder_4_out8, decoder_4_out9, decoder_4_out10, decoder_4_out11,
       decoder_4_out12, decoder_4_out13, decoder_4_out14, decoder_4_out15, not_9_out, not_10_out, not_11_out,
       not_12_out, not_13_out, not_14_out, not_15_out, not_16_out, not_17_out, not_18_out, not_19_out,
       not_20_out, not_21_out, not_22_out, not_23_out, not_24_out, not_25_out, not_26_out, not_27_out,
       xor_1_out, xor_2_out, xor_3_out, xor_4_out, xor_5_out, xor_6_out, xor_7_out, xor_8_out, xor_9_out,
       xor_10_out, xor_11_out, xor_12_out, xor_13_out, xor_14_out, xor_15_out, xor_16_out;
  wire [3:0] and_3_out, and_4_out, and_5_out, and_6_out, and_7_out, and_8_out, and_9_out, and_10_out,
       and_11_out, and_12_out, and_13_out, and_14_out, and_15_out, and_16_out, and_17_out, and_18_out,
       not_1_out, not_2_out, not_3_out, not_4_out, not_5_out, not_6_out, not_7_out, not_8_out, or_1_out,
       or_2_out, or_3_out, or_4_out, or_5_out, or_6_out, or_7_out, or_8_out, register_4bit_1_q0,
       register_4bit_2_q0, register_4bit_3_q0, register_4bit_4_q0;
  wire [3:3] and_19_out, and_20_out, and_21_out, and_22_out;
  wire [7:0] or_9_out, or_10_out, or_11_out, or_12_out, wire0_1_out_2, wire0_2_out_2, wire0_3_out_2,
       wire0_4_out_2, wire1_1_out_2, wire1_2_out_2, wire1_3_out_2, wire1_4_out_2, wire2_1_out_2,
       wire2_2_out_2, wire2_3_out_2, wire2_4_out_2, wire3_1_out_2, wire3_2_out_2, wire3_3_out_2,
       wire3_4_out_2, wire4_1_out_2, wire4_2_out_2, wire4_3_out_2, wire4_4_out_2, wire5_1_out_2,
       wire5_2_out_2, wire5_3_out_2, wire5_4_out_2, wire6_1_out_2, wire6_2_out_2, wire6_3_out_2,
       wire6_4_out_2, wire7_1_out_2, wire7_2_out_2, wire7_3_out_2, wire7_4_out_2, wire8_1_out_2,
       wire8_2_out_2, wire8_3_out_2, wire8_4_out_2, wire9_1_out_2, wire9_2_out_2, wire9_3_out_2,
       wire9_4_out_2, wire10_1_out_2, wire10_2_out_2, wire10_3_out_2, wire10_4_out_2, wire11_1_out_2,
       wire11_2_out_2, wire11_3_out_2, wire11_4_out_2, wire12_1_out_2, wire12_2_out_2, wire12_3_out_2,
       wire12_4_out_2, wire13_1_out_2, wire13_2_out_2, wire13_3_out_2, wire13_4_out_2, wire14_1_out_2,
       wire14_2_out_2, wire14_3_out_2, wire14_4_out_2, wire15_1_out_2, wire15_2_out_2, wire15_3_out_2,
       wire15_4_out_2;

  and and_1 (and_1_out, and_22_out[3], and_19_out[3], and_20_out[3]);
  and and_2 (and_2_out, and_22_out[3], and_19_out[3]);
  assign not_1_out = ~{4{and_22_out[3]}};  // NOT_Gate not_1, 4 bits wide
  assign not_2_out = ~{4{and_19_out[3]}};  // NOT_Gate not_2, 4 bits wide
  assign not_3_out = ~{4{and_20_out[3]}};  // NOT_Gate not_3, 4 bits wide
  assign not_4_out = ~{4{and_21_out[3]}};  // NOT_Gate not_4, 4 bits wide
  assign not_5_out = ~{4{and_19_out[3]}};  // NOT_Gate not_5, 4 bits wide
  assign not_6_out = ~{4{and_20_out[3]}};  // NOT_Gate not_6, 4 bits wide
  assign not_7_out = ~{4{and_21_out[3]}};  // NOT_Gate not_7, 4 bits wide
  assign not_8_out = ~{4{and_22_out[3]}};  // NOT_Gate not_8, 4 bits wide
  assign and_3_out = 4'b0001 & not_1_out;  // AND_Gate and_3, 4 bits wide
  assign and_4_out = {4{and_22_out[3]}} & 4'b0000;  // AND_Gate and_4, 4 bits wide
  assign and_5_out = 4'b0001 & not_2_out;  // AND_Gate and_5, 4 bits wide
  assign and_6_out = {4{and_19_out[3]}} & 4'b0000;  // AND_Gate and_6, 4 bits wide
  assign and_7_out = 4'b0001 & not_3_out;  // AND_Gate and_7, 4 bits wide
  assign and_8_out = {4{and_20_out[3]}} & 4'b0000;  // AND_Gate and_8, 4 bits wide
  assign and_9_out = 4'b0001 & not_4_out;  // AND_Gate and_9, 4 bits wide
  assign and_10_out = {4{and_21_out[3]}} & 4'b0000;  // AND_Gate and_10, 4 bits wide
  assign and_11_out = register_4bit_1_q0 & not_8_out;  // AND_Gate and_11, 4 bits wide
  assign and_12_out = {4{and_22_out[3]}} & 4'b0000;  // AND_Gate and_12, 4 bits wide
  assign or_1_out = and_3_out | and_4_out;  // OR_Gate or_1, 4 bits wide
  assign and_13_out = register_4bit_2_q0 & not_5_out;  // AND_Gate and_13, 4 bits wide
  assign and_14_out = {4{and_19_out[3]}} & 4'b0000;  // AND_Gate and_14, 4 bits wide
  assign or_2_out = and_5_out | and_6_out;  // OR_Gate or_2, 4 bits wide
  assign and_15_out = register_4bit_3_q0 & not_6_out;  // AND_Gate and_15, 4 bits wide
  assign and_16_out = {4{and_20_out[3]}} & 4'b0000;  // AND_Gate and_16, 4 bits wide
  assign or_3_out = and_7_out | and_8_out;  // OR_Gate or_3, 4 bits wide
  assign and_17_out = register_4bit_4_q0 & not_7_out;  // AND_Gate and_17, 4 bits wide
  assign and_18_out = {4{and_21_out[3]}} & 4'b0000;  // AND_Gate and_18, 4 bits wide
  assign or_4_out = and_9_out | and_10_out;  // OR_Gate or_4, 4 bits wide
  assign or_5_out = and_13_out | and_14_out;  // OR_Gate or_5, 4 bits wide
  assign or_6_out = and_15_out | and_16_out;  // OR_Gate or_6, 4 bits wide
  assign or_7_out = and_17_out | and_18_out;  // OR_Gate or_7, 4 bits wide
  assign or_8_out = and_11_out | and_12_out;  // OR_Gate or_8, 4 bits wide
  and and_19 (and_19_out[3], not_13_out, not_14_out, not_15_out, not_16_out);
  and and_20 (and_20_out[3], not_17_out, not_18_out, not_19_out, not_20_out);
  and and_21 (and_21_out[3], not_21_out, not_22_out, not_23_out, not_24_out);
  and and_22 (and_22_out[3], not_9_out, not_10_out, not_11_out, not_12_out);
  not not_9 (not_9_out, xor_1_out);
  not not_10 (not_10_out, xor_2_out);
  not not_11 (not_11_out, xor_3_out);
  not not_12 (not_12_out, xor_4_out);
  not not_13 (not_13_out, xor_5_out);
  not not_14 (not_14_out, xor_6_out);
  not not_15 (not_15_out, xor_7_out);
  not not_16 (not_16_out, xor_8_out);
  not not_17 (not_17_out, xor_9_out);
  not not_18 (not_18_out, xor_10_out);
  not not_19 (not_19_out, xor_11_out);
  not not_20 (not_20_out, xor_12_out);
  not not_21 (not_21_out, xor_13_out);
  not not_22 (not_22_out, xor_14_out);
  not not_23 (not_23_out, xor_15_out);
  not not_24 (not_24_out, xor_16_out);
  xor xor_1 (xor_1_out, register_4bit_1_q0[3], 1'b1);
  xor xor_2 (xor_2_out, register_4bit_1_q0[2], 1'b0);
  xor xor_3 (xor_3_out, register_4bit_1_q0[1], 1'b0);
  xor xor_4 (xor_4_out, register_4bit_1_q0[0], 1'b1);
  xor xor_5 (xor_5_out, register_4bit_2_q0[3], 1'b0);
  xor xor_6 (xor_6_out, register_4bit_2_q0[2], 1'b1);
  xor xor_7 (xor_7_out, register_4bit_2_q0[1], 1'b0);
  xor xor_8 (xor_8_out, register_4bit_2_q0[0], 1'b1);
  not not_25 (not_25_out, and_22_out[3]);
  xor xor_9 (xor_9_out, register_4bit_3_q0[3], 1'b1);
  xor xor_10 (xor_10_out, register_4bit_3_q0[2], 1'b0);
  xor xor_11 (xor_11_out, register_4bit_3_q0[1], 1'b0);
  xor xor_12 (xor_12_out, register_4bit_3_q0[0], 1'b1);
  not not_26 (not_26_out, and_2_out);
  xor xor_13 (xor_13_out, register_4bit_4_q0[3], 1'b0);
  xor xor_14 (xor_14_out, register_4bit_4_q0[2], 1'b1);
  xor xor_15 (xor_15_out, register_4bit_4_q0[1], 1'b0);
  xor xor_16 (xor_16_out, register_4bit_4_q0[0], 1'b1);
  not not_27 (not_27_out, and_1_out);
  Clock clock_1 (.out(clock_1_out));
  adder_to_4 adder_to_4_1 (
    .A3(or_5_out[3]), .A2(or_5_out[2]), .A1(or_5_out[1]), .A0(or_5_out[0]), .B3(or_2_out[3]),
    .B2(or_2_out[2]), .B1(or_2_out[1]), .B0(or_2_out[0]), .Y3(adder_to_4_1_y3), .Y2(adder_to_4_1_y2),
    .Y1(adder_to_4_1_y1), .Y0(adder_to_4_1_y0));
  adder_to_4 adder_to_4_2 (
    .A3(or_6_out[3]), .A2(or_6_out[2]), .A1(or_6_out[1]), .A0(or_6_out[0]), .B3(or_3_out[3]),
    .B2(or_3_out[2]), .B1(or_3_out[1]), .B0(or_3_out[0]), .Y3(adder_to_4_2_y3), .Y2(adder_to_4_2_y2),
    .Y1(adder_to_4_2_y1), .Y0(adder_to_4_2_y0));
  adder_to_4 adder_to_4_3 (
    .A3(or_7_out[3]), .A2(or_7_out[2]), .A1(or_7_out[1]), .A0(or_7_out[0]), .B3(or_4_out[3]),
    .B2(or_4_out[2]), .B1(or_4_out[1]), .B0(or_4_out[0]), .Y3(adder_to_4_3_y3), .Y2(adder_to_4_3_y2),
    .Y1(adder_to_4_3_y1), .Y0(adder_to_4_3_y0));
  adder_to_4 adder_to_4_4 (
    .A3(or_8_out[3]), .A2(or_8_out[2]), .A1(or_8_out[1]), .A0(or_8_out[0]), .B3(or_1_out[3]),
    .B2(or_1_out[2]), .B1(or_1_out[1]), .B0(or_1_out[0]), .Y3(adder_to_4_4_y3), .Y2(adder_to_4_4_y2),
    .Y1(adder_to_4_4_y1), .Y0(adder_to_4_4_y0));
  Register_4bit register_4bit_1 (
    .clk(clock_1_out), .RESET(in_1), .D3(adder_to_4_4_y3), .D2(adder_to_4_4_y2), .D1(adder_to_4_4_y1),
    .D0(adder_to_4_4_y0), .enable(in_2), .Q3(register_4bit_1_q0[3]), .Q2(register_4bit_1_q0[2]),
    .Q1(register_4bit_1_q0[1]), .Q0(register_4bit_1_q0[0]));
  Register_4bit register_4bit_2 (
    .clk(not_25_out), .RESET(in_3), .D3(adder_to_4_1_y3), .D2(adder_to_4_1_y2), .D1(adder_to_4_1_y1),
    .D0(adder_to_4_1_y0), .enable(in_4), .Q3(register_4bit_2_q0[3]), .Q2(register_4bit_2_q0[2]),
    .Q1(register_4bit_2_q0[1]), .Q0(register_4bit_2_q0[0]));
  Register_4bit register_4bit_3 (
    .clk(not_26_out), .RESET(in_5), .D3(adder_to_4_2_y3), .D2(adder_to_4_2_y2), .D1(adder_to_4_2_y1),
    .D0(adder_to_4_2_y0), .enable(in_6), .Q3(register_4bit_3_q0[3]), .Q2(register_4bit_3_q0[2]),
    .Q1(register_4bit_3_q0[1]), .Q0(register_4bit_3_q0[0]));
  Register_4bit register_4bit_4 (
    .clk(not_27_out), .RESET(in_7), .D3(adder_to_4_3_y3), .D2(adder_to_4_3_y2), .D1(adder_to_4_3_y1),
    .D0(adder_to_4_3_y0), .enable(in_8), .Q3(register_4bit_4_q0[3]), .Q2(register_4bit_4_q0[2]),
    .Q1(register_4bit_4_q0[1]), .Q0(register_4bit_4_q0[0]));
  Decoder #(.select(4)) decoder_1 (
    .out0(decoder_1_out0), .out1(decoder_1_out1), .out2(decoder_1_out2), .out3(decoder_1_out3),
    .out4(decoder_1_out4), .out5(decoder_1_out5), .out6(decoder_1_out6), .out7(decoder_1_out7),
    .out8(decoder_1_out8), .out9(decoder_1_out9), .out10(decoder_1_out10), .out11(decoder_1_out11),
    .out12(decoder_1_out12), .out13(decoder_1_out13), .out14(decoder_1_out14), .out15(decoder_1_out15),
    .sel(register_4bit_2_q0), .en(1'b1));
  Decoder #(.select(4)) decoder_2 (
    .out0(decoder_2_out0), .out1(decoder_2_out1), .out2(decoder_2_out2), .out3(decoder_2_out3),
    .out4(decoder_2_out4), .out5(decoder_2_out5), .out6(decoder_2_out6), .out7(decoder_2_out7),
    .out8(decoder_2_out8), .out9(decoder_2_out9), .out10(decoder_2_out10), .out11(decoder_2_out11),
    .out12(decoder_2_out12), .out13(decoder_2_out13), .out14(decoder_2_out14), .out15(decoder_2_out15),
    .sel(register_4bit_3_q0), .en(1'b1));
  Decoder #(.select(4)) decoder_3 (
    .out0(decoder_3_out0), .out1(decoder_3_out1), .out2(decoder_3_out2), .out3(decoder_3_out3),
    .out4(decoder_3_out4), .out5(decoder_3_out5), .out6(decoder_3_out6), .out7(decoder_3_out7),
    .out8(decoder_3_out8), .out9(decoder_3_out9), .out10(decoder_3_out10), .out11(decoder_3_out11),
    .out12(decoder_3_out12), .out13(decoder_3_out13), .out14(decoder_3_out14), .out15(decoder_3_out15),
    .sel(register_4bit_4_q0), .en(1'b1));
  Decoder #(.select(4)) decoder_4 (
    .out0(decoder_4_out0), .out1(decoder_4_out1), .out2(decoder_4_out2), .out3(decoder_4_out3),
    .out4(decoder_4_out4), .out5(decoder_4_out5), .out6(decoder_4_out6), .out7(decoder_4_out7),
    .out8(decoder_4_out8), .out9(decoder_4_out9), .out10(decoder_4_out10), .out11(decoder_4_out11),
    .out12(decoder_4_out12), .out13(decoder_4_out13), .out14(decoder_4_out14), .out15(decoder_4_out15),
    .sel(register_4bit_1_q0), .en(1'b1));
  wire0 wire0_1 (.in_1(decoder_1_out0), .out_2(wire0_1_out_2));
  wire1 wire1_1 (.in_1(decoder_1_out1), .out_2(wire1_1_out_2));
  wire2 wire2_1 (.in_1(decoder_1_out2), .out_2(wire2_1_out_2));
  wire3 wire3_1 (.in_1(decoder_1_out3), .out_2(wire3_1_out_2));
  wire4 wire4_1 (.in_1(decoder_1_out4), .out_2(wire4_1_out_2));
  wire5 wire5_1 (.in_1(decoder_1_out5), .out_2(wire5_1_out_2));
  wire6 wire6_1 (.in_1(decoder_1_out6), .out_2(wire6_1_out_2));
  wire7 wire7_1 (.in_1(decoder_1_out7), .out_2(wire7_1_out_2));
  wire8 wire8_1 (.in_1(decoder_1_out8), .out_2(wire8_1_out_2));
  wire9 wire9_1 (.in_1(decoder_1_out9), .out_2(wire9_1_out_2));
  wire10 wire10_1 (.in_1(decoder_1_out10), .out_2(wire10_1_out_2));
  wire11 wire11_1 (.in_1(decoder_1_out11), .out_2(wire11_1_out_2));
  wire12 wire12_1 (.in_1(decoder_1_out12), .out_2(wire12_1_out_2));
  wire13 wire13_1 (.in_1(decoder_1_out13), .out_2(wire13_1_out_2));
  wire14 wire14_1 (.in_1(decoder_1_out14), .out_2(wire14_1_out_2));
  wire15 wire15_1 (.in_1(decoder_1_out15), .out_2(wire15_1_out_2));
  wire0 wire0_2 (.in_1(decoder_3_out0), .out_2(wire0_2_out_2));
  wire1 wire1_2 (.in_1(decoder_3_out1), .out_2(wire1_2_out_2));
  wire2 wire2_2 (.in_1(decoder_3_out2), .out_2(wire2_2_out_2));
  wire3 wire3_2 (.in_1(decoder_3_out3), .out_2(wire3_2_out_2));
  wire4 wire4_2 (.in_1(decoder_3_out4), .out_2(wire4_2_out_2));
  wire5 wire5_2 (.in_1(decoder_3_out5), .out_2(wire5_2_out_2));
  wire6 wire6_2 (.in_1(decoder_3_out6), .out_2(wire6_2_out_2));
  wire7 wire7_2 (.in_1(decoder_3_out7), .out_2(wire7_2_out_2));
  wire8 wire8_2 (.in_1(decoder_3_out8), .out_2(wire8_2_out_2));
  wire9 wire9_2 (.in_1(decoder_3_out9), .out_2(wire9_2_out_2));
  wire10 wire10_2 (.in_1(decoder_3_out10), .out_2(wire10_2_out_2));
  wire11 wire11_2 (.in_1(decoder_3_out11), .out_2(wire11_2_out_2));
  wire12 wire12_2 (.in_1(decoder_3_out12), .out_2(wire12_2_out_2));
  wire13 wire13_2 (.in_1(decoder_3_out13), .out_2(wire13_2_out_2));
  wire14 wire14_2 (.in_1(decoder_3_out14), .out_2(wire14_2_out_2));
  wire15 wire15_2 (.in_1(decoder_3_out15), .out_2(wire15_2_out_2));
  wire0 wire0_3 (.in_1(decoder_4_out0), .out_2(wire0_3_out_2));
  wire1 wire1_3 (.in_1(decoder_4_out1), .out_2(wire1_3_out_2));
  wire2 wire2_3 (.in_1(decoder_4_out2), .out_2(wire2_3_out_2));
  wire3 wire3_3 (.in_1(decoder_4_out3), .out_2(wire3_3_out_2));
  wire4 wire4_3 (.in_1(decoder_4_out4), .out_2(wire4_3_out_2));
  wire5 wire5_3 (.in_1(decoder_4_out5), .out_2(wire5_3_out_2));
  wire6 wire6_3 (.in_1(decoder_4_out6), .out_2(wire6_3_out_2));
  wire7 wire7_3 (.in_1(decoder_4_out7), .out_2(wire7_3_out_2));
  wire8 wire8_3 (.in_1(decoder_4_out8), .out_2(wire8_3_out_2));
  wire9 wire9_3 (.in_1(decoder_4_out9), .out_2(wire9_3_out_2));
  wire10 wire10_3 (.in_1(decoder_4_out10), .out_2(wire10_3_out_2));
  wire11 wire11_3 (.in_1(decoder_4_out11), .out_2(wire11_3_out_2));
  wire12 wire12_3 (.in_1(decoder_4_out12), .out_2(wire12_3_out_2));
  wire13 wire13_3 (.in_1(decoder_4_out13), .out_2(wire13_3_out_2));
  wire14 wire14_3 (.in_1(decoder_4_out14), .out_2(wire14_3_out_2));
  wire15 wire15_3 (.in_1(decoder_4_out15), .out_2(wire15_3_out_2));
  wire0 wire0_4 (.in_1(decoder_2_out0), .out_2(wire0_4_out_2));
  wire1 wire1_4 (.in_1(decoder_2_out1), .out_2(wire1_4_out_2));
  wire2 wire2_4 (.in_1(decoder_2_out2), .out_2(wire2_4_out_2));
  wire3 wire3_4 (.in_1(decoder_2_out3), .out_2(wire3_4_out_2));
  wire4 wire4_4 (.in_1(decoder_2_out4), .out_2(wire4_4_out_2));
  wire5 wire5_4 (.in_1(decoder_2_out5), .out_2(wire5_4_out_2));
  wire6 wire6_4 (.in_1(decoder_2_out6), .out_2(wire6_4_out_2));
  wire7 wire7_4 (.in_1(decoder_2_out7), .out_2(wire7_4_out_2));
  wire8 wire8_4 (.in_1(decoder_2_out8), .out_2(wire8_4_out_2));
  wire9 wire9_4 (.in_1(decoder_2_out9), .out_2(wire9_4_out_2));
  wire10 wire10_4 (.in_1(decoder_2_out10), .out_2(wire10_4_out_2));
  wire11 wire11_4 (.in_1(decoder_2_out11), .out_2(wire11_4_out_2));
  wire12 wire12_4 (.in_1(decoder_2_out12), .out_2(wire12_4_out_2));
  wire13 wire13_4 (.in_1(decoder_2_out13), .out_2(wire13_4_out_2));
  wire14 wire14_4 (.in_1(decoder_2_out14), .out_2(wire14_4_out_2));
  wire15 wire15_4 (.in_1(decoder_2_out15), .out_2(wire15_4_out_2));
  assign or_9_out = wire0_2_out_2 | wire1_2_out_2 | wire2_2_out_2 | wire3_2_out_2 | wire4_2_out_2 | wire5_2_out_2 | wire6_2_out_2 | wire7_2_out_2 | wire8_2_out_2 | wire9_2_out_2 | wire10_2_out_2 | wire11_2_out_2 | wire12_2_out_2 | wire13_2_out_2 | wire14_2_out_2 | wire15_2_out_2;  // OR_Gate or_9, 8 bits wide
  assign or_10_out = wire0_3_out_2 | wire1_3_out_2 | wire2_3_out_2 | wire3_3_out_2 | wire4_3_out_2 | wire5_3_out_2 | wire6_3_out_2 | wire7_3_out_2 | wire8_3_out_2 | wire9_3_out_2 | wire10_3_out_2 | wire11_3_out_2 | wire12_3_out_2 | wire13_3_out_2 | wire14_3_out_2 | wire15_3_out_2;  // OR_Gate or_10, 8 bits wide
  assign or_11_out = wire0_1_out_2 | wire1_1_out_2 | wire2_1_out_2 | wire3_1_out_2 | wire4_1_out_2 | wire5_1_out_2 | wire6_1_out_2 | wire7_1_out_2 | wire8_1_out_2 | wire9_1_out_2 | wire10_1_out_2 | wire11_1_out_2 | wire12_1_out_2 | wire13_1_out_2 | wire14_1_out_2 | wire15_1_out_2;  // OR_Gate or_11, 8 bits wide
  assign or_12_out = wire0_4_out_2 | wire1_4_out_2 | wire2_4_out_2 | wire3_4_out_2 | wire4_4_out_2 | wire5_4_out_2 | wire6_4_out_2 | wire7_4_out_2 | wire8_4_out_2 | wire9_4_out_2 | wire10_4_out_2 | wire11_4_out_2 | wire12_4_out_2 | wire13_4_out_2 | wire14_4_out_2 | wire15_4_out_2;  // OR_Gate or_12, 8 bits wide
  _7_Segment_Display u_7_segment_display_1 (
    .g(or_9_out[6]), .f(or_9_out[5]), .a(or_9_out[0]), .b(or_9_out[1]), .e(or_9_out[4]), .d(or_9_out[3]),
    .c(or_9_out[2]), .dp(or_9_out[7]));
  _7_Segment_Display u_7_segment_display_2 (
    .g(or_12_out[6]), .f(or_12_out[5]), .a(or_12_out[0]), .b(or_12_out[1]), .e(or_12_out[4]),
    .d(or_12_out[3]), .c(or_12_out[2]), .dp(or_12_out[7]));
  _7_Segment_Display u_7_segment_display_3 (
    .g(or_11_out[6]), .f(or_11_out[5]), .a(or_11_out[0]), .b(or_11_out[1]), .e(or_11_out[4]),
    .d(or_11_out[3]), .c(or_11_out[2]), .dp(or_11_out[7]));
  _7_Segment_Display u_7_segment_display_4 (
    .g(or_10_out[6]), .f(or_10_out[5]), .a(or_10_out[0]), .b(or_10_out[1]), .e(or_10_out[4]),
    .d(or_10_out[3]), .c(or_10_out[2]), .dp(or_10_out[7]));
endmodule
